// Digital circuit countertest.dig as structural Verilog
module countertest (
  input  clk
);

  wire _74191_1_pin1, _74191_1_pin2, _74191_1_pin3, _74191_1_pin6, _74191_1_pin7, _74191_1_pin9,
       _74191_1_pin10, _74191_1_pin11, _74191_1_pin12, _74191_1_pin13, _74191_1_pin15, _74191_2_pin1,
       _74191_2_pin2, _74191_2_pin3, _74191_2_pin6, _74191_2_pin7, _74191_2_pin9, _74191_2_pin10,
       _74191_2_pin12, _74191_2_pin13, _74191_2_pin15, dipswitch_1_out, dipswitch_2_out;

  DipSwitch dipswitch_1 (.out(dipswitch_1_out));
  DipSwitch dipswitch_2 (.out(dipswitch_2_out));
  LED led_1 (.in(_74191_2_pin6));
  LED led_2 (.in(_74191_2_pin7));
  LED led_3 (.in(_74191_2_pin3));
  LED led_4 (.in(_74191_2_pin2));
  LED led_5 (.in(_74191_1_pin6));
  LED led_6 (.in(_74191_1_pin7));
  LED led_7 (.in(_74191_1_pin3));
  LED led_8 (.in(_74191_1_pin2));
  _74191 _74191_1 (
    .pin1(_74191_1_pin1), .pin2(_74191_1_pin2), .pin3(_74191_1_pin3), .pin4(dipswitch_1_out),
    .pin5(dipswitch_2_out), .pin6(_74191_1_pin6), .pin7(_74191_1_pin7), .pin8(1'b0), .pin9(_74191_1_pin9),
    .pin10(_74191_1_pin10), .pin11(_74191_1_pin11), .pin12(_74191_1_pin12), .pin13(_74191_1_pin13),
    .pin14(clk), .pin15(_74191_1_pin15), .pin16(1'b1));
  _74191 _74191_2 (
    .pin1(_74191_2_pin1), .pin2(_74191_2_pin2), .pin3(_74191_2_pin3), .pin4(_74191_1_pin13),
    .pin5(dipswitch_2_out), .pin6(_74191_2_pin6), .pin7(_74191_2_pin7), .pin8(1'b0), .pin9(_74191_2_pin9),
    .pin10(_74191_2_pin10), .pin11(_74191_1_pin11), .pin12(_74191_2_pin12), .pin13(_74191_2_pin13),
    .pin14(clk), .pin15(_74191_2_pin15), .pin16(1'b1));
  LED led_9 (.in(_74191_1_pin13));
  LED led_10 (.in(_74191_1_pin12));
  DipSwitch dipswitch_3 (.out(_74191_1_pin11));
  LED led_11 (.in(_74191_2_pin13));
  LED led_12 (.in(_74191_2_pin12));
  DipSwitch dipswitch_4 (.out(_74191_2_pin9));
  DipSwitch dipswitch_5 (.out(_74191_2_pin10));
  DipSwitch dipswitch_6 (.out(_74191_2_pin1));
  DipSwitch dipswitch_7 (.out(_74191_2_pin15));
  DipSwitch dipswitch_8 (.out(_74191_1_pin9));
  DipSwitch dipswitch_9 (.out(_74191_1_pin10));
  DipSwitch dipswitch_10 (.out(_74191_1_pin1));
  DipSwitch dipswitch_11 (.out(_74191_1_pin15));

  // Notes on the sheet:
  //   clk: Hz: 4
endmodule
