// Digital circuit 8B_BDSR.dig as structural Verilog
// 8 cell serial organized register file, think a shift register but 8 of them in parallel
module _8B_BDSR (
  input  EN,
  input  CLK,
  input  DIR,
  input  RST,
  input  SRI,
  input  RSI,
  input  D_0,
  input  D_1,
  input  D_2,
  input  D_3,
  input  D_4,
  input  D_5,
  input  D_6,
  input  D_7,
  input  LOAD,
  output SRO,
  output Q_0,
  output CPT,
  output DPT,
  output Q_1,
  output Q_2,
  output Q_3,
  output Q_4,
  output Q_5,
  output Q_6,
  output Q_7
);

  wire multiplexer_1_out, multiplexer_2_out, multiplexer_3_out, multiplexer_4_out, multiplexer_5_out,
       multiplexer_6_out, multiplexer_7_out, multiplexer_8_out, multiplexer_9_out, multiplexer_10_out,
       multiplexer_11_out, multiplexer_12_out, multiplexer_13_out, multiplexer_14_out, multiplexer_15_out,
       multiplexer_16_out;

  and and_1 (CPT, EN, CLK);
  Multiplexer multiplexer_1 (.sel(DIR), .in_0(SRI), .in_1(Q_1), .out(multiplexer_1_out));
  Multiplexer multiplexer_2 (.sel(LOAD), .in_0(multiplexer_1_out), .in_1(D_0), .out(multiplexer_2_out));
  D_FF_AS SR0 (.Set(1'b0), .D(multiplexer_2_out), .C(CPT), .Clr(RST), .Q(Q_0));  // open: nQ
  Multiplexer multiplexer_3 (.sel(DIR), .in_0(Q_0), .in_1(Q_2), .out(multiplexer_3_out));
  Multiplexer multiplexer_4 (.sel(LOAD), .in_0(multiplexer_3_out), .in_1(D_1), .out(multiplexer_4_out));
  D_FF_AS SR1 (.Set(1'b0), .D(multiplexer_4_out), .C(CPT), .Clr(RST), .Q(Q_1));  // open: nQ
  Multiplexer multiplexer_5 (.sel(DIR), .in_0(Q_1), .in_1(Q_3), .out(multiplexer_5_out));
  Multiplexer multiplexer_6 (.sel(LOAD), .in_0(multiplexer_5_out), .in_1(D_2), .out(multiplexer_6_out));
  D_FF_AS SR2 (.Set(1'b0), .D(multiplexer_6_out), .C(CPT), .Clr(RST), .Q(Q_2));  // open: nQ
  Multiplexer multiplexer_7 (.sel(DIR), .in_0(Q_2), .in_1(Q_4), .out(multiplexer_7_out));
  Multiplexer multiplexer_8 (.sel(LOAD), .in_0(multiplexer_7_out), .in_1(D_3), .out(multiplexer_8_out));
  D_FF_AS SR3 (.Set(1'b0), .D(multiplexer_8_out), .C(CPT), .Clr(RST), .Q(Q_3));  // open: nQ
  Multiplexer multiplexer_9 (.sel(DIR), .in_0(Q_3), .in_1(Q_5), .out(multiplexer_9_out));
  Multiplexer multiplexer_10 (.sel(LOAD), .in_0(multiplexer_9_out), .in_1(D_4), .out(multiplexer_10_out));
  D_FF_AS SR4 (.Set(1'b0), .D(multiplexer_10_out), .C(CPT), .Clr(RST), .Q(Q_4));  // open: nQ
  Multiplexer multiplexer_11 (.sel(DIR), .in_0(Q_4), .in_1(Q_6), .out(multiplexer_11_out));
  Multiplexer multiplexer_12 (.sel(LOAD), .in_0(multiplexer_11_out), .in_1(D_5), .out(multiplexer_12_out));
  D_FF_AS SR5 (.Set(1'b0), .D(multiplexer_12_out), .C(CPT), .Clr(RST), .Q(Q_5));  // open: nQ
  Multiplexer multiplexer_13 (.sel(DIR), .in_0(Q_5), .in_1(Q_7), .out(multiplexer_13_out));
  Multiplexer multiplexer_14 (.sel(LOAD), .in_0(multiplexer_13_out), .in_1(D_6), .out(multiplexer_14_out));
  D_FF_AS SR6 (.Set(1'b0), .D(multiplexer_14_out), .C(CPT), .Clr(RST), .Q(Q_6));  // open: nQ
  Multiplexer multiplexer_15 (.sel(DIR), .in_0(Q_6), .in_1(RSI), .out(multiplexer_15_out));
  Multiplexer multiplexer_16 (.sel(LOAD), .in_0(multiplexer_15_out), .in_1(D_7), .out(multiplexer_16_out));
  D_FF_AS SR7 (.Set(1'b0), .D(multiplexer_16_out), .C(CPT), .Clr(RST), .Q(Q_7));  // open: nQ

  assign DPT = DIR;
  assign SRO = Q_7;

  // Notes on the sheet:
  //   SRI: Serial Input
  //   SRO: Serial Output
  //   Q_0: SR0 OUTPUT
  //   RSI: Rear Serial In
  //   CPT: Clock Passthrough
  //   DPT: DIrection passthrough
  //   Q_1: SR0 OUTPUT
  //   Q_2: SR0 OUTPUT
  //   Q_3: SR0 OUTPUT
  //   Q_4: SR0 OUTPUT
  //   Q_5: SR0 OUTPUT
  //   Q_6: SR0 OUTPUT
  //   Q_7: SR0 OUTPUT
endmodule
