// Digital circuit 8B_BDSR_PP.dig as structural Verilog
// 8 cell serial organized register file, think a shift register but 8 of them in parallel
module _8B_BDSR_PP (
  input  EN,
  input  CLK,
  input  DIR,
  input  RST,
  input  SRI,
  input  RSI,
  input  LOAD,
  input  [7:0] D,
  output SRO,
  output CPT,
  output DPT,
  output [7:0] Q
);

  wire multiplexer_1_out, multiplexer_2_out, multiplexer_3_out, multiplexer_4_out, multiplexer_5_out,
       multiplexer_6_out, multiplexer_7_out, multiplexer_8_out, multiplexer_9_out, multiplexer_10_out,
       multiplexer_11_out, multiplexer_12_out, multiplexer_13_out, multiplexer_14_out, multiplexer_15_out,
       multiplexer_16_out;

  and and_1 (CPT, EN, CLK);
  Multiplexer multiplexer_1 (.sel(DIR), .in_0(SRI), .in_1(Q[6]), .out(multiplexer_1_out));
  Multiplexer multiplexer_2 (.sel(LOAD), .in_0(multiplexer_1_out), .in_1(D[7]), .out(multiplexer_2_out));
  D_FF_AS SR0 (.Set(1'b0), .D(multiplexer_2_out), .C(CPT), .Clr(RST), .Q(Q[7]));  // open: nQ
  Multiplexer multiplexer_3 (.sel(DIR), .in_0(Q[7]), .in_1(Q[5]), .out(multiplexer_3_out));
  Multiplexer multiplexer_4 (.sel(LOAD), .in_0(multiplexer_3_out), .in_1(D[6]), .out(multiplexer_4_out));
  D_FF_AS SR1 (.Set(1'b0), .D(multiplexer_4_out), .C(CPT), .Clr(RST), .Q(Q[6]));  // open: nQ
  Multiplexer multiplexer_5 (.sel(DIR), .in_0(Q[6]), .in_1(Q[4]), .out(multiplexer_5_out));
  Multiplexer multiplexer_6 (.sel(LOAD), .in_0(multiplexer_5_out), .in_1(D[5]), .out(multiplexer_6_out));
  D_FF_AS SR2 (.Set(1'b0), .D(multiplexer_6_out), .C(CPT), .Clr(RST), .Q(Q[5]));  // open: nQ
  Multiplexer multiplexer_7 (.sel(DIR), .in_0(Q[5]), .in_1(Q[3]), .out(multiplexer_7_out));
  Multiplexer multiplexer_8 (.sel(LOAD), .in_0(multiplexer_7_out), .in_1(D[4]), .out(multiplexer_8_out));
  D_FF_AS SR3 (.Set(1'b0), .D(multiplexer_8_out), .C(CPT), .Clr(RST), .Q(Q[4]));  // open: nQ
  Multiplexer multiplexer_9 (.sel(DIR), .in_0(Q[4]), .in_1(Q[2]), .out(multiplexer_9_out));
  Multiplexer multiplexer_10 (.sel(LOAD), .in_0(multiplexer_9_out), .in_1(D[3]), .out(multiplexer_10_out));
  D_FF_AS SR4 (.Set(1'b0), .D(multiplexer_10_out), .C(CPT), .Clr(RST), .Q(Q[3]));  // open: nQ
  Multiplexer multiplexer_11 (.sel(DIR), .in_0(Q[3]), .in_1(Q[1]), .out(multiplexer_11_out));
  Multiplexer multiplexer_12 (.sel(LOAD), .in_0(multiplexer_11_out), .in_1(D[2]), .out(multiplexer_12_out));
  D_FF_AS SR5 (.Set(1'b0), .D(multiplexer_12_out), .C(CPT), .Clr(RST), .Q(Q[2]));  // open: nQ
  Multiplexer multiplexer_13 (.sel(DIR), .in_0(Q[2]), .in_1(Q[0]), .out(multiplexer_13_out));
  Multiplexer multiplexer_14 (.sel(LOAD), .in_0(multiplexer_13_out), .in_1(D[1]), .out(multiplexer_14_out));
  D_FF_AS SR6 (.Set(1'b0), .D(multiplexer_14_out), .C(CPT), .Clr(RST), .Q(Q[1]));  // open: nQ
  Multiplexer multiplexer_15 (.sel(DIR), .in_0(Q[1]), .in_1(RSI), .out(multiplexer_15_out));
  Multiplexer multiplexer_16 (.sel(LOAD), .in_0(multiplexer_15_out), .in_1(D[0]), .out(multiplexer_16_out));
  D_FF_AS SR7 (.Set(1'b0), .D(multiplexer_16_out), .C(CPT), .Clr(RST), .Q(Q[0]));  // open: nQ

  assign DPT = DIR;
  assign SRO = Q[0];

  // Notes on the sheet:
  //   SRI: Serial Input
  //   SRO: Serial Output
  //   RSI: Rear Serial In
  //   CPT: Clock Passthrough
  //   DPT: DIrection passthrough
  //   D: Parallel In
  //   Q: Parallel Out
endmodule
