// Digital circuit CREG16.dig as structural Verilog
module CREG16 (
  input  E,
  input  [15:0] DW,
  input  CLK,
  input  S_l,
  input  S_u,
  input  R,
  output [15:0] QW
);

  wire driver_1_out, driver_2_out, driver_3_out, driver_4_out;

  assign driver_1_out = S_l ? R : 1'bz;  // Driver driver_1
  assign driver_2_out = S_u ? R : 1'bz;  // Driver driver_2
  PullDown pulldown_1 (.out(driver_2_out));
  assign driver_3_out = S_l ? E : 1'bz;  // Driver driver_3
  PullDown pulldown_2 (.out(driver_3_out));
  assign driver_4_out = S_u ? E : 1'bz;  // Driver driver_4
  PullDown pulldown_3 (.out(driver_4_out));
  PullDown pulldown_4 (.out(driver_1_out));
  CREG8 R_lower (.D(DW[7:0]), .R(driver_1_out), .CLK(CLK), .EN(driver_3_out), .Q(QW[7:0]));
  CREG8 R_upper (.D(DW[15:8]), .R(driver_2_out), .CLK(CLK), .EN(driver_4_out), .Q(QW[15:8]));
endmodule
