// Digital circuit CREG16CR.dig as structural Verilog
module CREG16CR (
  input  E,
  input  [15:0] DW,
  input  CLK,
  input  S_l,
  input  S_u,
  input  R,
  output [15:0] QW
);

  wire driver_1_out, driver_2_out;

  assign driver_1_out = S_l ? E : 1'bz;  // Driver driver_1
  PullDown pulldown_1 (.out(driver_1_out));
  assign driver_2_out = S_u ? E : 1'bz;  // Driver driver_2
  PullDown pulldown_2 (.out(driver_2_out));
  CREG8 R_lower (.D(DW[7:0]), .R(R), .CLK(CLK), .EN(driver_1_out), .Q(QW[7:0]));
  CREG8 R_upper (.D(DW[15:8]), .R(R), .CLK(CLK), .EN(driver_2_out), .Q(QW[15:8]));
endmodule
