// Digital circuit CREG8.dig as structural Verilog
module CREG8 (
  input  [7:0] D,
  input  R,
  input  CLK,
  input  EN,
  output [7:0] Q
);

  wire and_1_out;

  and and_1 (and_1_out, EN, CLK);
  D_FF_AS #(.Bits(8)) d_ff_as_1 (.Set(1'b0), .D(D), .C(and_1_out), .Clr(R), .Q(Q));  // open: nQ
endmodule
