// Digital circuit CWR32.dig as structural Verilog
module CWR32 (
  input  [31:0] DCW,
  input  CLK,
  input  R,
  input  E,
  output [31:0] QW
);

  CREG8 R_0 (.D(DCW[7:0]), .R(R), .CLK(CLK), .EN(E), .Q(QW[7:0]));
  CREG8 R_1 (.D(DCW[15:8]), .R(R), .CLK(CLK), .EN(E), .Q(QW[15:8]));
  CREG8 R_2 (.D(DCW[23:16]), .R(R), .CLK(CLK), .EN(E), .Q(QW[23:16]));
  CREG8 R_3 (.D(DCW[31:24]), .R(R), .CLK(CLK), .EN(E), .Q(QW[31:24]));
endmodule
