// Digital circuit INCR7BTSTBOARD.dig as structural Verilog
module INCR7BTSTBOARD (
  input  clk,
  input  [3:0] in_2,
  input  [7:0] in_3
);

  wire and_1_out, and_2_out, and_3_out, and_4_out, and_5_out, button_1_out, button_2_out, button_3_out,
       button_4_out, button_5_out, d_ff_as_1_q, d_ff_as_2_q, d_ff_as_3_q, d_ff_as_4_q, d_ff_as_5_q,
       d_ff_as_6_q, dipswitch_1_out, dipswitch_2_out, dipswitch_3_out, dipswitch_4_out, dipswitch_5_out,
       incr7bchp_1_p8, or_1_out, or_2_out, PAGEADDR_ovf;
  wire [3:0] dipswitch_6_out, dipswitch_10_out, PAGESEL_out;
  wire [7:0] demultiplexer_1_out_0, demultiplexer_1_out_1, incr7bchp_1_p4, incr7bchp_1_p9, PAGEADDR_out;

  Button button_1 (.out(button_1_out));
  DipSwitch dipswitch_1 (.out(dipswitch_1_out));
  Button button_2 (.out(button_2_out));
  DipSwitch dipswitch_2 (.out(dipswitch_2_out));
  and and_1 (and_1_out, dipswitch_2_out, clk);
  or or_1 (or_1_out, button_2_out, and_1_out);
  Button button_3 (.out(button_3_out));
  or or_2 (or_2_out, and_3_out, and_2_out);
  Button button_4 (.out(button_4_out));
  Button button_5 (.out(button_5_out));
  DipSwitch dipswitch_3 (.out(dipswitch_3_out));
  DipSwitch dipswitch_4 (.out(dipswitch_4_out));
  DipSwitch dipswitch_5 (.out(dipswitch_5_out));
  CounterPreset #(.Bits(4)) PAGESEL (
    .en(button_3_out), .C(or_1_out), .dir(dipswitch_3_out), .in(in_2), .ld(dipswitch_4_out),
    .clr(button_1_out), .out(PAGESEL_out));  // open: ovf
  CounterPreset #(.Bits(8)) PAGEADDR (
    .en(or_2_out), .C(or_1_out), .dir(1'b0), .in(in_3), .ld(dipswitch_5_out), .clr(button_1_out),
    .out(PAGEADDR_out), .ovf(PAGEADDR_ovf));
  DipSwitch dipswitch_6 (.out(dipswitch_6_out[0]));
  DipSwitch dipswitch_7 (.out(dipswitch_6_out[1]));
  DipSwitch dipswitch_8 (.out(dipswitch_6_out[2]));
  DipSwitch dipswitch_9 (.out(dipswitch_6_out[3]));
  DipSwitch dipswitch_10 (.out(dipswitch_10_out[0]));
  DipSwitch dipswitch_11 (.out(dipswitch_10_out[1]));
  DipSwitch dipswitch_12 (.out(dipswitch_10_out[2]));
  DipSwitch dipswitch_13 (.out(dipswitch_10_out[3]));
  Seven_Seg_Hex seven_seg_hex_1 (.d(dipswitch_6_out), .dp(1'b0));
  and and_2 (and_2_out, d_ff_as_3_q, ~PAGEADDR_ovf);  // And
  and and_3 (and_3_out, d_ff_as_4_q, ~PAGEADDR_ovf);  // And
  Seven_Seg_Hex seven_seg_hex_2 (.d(dipswitch_10_out), .dp(1'b0));
  D_FF_AS d_ff_as_1 (.Set(button_4_out), .D(and_4_out), .C(or_1_out), .Clr(button_1_out), .Q(d_ff_as_1_q));  // open: nQ
  D_FF_AS d_ff_as_2 (.Set(button_5_out), .D(and_5_out), .C(or_1_out), .Clr(button_1_out), .Q(d_ff_as_2_q));  // open: nQ
  // INCR7BCHP incr7bchp_1: pin names not known; wires that end beside it: {dipswitch_10_out, dipswitch_6_out}, PAGEADDR_out, dipswitch_1_out, incr7bchp_1_p4, button_1_out, d_ff_as_2_q, or_1_out, incr7bchp_1_p8, incr7bchp_1_p9
  EEPROMDualPort #(.AddrBits(12), .Bits(8)) FLASH (
    .A({PAGESEL_out, PAGEADDR_out}), .Din(demultiplexer_1_out_1), .str(d_ff_as_1_q), .C(or_1_out),
    .ld(d_ff_as_2_q), .D(incr7bchp_1_p4));
  D_FF_AS d_ff_as_3 (.Set(1'b0), .D(d_ff_as_1_q), .C(or_1_out), .Clr(button_1_out), .Q(d_ff_as_3_q));  // open: nQ
  D_FF_AS d_ff_as_4 (.Set(1'b0), .D(d_ff_as_2_q), .C(or_1_out), .Clr(button_1_out), .Q(d_ff_as_4_q));  // open: nQ
  and and_4 (and_4_out, d_ff_as_5_q, ~PAGEADDR_ovf);  // And
  D_FF_AS d_ff_as_5 (.Set(1'b0), .D(d_ff_as_3_q), .C(or_1_out), .Clr(button_1_out), .Q(d_ff_as_5_q));  // open: nQ
  and and_5 (and_5_out, d_ff_as_6_q, ~PAGEADDR_ovf);  // And
  D_FF_AS d_ff_as_6 (.Set(1'b0), .D(d_ff_as_4_q), .C(or_1_out), .Clr(button_1_out), .Q(d_ff_as_6_q));  // open: nQ
  DipSwitch dipswitch_14 (.out(incr7bchp_1_p8));
  Demultiplexer #(.Bits(8)) demultiplexer_1 (
    .sel(incr7bchp_1_p8), .in(incr7bchp_1_p9), .out_0(demultiplexer_1_out_0), .out_1(demultiplexer_1_out_1));
  Seven_Seg_Hex seven_seg_hex_3 (.d(demultiplexer_1_out_0[7:4]), .dp(1'b0));
  Seven_Seg_Hex seven_seg_hex_4 (.d(demultiplexer_1_out_0[3:0]), .dp(1'b0));
endmodule
