// Digital circuit INCR8TB.dig as structural Verilog
module INCR8TB (
  input  clk
);

  wire and_1_out, CLOCK_ENABLE_out, or_1_out, STEP_MANUAL_out;

  DipSwitch CLOCK_ENABLE (.out(CLOCK_ENABLE_out));
  Button STEP_MANUAL (.out(STEP_MANUAL_out));
  and and_1 (and_1_out, CLOCK_ENABLE_out, clk);
  or or_1 (or_1_out, STEP_MANUAL_out, and_1_out);
  // incr8upgr8 incr8upgr8_1: pin names not known; wires that end beside it: or_1_out
  EEPROM eeprom_1 ();  // open: A, CS, WE, OE, D

  // Notes on the sheet:
  //   clk: Hz: 100
endmodule
