// Digital circuit PC16.dig as structural Verilog
module PC16 (
  input  WE,
  input  [15:0] DW,
  input  CLK,
  input  S_l,
  input  S_u,
  input  R,
  input  PC_plus__plus,
  input  [1:0] STRIDE,
  input  COUNT,
  input  LOAD,
  output [15:0] QW
);

  wire driver_1_out, driver_2_out, driver_3_out, driver_4_out, or_1_out, or_2_out;
  wire [15:0] add_1_s, multiplexer_1_out, pulldown_5_out;

  Multiplexer #(.Bits(16)) multiplexer_1 (.sel(LOAD), .in_0(pulldown_5_out), .in_1(DW), .out(multiplexer_1_out));
  assign driver_1_out = S_l ? R : 1'bz;  // Driver driver_1
  assign driver_2_out = S_u ? R : 1'bz;  // Driver driver_2
  assign driver_3_out = S_l ? WE : 1'bz;  // Driver driver_3
  assign driver_4_out = S_u ? WE : 1'bz;  // Driver driver_4
  PullDown pulldown_1 (.out(driver_2_out));
  PullDown pulldown_2 (.out(driver_3_out));
  PullDown pulldown_3 (.out(driver_4_out));
  or or_1 (or_1_out, driver_3_out, COUNT);
  or or_2 (or_2_out, driver_4_out, COUNT);
  PullDown pulldown_4 (.out(driver_1_out));
  CREG8 R_lower (.D(multiplexer_1_out[7:0]), .R(driver_1_out), .CLK(CLK), .EN(or_1_out), .Q(QW[7:0]));
  CREG8 R_upper (.D(multiplexer_1_out[15:8]), .R(driver_2_out), .CLK(CLK), .EN(or_2_out), .Q(QW[15:8]));
  Add #(.Bits(16)) add_1 (.a(QW), .b({{14{1'b0}}, STRIDE}), .c_i(PC_plus__plus), .s(add_1_s));  // open: c_o
  PullDown #(.Bits(16)) pulldown_5 (.out(pulldown_5_out));
  assign pulldown_5_out = COUNT ? add_1_s : 16'bz;  // Driver driver_5
endmodule
