// Digital circuit RISIKO168.dig as structural Verilog
module RISIKO168 (
);

  wire undriven;
  wire [15:0] PC_out;

  CounterPreset #(.Bits(16)) PC (.C(undriven), .out(PC_out));  // open: en, dir, in, ld, clr, ovf
  RAMDualAccess #(.AddrBits(8), .Bits(16)) CACHE (.C(undriven), .A2(PC_out[7:0]));  // open: str, ld, A1, Din1, D1, D2
  // Pins of 8 and 16 bits meet at PC_out
endmodule
