// Digital circuit RISIKOFL.dig as structural Verilog
module RISIKOFL (
);

  wire demultiplexer_4_out_0, demultiplexer_4_out_1, demultiplexer_5_out_0, demultiplexer_5_out_1,
       demultiplexer_6_out_0, demultiplexer_6_out_1, demultiplexer_7_out_0, demultiplexer_7_out_1,
       lower_PC_ovf, undriven, undriven_2, undriven_3, undriven_4, undriven_5, undriven_6, undriven_7,
       undriven_8, undriven_9, undriven_10, undriven_11, undriven_12;
  wire [7:0] AL_q, AU_q, demultiplexer_1_out_0, demultiplexer_1_out_1, demultiplexer_2_out_0,
       demultiplexer_2_out_1, demultiplexer_3_out_0, demultiplexer_3_out_1, driver_2_out, eeprom_1_d,
       lower_PC_out, multiplexer_2_out, ramsingleportsel_1_d, undriven_13, upper_PC_out;
  wire [15:0] multiplexer_1_out;

  Demultiplexer #(.Bits(8)) demultiplexer_1 (
    .sel(undriven), .out_0(demultiplexer_1_out_0), .out_1(demultiplexer_1_out_1));  // open: in
  Demultiplexer #(.Bits(8)) demultiplexer_2 (
    .sel(undriven_3), .in(demultiplexer_1_out_1), .out_0(demultiplexer_2_out_0), .out_1(demultiplexer_2_out_1));
  Demultiplexer #(.Bits(8)) demultiplexer_3 (
    .sel(undriven_5), .in(demultiplexer_1_out_0), .out_0(demultiplexer_3_out_0), .out_1(demultiplexer_3_out_1));
  Demultiplexer demultiplexer_4 (
    .sel(undriven_3), .in(undriven_2), .out_0(demultiplexer_4_out_0), .out_1(demultiplexer_4_out_1));
  Demultiplexer demultiplexer_5 (
    .sel(undriven_5), .in(undriven_4), .out_0(demultiplexer_5_out_0), .out_1(demultiplexer_5_out_1));
  CREG8 AL (.D(demultiplexer_3_out_0), .R(undriven_8), .CLK(undriven_9), .EN(demultiplexer_5_out_0), .Q(AL_q));
  CREG8 AU (.D(demultiplexer_3_out_1), .R(undriven_8), .CLK(undriven_9), .EN(demultiplexer_5_out_1), .Q(AU_q));
  CounterPreset #(.Bits(8)) lower_PC (
    .C(undriven_7), .dir(1'b0), .in(demultiplexer_2_out_0), .ld(demultiplexer_4_out_0), .clr(undriven_6),
    .out(lower_PC_out), .ovf(lower_PC_ovf));  // open: en
  CounterPreset #(.Bits(8)) upper_PC (
    .en(lower_PC_ovf), .C(undriven_7), .dir(1'b0), .in(demultiplexer_2_out_1), .ld(demultiplexer_4_out_1),
    .clr(undriven_6), .out(upper_PC_out));  // open: ovf
  Multiplexer #(.Bits(16)) multiplexer_1 (
    .sel(undriven_10), .in_0({AU_q, AL_q}), .in_1({upper_PC_out, lower_PC_out}), .out(multiplexer_1_out));
  Demultiplexer demultiplexer_6 (
    .sel(multiplexer_1_out[15]), .in(undriven_11), .out_0(demultiplexer_6_out_0),
    .out_1(demultiplexer_6_out_1));
  Multiplexer #(.Bits(8), .Selector_Bits(3)) multiplexer_2 (.out(multiplexer_2_out));  // open: sel, in_0, in_1, in_2, in_3, in_4, in_5, in_6, in_7
  Demultiplexer demultiplexer_7 (
    .sel(multiplexer_1_out[15]), .in(undriven_12), .out_0(demultiplexer_7_out_0),
    .out_1(demultiplexer_7_out_1));
  RAMSinglePortSel #(.AddrBits(15), .Bits(8)) ramsingleportsel_1 (
    .A(multiplexer_1_out[14:0]), .CS(multiplexer_1_out[15]), .WE(demultiplexer_7_out_1),
    .OE(demultiplexer_6_out_1), .D(ramsingleportsel_1_d));
  EEPROM #(.AddrBits(15), .Bits(8)) eeprom_1 (
    .A(multiplexer_1_out[14:0]), .CS(~multiplexer_1_out[15]), .WE(demultiplexer_7_out_0),
    .OE(demultiplexer_6_out_0), .D(eeprom_1_d));
  // od8x8bsrfV2 od8x8bsrfv2_1: pin names not known; wires that end beside it: multiplexer_2_out
  PullDown #(.Bits(8)) pulldown_1 (.out(ramsingleportsel_1_d));
  PullDown #(.Bits(8)) pulldown_2 (.out(eeprom_1_d));
  assign ramsingleportsel_1_d = demultiplexer_7_out_1 ? undriven_13 : 8'bz;  // Driver driver_1
  assign driver_2_out = demultiplexer_6_out_1 ? ramsingleportsel_1_d : 8'bz;  // Driver driver_2
  assign eeprom_1_d = demultiplexer_7_out_0 ? undriven_13 : 8'bz;  // Driver driver_3
  assign driver_2_out = demultiplexer_6_out_0 ? eeprom_1_d : 8'bz;  // Driver driver_4
  PullDown #(.Bits(8)) pulldown_3 (.out(driver_2_out));
endmodule
