// Digital circuit RISIKOFL2.dig as structural Verilog
module RISIKOFL2 (
  input  [7:0] I,
  output [7:0] O
);

  wire AL_EN, ALU_FLG_SET, and_1_out, and_2_out, and_4_out, and_6_out, and_9_out, and_10_out, and_11_out,
       AU_EN, CLK_out, DECODE, decoder_1_out_0, decoder_1_out_1, decoder_1_out_2, decoder_1_out_3,
       demultiplexer_6_out_0, demultiplexer_6_out_1, demultiplexer_7_out_0, demultiplexer_7_out_1, DXAPC,
       EXECUTE, FETCH, FETCH_IR, FETCH_OP, FLG_CARRY, FLG_NEGATIVE, FLG_NZ, FLG_ZERO, KICKIT_out, LD_ST,
       lower_PC_ovf, LPC_EN, MEM_RD, MEM_WRT, multiplexer_4_out, or_2_out, or_3_out, PC_INC, RESET_out,
       RX_EN, RY_EN, ssalu8_1_co, ssalu8_1_n, ssalu8_1_z, STK_EN, SXY, UPC_EN, WCARRY;
  wire [0:0] demultiplexer_2_out_2;
  wire [1:0] demultiplexer_2_out_2_2;
  wire [2:0] ALUOP, INSTRUCTION_q_2, POP_PLX, PSH_PLX;
  wire [2:2] demultiplexer_1_out_3;
  wire [7:0] AL_q, ALUOUT, AU_q, demultiplexer_3_out_1, demultiplexer_3_out_2, demultiplexer_3_out_3,
       demultiplexer_3_out_4, demultiplexer_3_out_5, demultiplexer_3_out_6, demultiplexer_3_out_7,
       demultiplexer_5_out_0, demultiplexer_5_out_1, demultiplexer_8_out_0, demultiplexer_8_out_1,
       driver_2_out, eeprom_1_d, INSTRUCTION_q, LIT, lower_PC_out, multiplexer_1_out, multiplexer_2_out,
       multiplexer_3_out, multiplexer_5_out, multiplexer_6_out, od8x8bsrfv2_1_top, ramsingleportsel_1_d, X_q,
       Y_q;
  wire [15:0] multiplexer_7_out;
  wire [15:8] upper_PC_out;

  Multiplexer #(.Bits(8), .Selector_Bits(3)) multiplexer_1 (
    .sel(PSH_PLX), .in_0(I), .in_1(ALUOUT), .in_2(LIT), .in_3(demultiplexer_8_out_0), .in_4(AL_q),
    .in_5(AU_q), .in_6(lower_PC_out), .in_7(upper_PC_out), .out(multiplexer_1_out));
  Demultiplexer #(.Selector_Bits(2), .Bits(3)) demultiplexer_1 (
    .sel(INSTRUCTION_q[1:0]), .in(INSTRUCTION_q[7:5]), .out_3({demultiplexer_1_out_3[2], SXY, WCARRY}));  // open: out_0, out_1, out_2
  LED led_1 (.in(FLG_CARRY));
  LED led_2 (.in(FLG_ZERO));
  LED led_3 (.in(FLG_NEGATIVE));
  Decoder #(.Selector_Bits(2)) decoder_1 (
    .sel(INSTRUCTION_q[1:0]), .out_0(decoder_1_out_0), .out_1(decoder_1_out_1), .out_2(decoder_1_out_2),
    .out_3(decoder_1_out_3));
  Demultiplexer #(.Bits(3), .Selector_Bits(2)) demultiplexer_2 (
    .sel(INSTRUCTION_q[1:0]), .in(INSTRUCTION_q_2), .out_0(PSH_PLX), .out_1(POP_PLX),
    .out_2({demultiplexer_2_out_2_2, demultiplexer_2_out_2[0]}), .out_3(ALUOP));
  and and_1 (and_1_out, INSTRUCTION_q_2[1], EXECUTE, INSTRUCTION_q_2[0]);
  and and_2 (and_2_out, decoder_1_out_0, EXECUTE);
  and and_3 (LD_ST, decoder_1_out_1, EXECUTE);
  and and_4 (and_4_out, decoder_1_out_2, EXECUTE);
  and and_5 (ALU_FLG_SET, decoder_1_out_3, EXECUTE);
  od8x8bsrfV2 od8x8bsrfv2_1 (
    .SRI(multiplexer_1_out), .DIR(LD_ST), .EN(STK_EN), .CLK(CLK_out), .RST(RESET_out), .RSI({8{1'b0}}),
    .TOP(od8x8bsrfv2_1_top));  // open: SRO, CPT, DPT
  DipSwitch CLK (.out(CLK_out));
  DipSwitch RESET (.out(RESET_out));
  Demultiplexer #(.Selector_Bits(3), .Bits(8)) demultiplexer_3 (
    .sel(POP_PLX), .in(od8x8bsrfv2_1_top), .out_0(O), .out_1(demultiplexer_3_out_1),
    .out_2(demultiplexer_3_out_2), .out_3(demultiplexer_3_out_3), .out_4(demultiplexer_3_out_4),
    .out_5(demultiplexer_3_out_5), .out_6(demultiplexer_3_out_6), .out_7(demultiplexer_3_out_7));
  and and_6 (and_6_out, and_1_out, and_2_out);
  or or_1 (STK_EN, and_2_out, LD_ST);
  Demultiplexer #(.Selector_Bits(3)) demultiplexer_4 (
    .sel(POP_PLX), .in(LD_ST), .out_1(RX_EN), .out_2(RY_EN), .out_3(MEM_WRT), .out_4(AL_EN), .out_5(AU_EN),
    .out_6(LPC_EN), .out_7(UPC_EN));  // open: out_0
  Multiplexer #(.Bits(8)) multiplexer_2 (
    .sel(DXAPC), .in_0(demultiplexer_3_out_6), .in_1(AL_q), .out(multiplexer_2_out));
  Multiplexer #(.Bits(8)) multiplexer_3 (
    .sel(DXAPC), .in_0(demultiplexer_3_out_7), .in_1(AU_q), .out(multiplexer_3_out));
  and and_7 (MEM_WRT, and_1_out, LD_ST);
  Demultiplexer #(.Bits(8)) demultiplexer_5 (
    .sel(FETCH_OP), .in(demultiplexer_8_out_1), .out_0(demultiplexer_5_out_0), .out_1(demultiplexer_5_out_1));
  CREG8 INSTRUCTION (
    .D(demultiplexer_5_out_0), .R(RESET_out), .CLK(CLK_out), .EN(FETCH_IR),
    .Q({INSTRUCTION_q[7:5], INSTRUCTION_q_2, INSTRUCTION_q[1:0]}));
  CREG8 OPERAND (.D(demultiplexer_5_out_1), .R(RESET_out), .CLK(CLK_out), .EN(FETCH_OP), .Q(LIT));
  CREG8 X (.D(demultiplexer_3_out_1), .R(RESET_out), .CLK(CLK_out), .EN(RX_EN), .Q(X_q));
  CREG8 Y (.D(demultiplexer_3_out_2), .R(RESET_out), .CLK(CLK_out), .EN(RY_EN), .Q(Y_q));
  CREG8 AL (.D(demultiplexer_3_out_4), .R(RESET_out), .CLK(CLK_out), .EN(AL_EN), .Q(AL_q));
  CREG8 AU (.D(demultiplexer_3_out_5), .R(RESET_out), .CLK(CLK_out), .EN(AU_EN), .Q(AU_q));
  CounterPreset #(.Bits(8)) lower_PC (
    .en(PC_INC), .C(CLK_out), .dir(1'b0), .in(multiplexer_2_out), .ld(LPC_EN), .clr(RESET_out),
    .out(lower_PC_out), .ovf(lower_PC_ovf));
  CounterPreset #(.Bits(8)) upper_PC (
    .en(lower_PC_ovf), .C(CLK_out), .dir(1'b0), .in(multiplexer_3_out), .ld(UPC_EN), .clr(RESET_out),
    .out(upper_PC_out));  // open: ovf
  // Probe on {INSTRUCTION_q[7:5], INSTRUCTION_q_2, INSTRUCTION_q[1:0]}
  // Probe on LIT
  and and_8 (DXAPC, and_4_out, or_2_out);
  Multiplexer #(.Selector_Bits(2)) multiplexer_4 (
    .sel(demultiplexer_2_out_2_2), .in_0(FLG_ZERO), .in_1(FLG_NZ), .in_2(FLG_NEGATIVE), .in_3(FLG_CARRY),
    .out(multiplexer_4_out));
  Multiplexer #(.Bits(8)) multiplexer_5 (.sel(SXY), .in_0(X_q), .in_1(Y_q), .out(multiplexer_5_out));
  Multiplexer #(.Bits(8)) multiplexer_6 (.sel(SXY), .in_0(Y_q), .in_1(X_q), .out(multiplexer_6_out));
  or or_2 (or_2_out, multiplexer_4_out, ~demultiplexer_2_out_2[0]);  // Or
  PullDown #(.Bits(8)) pulldown_1 (.out({INSTRUCTION_q[7:5], INSTRUCTION_q_2, INSTRUCTION_q[1:0]}));
  Multiplexer #(.Bits(16)) multiplexer_7 (
    .sel(FETCH), .in_0({AU_q, AL_q}), .in_1({upper_PC_out, lower_PC_out}), .out(multiplexer_7_out));
  Demultiplexer demultiplexer_6 (
    .sel(multiplexer_7_out[15]), .in(MEM_RD), .out_0(demultiplexer_6_out_0), .out_1(demultiplexer_6_out_1));
  and and_9 (and_9_out, MEM_WRT, CLK_out);
  Demultiplexer demultiplexer_7 (
    .sel(multiplexer_7_out[15]), .in(and_9_out), .out_0(demultiplexer_7_out_0), .out_1(demultiplexer_7_out_1));
  D_FF_AS FIR (.Set(KICKIT_out), .D(EXECUTE), .C(CLK_out), .Clr(RESET_out), .Q(FETCH_IR));  // open: nQ
  DipSwitch KICKIT (.out(KICKIT_out));
  SSALU8 ssalu8_1 (
    .A(multiplexer_5_out), .X(multiplexer_6_out), .OP(ALUOP[1:0]), .ALT(ALUOP[2]), .CO(ssalu8_1_co),
    .CIN(and_11_out), .Y(ALUOUT), .Z(ssalu8_1_z), .N(ssalu8_1_n));
  or or_3 (or_3_out, FETCH_IR, FETCH_OP);
  RAMSinglePortSel #(.AddrBits(15), .Bits(8)) ramsingleportsel_1 (
    .A(multiplexer_7_out[14:0]), .CS(multiplexer_7_out[15]), .WE(demultiplexer_7_out_1),
    .OE(demultiplexer_6_out_1), .D(ramsingleportsel_1_d));
  EEPROM #(.AddrBits(15), .Bits(8)) eeprom_1 (
    .A(multiplexer_7_out[14:0]), .CS(~multiplexer_7_out[15]), .WE(demultiplexer_7_out_0),
    .OE(demultiplexer_6_out_0), .D(eeprom_1_d));
  or or_4 (MEM_RD, and_6_out, or_3_out);
  or or_5 (FETCH, FETCH_IR, FETCH_OP);
  or or_6 (PC_INC, FETCH_IR, FETCH_OP);
  D_FF_AS FOP (.Set(1'b0), .D(FETCH_IR), .C(CLK_out), .Clr(RESET_out), .Q(FETCH_OP));  // open: nQ
  PullDown #(.Bits(8)) pulldown_2 (.out(ramsingleportsel_1_d));
  PullDown #(.Bits(8)) pulldown_3 (.out(eeprom_1_d));
  and and_10 (and_10_out, CLK_out, ALU_FLG_SET);
  assign ramsingleportsel_1_d = demultiplexer_7_out_1 ? demultiplexer_3_out_3 : 8'bz;  // Driver driver_1
  assign driver_2_out = demultiplexer_6_out_1 ? ramsingleportsel_1_d : 8'bz;  // Driver driver_2
  assign eeprom_1_d = demultiplexer_7_out_0 ? demultiplexer_3_out_3 : 8'bz;  // Driver driver_3
  assign driver_2_out = demultiplexer_6_out_0 ? eeprom_1_d : 8'bz;  // Driver driver_4
  PullDown #(.Bits(8)) pulldown_4 (.out(driver_2_out));
  D_FF_AS DEC (.Set(1'b0), .D(FETCH_OP), .C(CLK_out), .Clr(RESET_out), .Q(DECODE));  // open: nQ
  and and_11 (and_11_out, FLG_CARRY, WCARRY);
  D_FF_AS CARRY (.Set(1'b0), .D(ssalu8_1_co), .C(and_10_out), .Clr(CLK_out), .Q(FLG_CARRY));  // open: nQ
  Demultiplexer #(.Bits(8)) demultiplexer_8 (
    .sel(FETCH), .in(driver_2_out), .out_0(demultiplexer_8_out_0), .out_1(demultiplexer_8_out_1));
  D_FF_AS EXE (.Set(1'b0), .D(DECODE), .C(CLK_out), .Clr(RESET_out), .Q(EXECUTE));  // open: nQ
  D_FF_AS ZERO (.Set(1'b0), .D(ssalu8_1_z), .C(and_10_out), .Clr(CLK_out), .Q(FLG_ZERO), .nQ(FLG_NZ));
  D_FF_AS NEGATIVE (.Set(1'b0), .D(ssalu8_1_n), .C(and_10_out), .Clr(CLK_out), .Q(FLG_NEGATIVE));  // open: nQ

  // Other names for the same wires on the sheet: STK_DIR = LD_ST

  // Notes on the sheet:
  //   contents of eeprom_1 (hex, n*v repeats v):
  //   8,10,5,0,37,0,5,0,e
endmodule
