// Digital circuit RISIKOFL3A2B1.dig as structural Verilog
module RISIKOFL3A2B1 (
  input  [7:0] I,
  input  RST,
  input  CLK,
  input  EN,
  input  [7:0] D,
  output [7:0] O,
  output RD,
  output WD,
  output [15:0] A
);

  wire AL_EN, ALU_FLG_SET, and_1_out, and_2_out, and_3_out, and_5_out, and_7_out, and_10_out, and_11_out,
       and_12_out, and_13_out, and_14_out, AU_EN, DECODE, decoder_1_out_0, decoder_1_out_1, decoder_1_out_2,
       decoder_1_out_3, demultiplexer_5_out_6, demultiplexer_5_out_7, DXAPC, EXECUTE, FETCH, FETCH_IR,
       FETCH_OP, FLG_CARRY, FLG_NEGATIVE, FLG_NZ, FLG_ZERO, LD_ST, lower_PC_ovf, LPC_EN, multiplexer_5_out,
       or_1_out, or_2_out, or_4_out, or_7_out, PC_INC, RO_EN, RX_EN, RY_EN, ssalu8_1_co, ssalu8_1_n,
       ssalu8_1_z, STK_EN, SXY, UPC_EN, WCARRY;
  wire [0:0] demultiplexer_2_out_2;
  wire [1:0] demultiplexer_2_out_2_2;
  wire [2:0] ALUOP, demultiplexer_2_out_0, INSTRUCTION_q_2, POP_PLX, PSH_PLX;
  wire [2:2] demultiplexer_1_out_3;
  wire [7:0] AL_q, ALUOUT, AU_q, demultiplexer_3_out_0, demultiplexer_3_out_1, demultiplexer_3_out_2,
       demultiplexer_3_out_3, demultiplexer_3_out_4, demultiplexer_3_out_5, demultiplexer_3_out_6,
       demultiplexer_3_out_7, demultiplexer_4_out_0, demultiplexer_4_out_1, demultiplexer_6_out_0,
       demultiplexer_6_out_1, driver_2_out, INSTRUCTION_q, LIT, lower_PC_out, multiplexer_1_out,
       multiplexer_3_out, multiplexer_4_out, multiplexer_6_out, multiplexer_7_out, od8x8bsrfv2_1_top, X_q,
       Y_q;
  wire [15:8] upper_PC_out;

  and and_1 (and_1_out, INSTRUCTION_q[1], INSTRUCTION_q[0]);
  Multiplexer #(.Selector_Bits(3), .Bits(8)) multiplexer_1 (
    .sel(PSH_PLX), .in_0(I), .in_1(ALUOUT), .in_2(LIT), .in_3(demultiplexer_6_out_0), .in_4(AL_q),
    .in_5(AU_q), .in_6(lower_PC_out), .in_7(upper_PC_out), .out(multiplexer_1_out));
  Demultiplexer #(.Selector_Bits(2), .Bits(3)) demultiplexer_1 (
    .sel(INSTRUCTION_q[1:0]), .in(INSTRUCTION_q[7:5]), .out_3({demultiplexer_1_out_3[2], SXY, WCARRY}));  // open: out_0, out_1, out_2
  Decoder #(.Selector_Bits(2)) decoder_1 (
    .sel(INSTRUCTION_q[1:0]), .out_0(decoder_1_out_0), .out_1(decoder_1_out_1), .out_2(decoder_1_out_2),
    .out_3(decoder_1_out_3));
  Demultiplexer #(.Selector_Bits(2), .Bits(3)) demultiplexer_2 (
    .sel(INSTRUCTION_q[1:0]), .in(INSTRUCTION_q_2), .out_0(demultiplexer_2_out_0), .out_1(POP_PLX),
    .out_2({demultiplexer_2_out_2_2, demultiplexer_2_out_2[0]}), .out_3(ALUOP));
  and and_2 (and_2_out, INSTRUCTION_q_2[1], INSTRUCTION_q_2[0]);
  and and_3 (and_3_out, decoder_1_out_0, INSTRUCTION_q[7], DECODE);
  and and_4 (LD_ST, decoder_1_out_1, DECODE);
  and and_5 (and_5_out, decoder_1_out_2, DECODE);
  and and_6 (ALU_FLG_SET, decoder_1_out_3, DECODE);
  od8x8bsrfV2 od8x8bsrfv2_1 (
    .SRI(multiplexer_1_out), .DIR(LD_ST), .EN(STK_EN), .CLK(CLK), .RST(RST), .RSI({8{1'b0}}),
    .TOP(od8x8bsrfv2_1_top));  // open: SRO, CPT, DPT
  CREG8 OUTPUT (.D(demultiplexer_3_out_0), .R(RST), .CLK(CLK), .EN(RO_EN), .Q(O));
  Demultiplexer #(.Selector_Bits(3), .Bits(8)) demultiplexer_3 (
    .sel(POP_PLX), .in(od8x8bsrfv2_1_top), .out_0(demultiplexer_3_out_0), .out_1(demultiplexer_3_out_1),
    .out_2(demultiplexer_3_out_2), .out_3(demultiplexer_3_out_3), .out_4(demultiplexer_3_out_4),
    .out_5(demultiplexer_3_out_5), .out_6(demultiplexer_3_out_6), .out_7(demultiplexer_3_out_7));
  and and_7 (and_7_out, and_2_out, and_3_out);
  or or_1 (or_1_out, EXECUTE, DECODE);
  or or_2 (or_2_out, and_3_out, LD_ST);
  Multiplexer #(.Bits(3)) multiplexer_2 (.sel(and_1_out), .in_0(demultiplexer_2_out_0), .in_1(3'b001), .out(PSH_PLX));
  Multiplexer #(.Bits(8)) multiplexer_3 (
    .sel(DXAPC), .in_0(demultiplexer_3_out_6), .in_1(AL_q), .out(multiplexer_3_out));
  Multiplexer #(.Bits(8)) multiplexer_4 (
    .sel(DXAPC), .in_0(demultiplexer_3_out_7), .in_1(AU_q), .out(multiplexer_4_out));
  and and_8 (WD, and_2_out, or_1_out, LD_ST);
  Demultiplexer #(.Bits(8)) demultiplexer_4 (
    .sel(FETCH_OP), .in(demultiplexer_6_out_1), .out_0(demultiplexer_4_out_0), .out_1(demultiplexer_4_out_1));
  CREG8 INSTRUCTION (
    .D(demultiplexer_4_out_0), .R(RST), .CLK(CLK), .EN(FETCH_IR),
    .Q({INSTRUCTION_q[7:5], INSTRUCTION_q_2, INSTRUCTION_q[1:0]}));
  CREG8 OPERAND (.D(demultiplexer_4_out_1), .R(RST), .CLK(CLK), .EN(FETCH_OP), .Q(LIT));
  CREG8 X (.D(demultiplexer_3_out_1), .R(RST), .CLK(CLK), .EN(RX_EN), .Q(X_q));
  CREG8 Y (.D(demultiplexer_3_out_2), .R(RST), .CLK(CLK), .EN(RY_EN), .Q(Y_q));
  CREG8 AL (.D(demultiplexer_3_out_4), .R(RST), .CLK(CLK), .EN(AL_EN), .Q(AL_q));
  CREG8 AU (.D(demultiplexer_3_out_5), .R(RST), .CLK(CLK), .EN(AU_EN), .Q(AU_q));
  CounterPreset #(.Bits(8)) lower_PC (
    .en(PC_INC), .C(CLK), .dir(1'b0), .in(multiplexer_3_out), .ld(LPC_EN), .clr(RST), .out(lower_PC_out),
    .ovf(lower_PC_ovf));
  CounterPreset #(.Bits(8)) upper_PC (
    .en(lower_PC_ovf), .C(CLK), .dir(1'b0), .in(multiplexer_4_out), .ld(UPC_EN), .clr(RST), .out(upper_PC_out));  // open: ovf
  or or_3 (STK_EN, or_2_out, and_1_out);
  // Probe on {INSTRUCTION_q[7:5], INSTRUCTION_q_2, INSTRUCTION_q[1:0]}
  // Probe on LIT
  and and_9 (DXAPC, and_5_out, or_4_out);
  Multiplexer #(.Selector_Bits(2)) multiplexer_5 (
    .sel(demultiplexer_2_out_2_2), .in_0(FLG_ZERO), .in_1(FLG_NZ), .in_2(FLG_NEGATIVE), .in_3(FLG_CARRY),
    .out(multiplexer_5_out));
  Multiplexer #(.Bits(8)) multiplexer_6 (.sel(SXY), .in_0(X_q), .in_1(Y_q), .out(multiplexer_6_out));
  Multiplexer #(.Bits(8)) multiplexer_7 (.sel(SXY), .in_0(Y_q), .in_1(X_q), .out(multiplexer_7_out));
  or or_4 (or_4_out, multiplexer_5_out, ~demultiplexer_2_out_2[0]);  // Or
  Demultiplexer #(.Selector_Bits(3)) demultiplexer_5 (
    .sel(POP_PLX), .in(LD_ST), .out_0(RO_EN), .out_1(RX_EN), .out_2(RY_EN), .out_3(WD), .out_4(AL_EN),
    .out_5(AU_EN), .out_6(demultiplexer_5_out_6), .out_7(demultiplexer_5_out_7));
  PullDown #(.Bits(8)) pulldown_1 (.out({INSTRUCTION_q[7:5], INSTRUCTION_q_2, INSTRUCTION_q[1:0]}));
  Multiplexer #(.Bits(16)) multiplexer_8 (
    .sel(FETCH), .in_0({AU_q, AL_q}), .in_1({upper_PC_out, lower_PC_out}), .out(A));
  and and_10 (and_10_out, EXECUTE, EN);
  and and_11 (and_11_out, CLK, EN);
  or or_5 (LPC_EN, DXAPC, demultiplexer_5_out_6);
  or or_6 (UPC_EN, demultiplexer_5_out_7, DXAPC);
  D_FF_AS FIR (.Set(RST), .D(and_10_out), .C(and_11_out), .Clr(1'b0), .Q(FETCH_IR));  // open: nQ
  SSALU8 ssalu8_1 (
    .A(multiplexer_6_out), .X(multiplexer_7_out), .OP(ALUOP[1:0]), .ALT(ALUOP[2]), .CO(ssalu8_1_co),
    .CIN(and_12_out), .Y(ALUOUT), .Z(ssalu8_1_z), .N(ssalu8_1_n));
  or or_7 (or_7_out, FETCH_IR, FETCH_OP);
  or or_8 (RD, and_7_out, or_7_out);
  or or_9 (FETCH, FETCH_IR, FETCH_OP);
  and and_12 (and_12_out, FLG_CARRY, WCARRY);
  or or_10 (PC_INC, FETCH_IR, FETCH_OP);
  D_FF_AS FOP (.Set(1'b0), .D(FETCH_IR), .C(and_11_out), .Clr(RST), .Q(FETCH_OP));  // open: nQ
  and and_13 (and_13_out, WCARRY, ssalu8_1_co);
  PullDown #(.Bits(8)) pulldown_2 (.out(D));
  and and_14 (and_14_out, CLK, ALU_FLG_SET);
  assign D = WD ? demultiplexer_3_out_3 : 8'bz;  // Driver driver_1
  assign driver_2_out = RD ? D : 8'bz;  // Driver driver_2
  PullDown #(.Bits(8)) pulldown_3 (.out(driver_2_out));
  D_FF_AS DEC (.Set(1'b0), .D(FETCH_OP), .C(and_11_out), .Clr(RST), .Q(DECODE));  // open: nQ
  D_FF_AS CARRY (.Set(1'b0), .D(and_13_out), .C(and_14_out), .Clr(RST), .Q(FLG_CARRY));  // open: nQ
  Demultiplexer #(.Bits(8)) demultiplexer_6 (
    .sel(FETCH), .in(driver_2_out), .out_0(demultiplexer_6_out_0), .out_1(demultiplexer_6_out_1));
  D_FF_AS EXE (.Set(1'b0), .D(DECODE), .C(and_11_out), .Clr(RST), .Q(EXECUTE));  // open: nQ
  D_FF_AS ZERO (.Set(1'b0), .D(ssalu8_1_z), .C(and_14_out), .Clr(RST), .Q(FLG_ZERO), .nQ(FLG_NZ));
  D_FF_AS NEGATIVE (.Set(1'b0), .D(ssalu8_1_n), .C(and_14_out), .Clr(RST), .Q(FLG_NEGATIVE));  // open: nQ

  // Other names for the same wires on the sheet: MEM_RD = RD; MEM_WRT = WD; STK_DIR = LD_ST
endmodule
