// Digital circuit RISIKOTB.dig as structural Verilog
module RISIKOTB (
  input  clk
);

  wire and_1_out, button_1_out, button_2_out, demultiplexer_1_out_0, demultiplexer_1_out_1,
       demultiplexer_2_out_0, demultiplexer_2_out_1, dipswitch_1_out, dipswitch_2_out, multiplexer_1_out,
       multiplexer_2_out, OPERATE_EDIT_out, or_1_out, READ_out, risikofl3a2_1_rd, risikofl3a2_1_wd, WRITE_out;
  wire [3:0] _3_out, _7_out, dipswitch_6_out, dipswitch_10_out, dipswitch_14_out, dipswitch_18_out;
  wire [7:0] eeprom_1_d, multiplexer_4_out, ramsingleportsel_1_d, risikofl3a2_1_o, undriven;
  wire [15:0] multiplexer_3_out, risikofl3a2_1_a;

  Button button_1 (.out(button_1_out));
  Button button_2 (.out(button_2_out));
  and and_1 (and_1_out, dipswitch_1_out, clk);
  DipSwitch dipswitch_1 (.out(dipswitch_1_out));
  DipSwitch dipswitch_2 (.out(dipswitch_2_out));
  or or_1 (or_1_out, button_2_out, and_1_out);
  Seven_Seg_Hex seven_seg_hex_1 (.d(_7_out), .dp(1'b0));
  DipSwitch _0 (.out(_3_out[0]));
  DipSwitch _1 (.out(_3_out[1]));
  DipSwitch _2 (.out(_3_out[2]));
  DipSwitch _3 (.out(_3_out[3]));
  DipSwitch _4 (.out(_7_out[0]));
  DipSwitch _5 (.out(_7_out[1]));
  DipSwitch _6 (.out(_7_out[2]));
  DipSwitch _7 (.out(_7_out[3]));
  Seven_Seg_Hex seven_seg_hex_2 (.d(_3_out), .dp(1'b0));
  DipSwitch OPERATE_EDIT (.out(OPERATE_EDIT_out));
  RISIKOFL3A2 risikofl3a2_1 (
    .I({_7_out, _3_out}), .RST(button_1_out), .CLK(or_1_out), .EN(dipswitch_2_out), .D(undriven),
    .O(risikofl3a2_1_o), .RD(risikofl3a2_1_rd), .WD(risikofl3a2_1_wd), .A(risikofl3a2_1_a));
  DipSwitch READ (.out(READ_out));
  DipSwitch WRITE (.out(WRITE_out));
  Seven_Seg_Hex seven_seg_hex_3 (.d(risikofl3a2_1_o[7:4]), .dp(1'b0));
  Multiplexer multiplexer_1 (.sel(OPERATE_EDIT_out), .in_0(risikofl3a2_1_rd), .in_1(READ_out), .out(multiplexer_1_out));
  Multiplexer multiplexer_2 (
    .sel(OPERATE_EDIT_out), .in_0(risikofl3a2_1_wd), .in_1(WRITE_out), .out(multiplexer_2_out));
  Seven_Seg_Hex seven_seg_hex_4 (.d(risikofl3a2_1_o[3:0]), .dp(1'b0));
  Multiplexer #(.Bits(16)) multiplexer_3 (
    .sel(OPERATE_EDIT_out), .in_0(risikofl3a2_1_a),
    .in_1({dipswitch_10_out, dipswitch_6_out, dipswitch_18_out, dipswitch_14_out}), .out(multiplexer_3_out));
  Multiplexer #(.Bits(8)) multiplexer_4 (
    .sel(OPERATE_EDIT_out), .in_0(undriven), .in_1({_7_out, _3_out}), .out(multiplexer_4_out));
  Demultiplexer demultiplexer_1 (
    .sel(multiplexer_3_out[15]), .in(multiplexer_1_out), .out_0(demultiplexer_1_out_0),
    .out_1(demultiplexer_1_out_1));
  Demultiplexer demultiplexer_2 (
    .sel(multiplexer_3_out[15]), .in(multiplexer_2_out), .out_0(demultiplexer_2_out_0),
    .out_1(demultiplexer_2_out_1));
  RAMSinglePortSel #(.AddrBits(15), .Bits(8)) ramsingleportsel_1 (
    .A(multiplexer_3_out[14:0]), .CS(multiplexer_3_out[15]), .WE(demultiplexer_2_out_1),
    .OE(demultiplexer_1_out_1), .D(ramsingleportsel_1_d));
  EEPROM #(.AddrBits(15), .Bits(8)) eeprom_1 (
    .A(multiplexer_3_out[14:0]), .CS(~multiplexer_3_out[15]), .WE(demultiplexer_2_out_0),
    .OE(demultiplexer_1_out_0), .D(eeprom_1_d));
  PullDown #(.Bits(8)) pulldown_1 (.out(ramsingleportsel_1_d));
  PullDown #(.Bits(8)) pulldown_2 (.out(eeprom_1_d));
  assign ramsingleportsel_1_d = demultiplexer_2_out_1 ? multiplexer_4_out : 8'bz;  // Driver driver_1
  assign multiplexer_4_out = demultiplexer_1_out_1 ? ramsingleportsel_1_d : 8'bz;  // Driver driver_2
  assign eeprom_1_d = demultiplexer_2_out_0 ? multiplexer_4_out : 8'bz;  // Driver driver_3
  assign multiplexer_4_out = demultiplexer_1_out_0 ? eeprom_1_d : 8'bz;  // Driver driver_4
  Seven_Seg_Hex seven_seg_hex_5 (.d(dipswitch_10_out), .dp(1'b0));
  DipSwitch dipswitch_3 (.out(dipswitch_6_out[0]));
  DipSwitch dipswitch_4 (.out(dipswitch_6_out[1]));
  DipSwitch dipswitch_5 (.out(dipswitch_6_out[2]));
  DipSwitch dipswitch_6 (.out(dipswitch_6_out[3]));
  DipSwitch dipswitch_7 (.out(dipswitch_10_out[0]));
  DipSwitch dipswitch_8 (.out(dipswitch_10_out[1]));
  DipSwitch dipswitch_9 (.out(dipswitch_10_out[2]));
  DipSwitch dipswitch_10 (.out(dipswitch_10_out[3]));
  PullDown #(.Bits(8)) pulldown_3 (.out(multiplexer_4_out));
  Seven_Seg_Hex seven_seg_hex_6 (.d(dipswitch_6_out), .dp(1'b0));
  Seven_Seg_Hex seven_seg_hex_7 (.d(dipswitch_18_out), .dp(1'b0));
  DipSwitch dipswitch_11 (.out(dipswitch_14_out[0]));
  DipSwitch dipswitch_12 (.out(dipswitch_14_out[1]));
  DipSwitch dipswitch_13 (.out(dipswitch_14_out[2]));
  DipSwitch dipswitch_14 (.out(dipswitch_14_out[3]));
  DipSwitch dipswitch_15 (.out(dipswitch_18_out[0]));
  DipSwitch dipswitch_16 (.out(dipswitch_18_out[1]));
  DipSwitch dipswitch_17 (.out(dipswitch_18_out[2]));
  DipSwitch dipswitch_18 (.out(dipswitch_18_out[3]));
  Seven_Seg_Hex seven_seg_hex_8 (.d(dipswitch_14_out), .dp(1'b0));

  // Notes on the sheet:
  //   clk: Hz: 100
  //   contents of eeprom_1 (hex, n*v repeats v):
  //   88,10,88,8,11,0,5,0,37,0,5,0,23,0,1,0,e,0,88,80,88,0,15,0,11,0
  //   ,88,de,d
endmodule
