// Digital circuit SEQGEN_FDE.dig as structural Verilog
module SEQGEN_FDE (
  input  R,
  input  C,
  output F,
  output D,
  output E
);

  D_FF_AS d_ff_as_1 (.Set(R), .D(E), .C(C), .Clr(1'b0), .Q(F));  // open: nQ
  D_FF_AS d_ff_as_2 (.Set(1'b0), .D(F), .C(C), .Clr(R), .Q(D));  // open: nQ
  D_FF_AS d_ff_as_3 (.Set(1'b0), .D(D), .C(C), .Clr(R), .Q(E));  // open: nQ
endmodule
