// Digital circuit SSALU8B.dig as structural Verilog
module SSALU8B (
  input  [7:0] A,
  input  [7:0] X,
  input  CIN,
  input  ALT,
  input  OP0,
  input  OP1,
  output CO,
  output [7:0] Y,
  output Z
);

  wire and_2_out, and_3_out, and_4_out, and_5_out, and_6_out, and_7_out, and_8_out, and_9_out, and_10_out,
       and_11_out, and_12_out, and_13_out, and_14_out, and_15_out, and_16_out, and_17_out, and_18_out,
       and_19_out, or_2_out, or_3_out, or_4_out, or_5_out, or_6_out, or_7_out, or_8_out, or_9_out, or_10_out,
       xor_1_out, xor_2_out, xor_3_out, xor_4_out, xor_5_out, xor_6_out, xor_7_out, xor_8_out, xor_10_out,
       xor_11_out, xor_12_out, xor_13_out, xor_14_out, xor_15_out, xor_16_out, xor_17_out;
  wire [7:0] and_1_out, barrelshifter_1_out, barrelshifter_2_out, multiplexer_1_out, multiplexer_2_out,
       multiplexer_3_out, not_1_out, or_1_out, xor_9_out, xor_18_out;

  xor xor_1 (xor_1_out, ALT, X[0]);
  xor xor_2 (xor_2_out, ALT, X[1]);
  xor xor_3 (xor_3_out, ALT, X[2]);
  xor xor_4 (xor_4_out, ALT, X[3]);
  xor xor_5 (xor_5_out, ALT, X[4]);
  xor xor_6 (xor_6_out, ALT, X[5]);
  xor xor_7 (xor_7_out, ALT, X[6]);
  xor xor_8 (xor_8_out, ALT, X[7]);
  assign and_1_out = A & X;  // And and_1, 8 bits wide
  assign or_1_out = A | X;  // Or or_1, 8 bits wide
  assign xor_9_out = A ^ X;  // XOr xor_9, 8 bits wide
  assign not_1_out = ~A;  // Not not_1, 8 bits wide
  or or_2 (or_2_out, CIN, ALT);
  xor xor_10 (xor_10_out, A[0], xor_1_out);
  and and_2 (and_2_out, xor_1_out, A[0]);
  xor xor_11 (xor_11_out, A[1], xor_2_out);
  and and_3 (and_3_out, xor_2_out, A[1]);
  xor xor_12 (xor_12_out, A[2], xor_3_out);
  and and_4 (and_4_out, xor_3_out, A[2]);
  xor xor_13 (xor_13_out, A[3], xor_4_out);
  and and_5 (and_5_out, xor_4_out, A[3]);
  xor xor_14 (xor_14_out, A[4], xor_5_out);
  and and_6 (and_6_out, xor_5_out, A[4]);
  xor xor_15 (xor_15_out, A[5], xor_6_out);
  and and_7 (and_7_out, xor_6_out, A[5]);
  xor xor_16 (xor_16_out, A[6], xor_7_out);
  and and_8 (and_8_out, xor_7_out, A[6]);
  xor xor_17 (xor_17_out, A[7], xor_8_out);
  and and_9 (and_9_out, xor_8_out, A[7]);
  Multiplexer #(.Bits(8)) multiplexer_1 (.sel(ALT), .in_0(and_1_out), .in_1(or_1_out), .out(multiplexer_1_out));
  Multiplexer #(.Bits(8)) multiplexer_2 (.sel(ALT), .in_0(xor_9_out), .in_1(not_1_out), .out(multiplexer_2_out));
  or or_3 (or_3_out, and_10_out, and_2_out);
  or or_4 (or_4_out, and_11_out, and_3_out);
  or or_5 (or_5_out, and_12_out, and_4_out);
  or or_6 (or_6_out, and_13_out, and_5_out);
  or or_7 (or_7_out, and_14_out, and_6_out);
  or or_8 (or_8_out, and_15_out, and_7_out);
  or or_9 (or_9_out, and_16_out, and_8_out);
  or or_10 (or_10_out, and_17_out, and_9_out);
  BarrelShifter #(.Bits(8)) barrelshifter_1 (.in(A), .shift(4'b0001), .out(barrelshifter_1_out));
  BarrelShifter #(.Bits(8), .direction("right")) barrelshifter_2 (.in(A), .shift(4'b0001), .out(barrelshifter_2_out));
  and and_10 (and_10_out, xor_10_out, or_2_out);
  and and_11 (and_11_out, xor_11_out, or_3_out);
  and and_12 (and_12_out, xor_12_out, or_4_out);
  and and_13 (and_13_out, xor_13_out, or_5_out);
  and and_14 (and_14_out, xor_14_out, or_6_out);
  and and_15 (and_15_out, xor_15_out, or_7_out);
  and and_16 (and_16_out, xor_16_out, or_8_out);
  and and_17 (and_17_out, xor_17_out, or_9_out);
  xor xor_18 (xor_18_out[0], or_2_out, xor_10_out);
  xor xor_19 (xor_18_out[1], or_3_out, xor_11_out);
  xor xor_20 (xor_18_out[2], or_4_out, xor_12_out);
  xor xor_21 (xor_18_out[3], or_5_out, xor_13_out);
  xor xor_22 (xor_18_out[4], or_6_out, xor_14_out);
  xor xor_23 (xor_18_out[5], or_7_out, xor_15_out);
  xor xor_24 (xor_18_out[6], or_8_out, xor_16_out);
  xor xor_25 (xor_18_out[7], or_9_out, xor_17_out);
  Multiplexer #(.Bits(8)) multiplexer_3 (
    .sel(ALT), .in_0(barrelshifter_1_out), .in_1(barrelshifter_2_out), .out(multiplexer_3_out));
  Multiplexer #(.Selector_Bits(2), .Bits(8)) multiplexer_4 (
    .sel({OP1, OP0}), .in_0(xor_18_out), .in_1(multiplexer_3_out), .in_2(multiplexer_1_out),
    .in_3(multiplexer_2_out), .out(Y));
  and and_18 (and_18_out, ~Y[0], ~Y[1], ~Y[2]);  // And
  and and_19 (and_19_out, ~Y[3], ~Y[4], ~Y[5]);  // And
  assign CO = ~OP1 ? or_10_out : 1'bz;  // DriverInvSel driverinvsel_1
  PullDown pulldown_1 (.out(CO));
  and and_20 (Z, and_18_out, and_19_out, ~Y[6], ~Y[7]);  // And

  // Notes on the sheet:
  //   ALT: ADD=SUB
  //   INC=DEC
  //   AND=OR
  //   XOR=NOT
  //   Y: 8 bit output of result from ALU operation
endmodule
