// Digital circuit SSALU8B2.dig as structural Verilog
module SSALU8B2 (
  input  [7:0] A,
  input  [7:0] X,
  input  CIN,
  input  [1:0] OP,
  input  ALT,
  output CO,
  output [7:0] Y,
  output Z,
  output N
);

  wire and_2_out, and_3_out, and_4_out, and_5_out, and_6_out, and_7_out, and_8_out, and_9_out, and_10_out,
       and_11_out, and_12_out, and_13_out, and_14_out, and_15_out, and_16_out, and_17_out, and_18_out,
       and_19_out, and_20_out, and_21_out, and_22_out, and_23_out, and_24_out, and_25_out, and_26_out,
       and_27_out, and_28_out, and_29_out, and_30_out, and_31_out, and_32_out, and_33_out, and_34_out,
       and_35_out, and_36_out, and_37_out, multiplexer_4_out, or_2_out, or_3_out, or_4_out, or_5_out,
       or_6_out, or_7_out, or_8_out, or_9_out, or_10_out, or_11_out, or_12_out, or_13_out, or_14_out,
       or_15_out, or_16_out, or_17_out, or_18_out, xor_1_out, xor_2_out, xor_3_out, xor_4_out, xor_5_out,
       xor_6_out, xor_7_out, xor_8_out, xor_9_out, xor_10_out, xor_11_out, xor_12_out, xor_13_out,
       xor_14_out, xor_15_out, xor_16_out, xor_18_out, xor_19_out, xor_20_out, xor_21_out, xor_22_out,
       xor_23_out, xor_24_out, xor_25_out, xor_26_out, xor_27_out, xor_28_out, xor_29_out, xor_30_out,
       xor_31_out, xor_32_out, xor_33_out;
  wire [7:0] and_1_out, multiplexer_1_out, multiplexer_2_out, not_1_out, or_1_out, xor_17_out, xor_34_out,
       xor_42_out;

  xor xor_1 (xor_1_out, ALT, X[0]);
  xor xor_2 (xor_2_out, ALT, X[1]);
  xor xor_3 (xor_3_out, ALT, X[2]);
  xor xor_4 (xor_4_out, ALT, X[3]);
  xor xor_5 (xor_5_out, ALT, X[4]);
  xor xor_6 (xor_6_out, ALT, X[5]);
  xor xor_7 (xor_7_out, ALT, X[6]);
  xor xor_8 (xor_8_out, ALT, X[7]);
  xor xor_9 (xor_9_out, ALT, 1'b1);
  xor xor_10 (xor_10_out, ALT, 1'b0);
  xor xor_11 (xor_11_out, ALT, 1'b0);
  xor xor_12 (xor_12_out, ALT, 1'b0);
  xor xor_13 (xor_13_out, ALT, 1'b0);
  xor xor_14 (xor_14_out, ALT, 1'b0);
  xor xor_15 (xor_15_out, ALT, 1'b0);
  xor xor_16 (xor_16_out, ALT, 1'b0);
  assign and_1_out = A & X;  // And and_1, 8 bits wide
  assign or_1_out = A | X;  // Or or_1, 8 bits wide
  assign xor_17_out = A ^ X;  // XOr xor_17, 8 bits wide
  assign not_1_out = ~A;  // Not not_1, 8 bits wide
  or or_2 (or_2_out, CIN, ALT);
  xor xor_18 (xor_18_out, A[0], xor_1_out);
  and and_2 (and_2_out, xor_1_out, A[0]);
  xor xor_19 (xor_19_out, A[1], xor_2_out);
  and and_3 (and_3_out, xor_2_out, A[1]);
  xor xor_20 (xor_20_out, A[2], xor_3_out);
  and and_4 (and_4_out, xor_3_out, A[2]);
  xor xor_21 (xor_21_out, A[3], xor_4_out);
  and and_5 (and_5_out, xor_4_out, A[3]);
  xor xor_22 (xor_22_out, A[4], xor_5_out);
  and and_6 (and_6_out, xor_5_out, A[4]);
  xor xor_23 (xor_23_out, A[5], xor_6_out);
  and and_7 (and_7_out, xor_6_out, A[5]);
  xor xor_24 (xor_24_out, A[6], xor_7_out);
  and and_8 (and_8_out, xor_7_out, A[6]);
  xor xor_25 (xor_25_out, A[7], xor_8_out);
  and and_9 (and_9_out, xor_8_out, A[7]);
  xor xor_26 (xor_26_out, A[0], xor_9_out);
  and and_10 (and_10_out, xor_9_out, A[0]);
  xor xor_27 (xor_27_out, A[1], xor_10_out);
  and and_11 (and_11_out, xor_10_out, A[1]);
  xor xor_28 (xor_28_out, A[2], xor_11_out);
  and and_12 (and_12_out, xor_11_out, A[2]);
  xor xor_29 (xor_29_out, A[3], xor_12_out);
  and and_13 (and_13_out, xor_12_out, A[3]);
  xor xor_30 (xor_30_out, A[4], xor_13_out);
  and and_14 (and_14_out, xor_13_out, A[4]);
  xor xor_31 (xor_31_out, A[5], xor_14_out);
  and and_15 (and_15_out, xor_14_out, A[5]);
  xor xor_32 (xor_32_out, A[6], xor_15_out);
  and and_16 (and_16_out, xor_15_out, A[6]);
  xor xor_33 (xor_33_out, A[7], xor_16_out);
  and and_17 (and_17_out, xor_16_out, A[7]);
  Multiplexer #(.Bits(8)) multiplexer_1 (.sel(ALT), .in_0(and_1_out), .in_1(or_1_out), .out(multiplexer_1_out));
  Multiplexer #(.Bits(8)) multiplexer_2 (.sel(ALT), .in_0(xor_17_out), .in_1(not_1_out), .out(multiplexer_2_out));
  or or_3 (or_3_out, and_18_out, and_2_out);
  or or_4 (or_4_out, and_19_out, and_3_out);
  or or_5 (or_5_out, and_20_out, and_4_out);
  or or_6 (or_6_out, and_21_out, and_5_out);
  or or_7 (or_7_out, and_22_out, and_6_out);
  or or_8 (or_8_out, and_23_out, and_7_out);
  or or_9 (or_9_out, and_24_out, and_8_out);
  or or_10 (or_10_out, and_25_out, and_9_out);
  or or_11 (or_11_out, and_26_out, and_10_out);
  or or_12 (or_12_out, and_27_out, and_11_out);
  or or_13 (or_13_out, and_28_out, and_12_out);
  or or_14 (or_14_out, and_29_out, and_13_out);
  or or_15 (or_15_out, and_30_out, and_14_out);
  or or_16 (or_16_out, and_31_out, and_15_out);
  or or_17 (or_17_out, and_32_out, and_16_out);
  or or_18 (or_18_out, and_33_out, and_17_out);
  and and_18 (and_18_out, xor_18_out, or_2_out);
  and and_19 (and_19_out, xor_19_out, or_3_out);
  and and_20 (and_20_out, xor_20_out, or_4_out);
  and and_21 (and_21_out, xor_21_out, or_5_out);
  and and_22 (and_22_out, xor_22_out, or_6_out);
  and and_23 (and_23_out, xor_23_out, or_7_out);
  and and_24 (and_24_out, xor_24_out, or_8_out);
  and and_25 (and_25_out, xor_25_out, or_9_out);
  and and_26 (and_26_out, xor_26_out, or_2_out);
  and and_27 (and_27_out, xor_27_out, or_11_out);
  and and_28 (and_28_out, xor_28_out, or_12_out);
  and and_29 (and_29_out, xor_29_out, or_13_out);
  and and_30 (and_30_out, xor_30_out, or_14_out);
  and and_31 (and_31_out, xor_31_out, or_15_out);
  and and_32 (and_32_out, xor_32_out, or_16_out);
  and and_33 (and_33_out, xor_33_out, or_17_out);
  xor xor_34 (xor_34_out[0], or_2_out, xor_18_out);
  xor xor_35 (xor_34_out[1], or_3_out, xor_19_out);
  xor xor_36 (xor_34_out[2], or_4_out, xor_20_out);
  xor xor_37 (xor_34_out[3], or_5_out, xor_21_out);
  xor xor_38 (xor_34_out[4], or_6_out, xor_22_out);
  xor xor_39 (xor_34_out[5], or_7_out, xor_23_out);
  xor xor_40 (xor_34_out[6], or_8_out, xor_24_out);
  xor xor_41 (xor_34_out[7], or_9_out, xor_25_out);
  xor xor_42 (xor_42_out[0], or_2_out, xor_26_out);
  xor xor_43 (xor_42_out[1], or_11_out, xor_27_out);
  xor xor_44 (xor_42_out[2], or_12_out, xor_28_out);
  xor xor_45 (xor_42_out[3], or_13_out, xor_29_out);
  xor xor_46 (xor_42_out[4], or_14_out, xor_30_out);
  xor xor_47 (xor_42_out[5], or_15_out, xor_31_out);
  xor xor_48 (xor_42_out[6], or_16_out, xor_32_out);
  xor xor_49 (xor_42_out[7], or_17_out, xor_33_out);
  and and_34 (and_34_out, ~ALT, or_10_out);  // And
  and and_35 (and_35_out, ~ALT, or_18_out);  // And
  Multiplexer #(.Selector_Bits(2), .Bits(8)) multiplexer_3 (
    .sel(OP), .in_0(xor_34_out), .in_1(xor_42_out), .in_2(multiplexer_1_out), .in_3(multiplexer_2_out),
    .out({N, Y[6:0]}));
  and and_36 (and_36_out, ~Y[0], ~Y[1], ~Y[2]);  // And
  and and_37 (and_37_out, ~Y[3], ~Y[4], ~Y[5]);  // And
  Multiplexer multiplexer_4 (.sel(OP[0]), .in_0(and_34_out), .in_1(and_35_out), .out(multiplexer_4_out));
  assign CO = ~OP[1] ? multiplexer_4_out : 1'bz;  // DriverInvSel driverinvsel_1
  PullDown pulldown_1 (.out(CO));
  and and_38 (Z, and_36_out, and_37_out, ~Y[6], ~N);  // And

  assign Y[7] = N;

  // Notes on the sheet:
  //   OP: 00 ADD/SUB 
  //   01 INC/DEC 
  //   10 AND/OR 
  //   11 XOR/NOT
  //   ALT: ADD=SUB
  //   INC=DEC
  //   AND=OR
  //   XOR=NOT
  //   Y: 8 bit output of result from ALU operation
endmodule
