// Digital circuit STACKERCL.dig as structural Verilog
module STACKERCL (
  input  [7:0] IN,
  input  ZERO,
  output BUSIN,
  output BUSOUT,
  output MEM_RD,
  output MEM_WRT,
  output BUS_ALU,
  output STK_DIR,
  output STK_EN,
  output MXOP,
  output XEN,
  output RS_0,
  output RS_1,
  output RS_2,
  output OP_0,
  output OP_1,
  output ALT
);

  wire and_1_out, and_2_out, and_3_out, and_4_out, and_5_out, and_6_out, decoder_1_out_0, decoder_1_out_1,
       decoder_2_out_0, decoder_2_out_1, demultiplexer_3_out_0, multiplexer_1_out, not_1_out, or_1_out,
       or_2_out;
  wire [2:0] demultiplexer_2_out_0, driver_2_out_2;
  wire [2:2] driver_2_out;
  wire [4:1] driver_1_out;
  wire [6:0] demultiplexer_1_out_0, demultiplexer_1_out_1;

  Demultiplexer #(.Bits(7)) demultiplexer_1 (
    .sel(IN[0]), .in(IN[7:1]), .out_0(demultiplexer_1_out_0), .out_1(demultiplexer_1_out_1));
  and and_1 (and_1_out, ~IN[7], ~IN[6], ~IN[5], ~IN[4]);  // And
  and and_2 (and_2_out, ~IN[3], ~IN[2], ~IN[1], ~IN[0]);  // And
  and and_3 (and_3_out, and_1_out, and_2_out);
  and and_4 (and_4_out, demultiplexer_1_out_1[6], ZERO);
  assign {driver_1_out, MXOP} = or_1_out ? {demultiplexer_1_out_0[5:3], demultiplexer_1_out_0[1:0]} : 5'bz;  // Driver driver_1
  or or_1 (or_1_out, ~demultiplexer_1_out_0[6], multiplexer_1_out);  // Or
  assign {driver_2_out_2, driver_2_out[2], BUS_ALU, STK_DIR} = or_2_out ? demultiplexer_1_out_1[5:0] : 6'bz;  // Driver driver_2
  or or_2 (or_2_out, ~demultiplexer_1_out_1[6], and_4_out);  // Or
  Multiplexer multiplexer_1 (.sel(demultiplexer_1_out_0[2]), .in_0(not_1_out), .in_1(ZERO), .out(multiplexer_1_out));
  not not_1 (not_1_out, ZERO);
  and and_5 (and_5_out, ~IN[0], ~and_3_out, or_1_out);  // And
  and and_6 (and_6_out, IN[0], or_2_out);
  Decoder decoder_1 (.sel(driver_1_out[1]), .out_0(decoder_1_out_0), .out_1(decoder_1_out_1));
  Demultiplexer #(.Bits(3)) demultiplexer_2 (
    .sel(BUS_ALU), .in(driver_2_out_2), .out_0(demultiplexer_2_out_0), .out_1({ALT, OP_1, OP_0}));
  assign MEM_RD = and_5_out ? decoder_1_out_0 : 1'bz;  // Driver driver_3
  assign MEM_WRT = and_5_out ? decoder_1_out_1 : 1'bz;  // Driver driver_4
  Demultiplexer demultiplexer_3 (.sel(BUS_ALU), .in(driver_2_out[2]), .out_0(demultiplexer_3_out_0), .out_1(XEN));
  PullDown pulldown_1 (.out(MEM_RD));
  PullDown pulldown_2 (.out(MEM_WRT));
  Decoder decoder_2 (.sel(demultiplexer_3_out_0), .out_0(decoder_2_out_0), .out_1(decoder_2_out_1));
  assign BUSIN = and_6_out ? decoder_2_out_0 : 1'bz;  // Driver driver_5
  assign BUSOUT = and_6_out ? decoder_2_out_1 : 1'bz;  // Driver driver_6
  PullDown pulldown_3 (.out(BUSIN));
  PullDown pulldown_4 (.out(BUSOUT));
  or or_3 (RS_0, demultiplexer_2_out_0[0], driver_1_out[2]);
  or or_4 (RS_1, demultiplexer_2_out_0[1], driver_1_out[3]);
  or or_5 (RS_2, demultiplexer_2_out_0[2], driver_1_out[4]);

  assign STK_EN = IN[0];
endmodule
