// Digital circuit STJR3P2B.dig as structural Verilog
module STJR3P2B (
  input  [7:0] IN,
  input  [7:0] DMA_DATA,
  input  [7:0] DMA_ADDR,
  input  DMA_STR,
  input  SIG_DMA,
  input  CLK,
  input  RST,
  input  EN,
  input  [7:0] RSI,
  output [7:0] OUT,
  output IN_RD,
  output OUT_WRT,
  output [7:0] SRO,
  output [7:0] CPT,
  output [7:0] DPT
);

  wire and_1_out, and_2_out, chkz_1_z, d_ff_as_1_q, d_ff_as_2_q, d_ff_as_3_q, multiplexer_1_out,
       multiplexer_12_out, not_1_out, not_2_out, or_1_out, or_2_out, or_3_out;
  wire [1:0] demultiplexer_1_out_3;
  wire [2:0] demultiplexer_1_out_0, demultiplexer_1_out_1, demultiplexer_1_out_2;
  wire [5:0] driver_1_out, driver_2_out;
  wire [7:0] blockramdualport_1_d, d_ff_as_4_q, d_ff_as_5_q, d_ff_as_6_q, d_ff_as_7_q, d_ff_as_8_q,
       d_ff_as_9_q, d_ff_as_10_q, d_ff_as_11_q, demultiplexer_2_out_0, demultiplexer_2_out_1,
       demultiplexer_3_out_0, demultiplexer_3_out_1, demultiplexer_3_out_2, demultiplexer_3_out_3, IR_q,
       MAC_out, multiplexer_2_out, multiplexer_3_out, multiplexer_4_out, multiplexer_6_out,
       multiplexer_7_out, multiplexer_8_out, multiplexer_9_out, multiplexer_10_out, multiplexer_11_out,
       multiplexer_13_out, multiplexer_14_out, multiplexer_15_out, multiplexer_16_out, od8x8bsrfv2_1_top,
       PC_out, pulldown_3_out, ssalu8b_1_y;
  wire [7:6] driver_2_out_2;

  D_FF_AS d_ff_as_1 (.Set(RST), .D(d_ff_as_3_q), .C(and_1_out), .Clr(1'b0), .Q(d_ff_as_1_q));  // open: nQ
  D_FF_AS d_ff_as_2 (.Set(1'b0), .D(d_ff_as_1_q), .C(and_1_out), .Clr(RST), .Q(d_ff_as_2_q));  // open: nQ
  D_FF_AS d_ff_as_3 (.Set(1'b0), .D(d_ff_as_2_q), .C(and_1_out), .Clr(RST), .Q(d_ff_as_3_q));  // open: nQ
  or or_1 (or_1_out, ~EN, SIG_DMA);  // Or
  and and_1 (and_1_out, ~or_1_out, CLK);  // And
  not not_1 (not_1_out, chkz_1_z);
  Multiplexer multiplexer_1 (.sel(driver_2_out_2[6]), .in_0(chkz_1_z), .in_1(not_1_out), .out(multiplexer_1_out));
  assign driver_1_out = or_2_out ? driver_2_out : 6'bz;  // Driver driver_1
  PullDown #(.Bits(6)) pulldown_1 (.out(driver_1_out));
  or or_2 (or_2_out, multiplexer_1_out, ~driver_2_out_2[7]);  // Or
  assign {driver_2_out_2, driver_2_out} = d_ff_as_3_q ? IR_q : 8'bz;  // Driver driver_2
  PullDown #(.Bits(8)) pulldown_2 (.out({driver_2_out_2, driver_2_out}));
  Demultiplexer #(.Selector_Bits(2), .Bits(3)) demultiplexer_1 (
    .sel(driver_1_out[4:3]), .in(driver_1_out[2:0]), .out_0(demultiplexer_1_out_0),
    .out_1(demultiplexer_1_out_1), .out_2(demultiplexer_1_out_2), .out_3({IN_RD, demultiplexer_1_out_3}));
  Multiplexer #(.Bits(8)) multiplexer_2 (.sel(IN_RD), .in_0(demultiplexer_3_out_3), .in_1(IN), .out(multiplexer_2_out));
  and and_2 (and_2_out, demultiplexer_1_out_3[0], ~CLK);  // And
  Multiplexer #(.Bits(8)) multiplexer_3 (
    .sel(demultiplexer_1_out_3[1]), .in_0(multiplexer_2_out), .in_1(d_ff_as_5_q), .out(multiplexer_3_out));
  or or_3 (or_3_out, d_ff_as_2_q, demultiplexer_1_out_2[0]);
  D_FF_AS #(.Bits(8)) d_ff_as_4 (
    .Set(1'b0), .D(multiplexer_3_out), .C(and_2_out), .Clr(RST), .Q(d_ff_as_4_q));  // open: nQ
  CounterPreset #(.Bits(8)) PC (
    .en(or_3_out), .C(CLK), .dir(demultiplexer_1_out_2[1]), .in(demultiplexer_3_out_2),
    .ld(demultiplexer_1_out_2[2]), .clr(RST), .out(PC_out));  // open: ovf
  CounterPreset #(.Bits(8)) MAC (
    .en(demultiplexer_1_out_1[0]), .C(CLK), .dir(demultiplexer_1_out_1[1]), .in(demultiplexer_3_out_1),
    .ld(demultiplexer_1_out_1[2]), .clr(RST), .out(MAC_out));  // open: ovf
  Multiplexer #(.Bits(8)) multiplexer_4 (
    .sel(demultiplexer_1_out_3[1]), .in_0(d_ff_as_4_q), .in_1(d_ff_as_6_q), .out(multiplexer_4_out));
  SSALU8B ssalu8b_1 (
    .A(d_ff_as_4_q), .X(demultiplexer_3_out_0), .OP0(demultiplexer_1_out_0[0]),
    .OP1(demultiplexer_1_out_0[1]), .ALT(demultiplexer_1_out_0[2]), .CIN(1'b0), .Y(ssalu8b_1_y));  // open: CO, Z
  PullDown #(.Bits(8)) pulldown_3 (.out(pulldown_3_out));
  assign pulldown_3_out = IN_RD ? d_ff_as_4_q : 8'bz;  // Driver driver_3
  Multiplexer #(.Bits(8)) multiplexer_5 (.sel(SIG_DMA), .in_0(pulldown_3_out), .in_1(blockramdualport_1_d), .out(OUT));
  D_FF_AS #(.Bits(8)) d_ff_as_5 (
    .Set(1'b0), .D(multiplexer_4_out), .C(and_2_out), .Clr(RST), .Q(d_ff_as_5_q));  // open: nQ
  and and_3 (OUT_WRT, SIG_DMA, demultiplexer_1_out_3[1]);
  Multiplexer #(.Bits(8)) multiplexer_6 (
    .sel(demultiplexer_1_out_3[1]), .in_0(d_ff_as_5_q), .in_1(d_ff_as_7_q), .out(multiplexer_6_out));
  Multiplexer #(.Bits(8)) multiplexer_7 (.sel(d_ff_as_1_q), .in_0(MAC_out), .in_1(PC_out), .out(multiplexer_7_out));
  Multiplexer #(.Selector_Bits(2), .Bits(8)) multiplexer_8 (
    .sel(driver_1_out[4:3]), .in_0(ssalu8b_1_y), .in_1(MAC_out), .in_2(PC_out), .in_3(d_ff_as_4_q),
    .out(multiplexer_8_out));
  D_FF_AS #(.Bits(8)) d_ff_as_6 (
    .Set(1'b0), .D(multiplexer_6_out), .C(and_2_out), .Clr(RST), .Q(d_ff_as_6_q));  // open: nQ
  Multiplexer #(.Bits(8)) multiplexer_9 (
    .sel(demultiplexer_1_out_3[1]), .in_0(d_ff_as_6_q), .in_1(d_ff_as_8_q), .out(multiplexer_9_out));
  Multiplexer #(.Bits(8)) multiplexer_10 (
    .sel(SIG_DMA), .in_0(multiplexer_7_out), .in_1(DMA_ADDR), .out(multiplexer_10_out));
  Multiplexer #(.Bits(8)) multiplexer_11 (
    .sel(SIG_DMA), .in_0(multiplexer_8_out), .in_1(DMA_DATA), .out(multiplexer_11_out));
  not not_2 (not_2_out, CLK);
  D_FF_AS #(.Bits(8)) d_ff_as_7 (
    .Set(1'b0), .D(multiplexer_9_out), .C(and_2_out), .Clr(RST), .Q(d_ff_as_7_q));  // open: nQ
  Multiplexer multiplexer_12 (.sel(SIG_DMA), .in_0(driver_1_out[5]), .in_1(DMA_STR), .out(multiplexer_12_out));
  BlockRAMDualPort #(.AddrBits(8), .Bits(8)) blockramdualport_1 (
    .A(multiplexer_10_out), .Din(multiplexer_11_out), .str(multiplexer_12_out), .C(not_2_out),
    .D(blockramdualport_1_d));
  Multiplexer #(.Bits(8)) multiplexer_13 (
    .sel(demultiplexer_1_out_3[1]), .in_0(d_ff_as_7_q), .in_1(d_ff_as_9_q), .out(multiplexer_13_out));
  Demultiplexer #(.Bits(8)) demultiplexer_2 (
    .sel(d_ff_as_1_q), .in(blockramdualport_1_d), .out_0(demultiplexer_2_out_0), .out_1(demultiplexer_2_out_1));
  CHKZ chkz_1 (.I(blockramdualport_1_d), .Z(chkz_1_z));
  D_FF_AS #(.Bits(8)) d_ff_as_8 (
    .Set(1'b0), .D(multiplexer_13_out), .C(and_2_out), .Clr(RST), .Q(d_ff_as_8_q));  // open: nQ
  Register #(.Bits(8)) IR (.D(demultiplexer_2_out_1), .C(CLK), .en(d_ff_as_1_q), .Q(IR_q));
  Multiplexer #(.Bits(8)) multiplexer_14 (
    .sel(demultiplexer_1_out_3[1]), .in_0(d_ff_as_8_q), .in_1(d_ff_as_10_q), .out(multiplexer_14_out));
  Demultiplexer #(.Selector_Bits(2), .Bits(8)) demultiplexer_3 (
    .sel(driver_1_out[4:3]), .in(demultiplexer_2_out_0), .out_0(demultiplexer_3_out_0),
    .out_1(demultiplexer_3_out_1), .out_2(demultiplexer_3_out_2), .out_3(demultiplexer_3_out_3));
  D_FF_AS #(.Bits(8)) d_ff_as_9 (
    .Set(1'b0), .D(multiplexer_14_out), .C(and_2_out), .Clr(RST), .Q(d_ff_as_9_q));  // open: nQ
  Multiplexer #(.Bits(8)) multiplexer_15 (
    .sel(demultiplexer_1_out_3[1]), .in_0(d_ff_as_9_q), .in_1(d_ff_as_11_q), .out(multiplexer_15_out));
  D_FF_AS #(.Bits(8)) d_ff_as_10 (
    .Set(1'b0), .D(multiplexer_15_out), .C(and_2_out), .Clr(RST), .Q(d_ff_as_10_q));  // open: nQ
  Multiplexer #(.Bits(8)) multiplexer_16 (
    .sel(demultiplexer_1_out_3[1]), .in_0(d_ff_as_10_q), .in_1(od8x8bsrfv2_1_top), .out(multiplexer_16_out));
  D_FF_AS #(.Bits(8)) d_ff_as_11 (
    .Set(1'b0), .D(multiplexer_16_out), .C(and_2_out), .Clr(RST), .Q(d_ff_as_11_q));  // open: nQ
  od8x8bsrfV2 od8x8bsrfv2_1 (
    .SRI(d_ff_as_11_q), .DIR(demultiplexer_1_out_3[1]), .EN(demultiplexer_1_out_3[0]), .CLK(and_2_out),
    .RST(RST), .RSI(RSI), .SRO(SRO), .CPT(CPT), .DPT(DPT), .TOP(od8x8bsrfv2_1_top));
  // Pins of 1 and 8 bits meet at CPT
  // Pins of 1 and 8 bits meet at DPT
  // also tied to GND on the sheet: {RSI[0], RSI[1], RSI[2], RSI[3], RSI[4], RSI[5], RSI[6], RSI[7]}

  // Notes on the sheet:
  //   OUT: Stack top out/cache out on DMA
  //   EN: ENABLE
  //   IN_RD: Signals/indicates that input is being read on the IN port
  //   OUT_WRT: Signals/indicates that output is being written on the OUT port
endmodule
