// Digital circuit STKR16P.dig as structural Verilog
module STKR16P (
  input  clk,
  input  [7:0] RSI,
  output [7:0] SRO
);

  wire A_eq_YX, ALU_ALT, ALU_BUS, ALU_CIN, ALU_CO, ALU_OP0, ALU_OP1, ALU_WC, ALU_ZERO, and_1_out, and_2_out,
       and_3_out, and_4_out, CARRY_q, CLOCK, CLOCK_ENABLE_out, DECODE, demultiplexer_7_out_0,
       demultiplexer_7_out_1, EXECUTE, FETCH, FTCH_OR, JMPYX, LIT_RD, MEM_RD, MEM_WRT, not_1_out,
       od8x8bsrfv2_1_p7, od8x8bsrfv2_1_p8, od8x8bsrfv2_1_p9, od8x8bsrfv2_1_p10, od8x8bsrfv2_2_p7,
       od8x8bsrfv2_2_p8, od8x8bsrfv2_2_p9, od8x8bsrfv2_2_p10, od8x8bsrfv2_3_p7, od8x8bsrfv2_3_p8,
       od8x8bsrfv2_3_p9, od8x8bsrfv2_3_p10, or_2_out, or_4_out, PC_INC, PC_sl, PC_su, RA_sl, RA_su,
       RESET_out, SIG_BOOT, SIG_ENABLE, STEP_out, STK_DIR, STK_EN, STK_IN, STK_OUT, XEN, XOUT, YEN, YOUT;
  wire [1:0] demultiplexer_3_out_0, demultiplexer_3_out_1;
  wire [7:0] demultiplexer_1_out_0, demultiplexer_2_out_0, demultiplexer_2_out_1, demultiplexer_4_out_0,
       demultiplexer_4_out_1, demultiplexer_5_out_0, demultiplexer_5_out_1, demultiplexer_6_out_0,
       demultiplexer_6_out_1, driver_1_out, driver_2_out, driver_5_out, driver_10_out, driver_12_out, IR_qw,
       multiplexer_1_out, multiplexer_3_out, NSEC_d, od8x8bsrfv2_1_p5, pulldown_2_out, ssalu8b_1_y, VSEC_d,
       X_q, Y_q;
  wire [15:0] A_qw, driver_8_out, driver_9_out, multiplexer_2_out, pc16_1_qw;
  wire [15:8] IR_qw_2;
  wire [31:0] CONTROL_WORD_qw, DECODER_d;
  wire [31:22] driver_14_out;

  DipSwitch START (.out(SIG_BOOT));
  DipSwitch RESET (.out(RESET_out));
  Button STEP (.out(STEP_out));
  DipSwitch CLOCK_ENABLE (.out(CLOCK_ENABLE_out));
  DipSwitch CPU_ENABLE (.out(SIG_ENABLE));
  assign driver_1_out = STK_OUT ? pulldown_2_out : 8'bz;  // Driver driver_1
  assign driver_2_out = STK_IN ? driver_1_out : 8'bz;  // Driver driver_2
  PullDown #(.Bits(8)) pulldown_1 (.out(driver_1_out));
  and and_1 (and_1_out, CLOCK_ENABLE_out, clk);
  PullDown #(.Bits(8)) pulldown_2 (.out(pulldown_2_out));
  Multiplexer #(.Bits(8)) multiplexer_1 (
    .sel(ALU_BUS), .in_0(ssalu8b_1_y), .in_1(driver_2_out), .out(multiplexer_1_out));
  or or_1 (CLOCK, STEP_out, and_1_out);
  assign driver_1_out = LIT_RD ? IR_qw : 8'bz;  // Driver driver_3
  // od8x8bsrfV2 od8x8bsrfv2_1: pin names not known; wires that end beside it: multiplexer_1_out, STK_DIR, STK_EN, CLOCK, od8x8bsrfv2_1_p5, RESET_out, od8x8bsrfv2_1_p7, od8x8bsrfv2_1_p8, od8x8bsrfv2_1_p9, od8x8bsrfv2_1_p10
  Demultiplexer #(.Bits(8)) demultiplexer_1 (
    .sel(ALU_BUS), .in(od8x8bsrfv2_1_p5), .out_0(demultiplexer_1_out_0), .out_1(pulldown_2_out));
  assign driver_1_out = MEM_RD ? demultiplexer_5_out_0 : 8'bz;  // Driver driver_4
  assign driver_5_out = MEM_WRT ? driver_1_out : 8'bz;  // Driver driver_5
  assign driver_1_out = XOUT ? X_q : 8'bz;  // Driver driver_6
  assign driver_1_out = YOUT ? Y_q : 8'bz;  // Driver driver_7
  Demultiplexer #(.Bits(8)) demultiplexer_2 (
    .sel(YEN), .in(demultiplexer_1_out_0), .out_0(demultiplexer_2_out_0), .out_1(demultiplexer_2_out_1));
  CREG8 X (.D(demultiplexer_2_out_0), .R(RESET_out), .CLK(CLOCK), .EN(XEN), .Q(X_q));
  CREG8 Y (.D(demultiplexer_2_out_1), .R(RESET_out), .CLK(CLOCK), .EN(YEN), .Q(Y_q));
  // od8x8bsrfV2 od8x8bsrfv2_2: pin names not known; wires that end beside it: od8x8bsrfv2_1_p8, od8x8bsrfv2_1_p10, STK_EN, od8x8bsrfv2_1_p9, od8x8bsrfv2_1_p7, RESET_out, od8x8bsrfv2_2_p7, od8x8bsrfv2_2_p8, od8x8bsrfv2_2_p9, od8x8bsrfv2_2_p10
  or or_2 (or_2_out, JMPYX, PC_INC);
  assign driver_8_out = or_2_out ? {Y_q, X_q} : 16'bz;  // Driver driver_8
  assign driver_9_out = A_eq_YX ? {Y_q, X_q} : 16'bz;  // Driver driver_9
  SSALU8B ssalu8b_1 (
    .A(X_q), .X(Y_q), .OP0(ALU_OP0), .OP1(ALU_OP1), .ALT(ALU_ALT), .CO(ALU_CO), .CIN(ALU_CIN),
    .Y(ssalu8b_1_y), .Z(ALU_ZERO));
  PC16 pc16_1 (
    .WE(or_2_out), .DW(driver_8_out), .CLK(CLOCK), .S_l(PC_sl), .S_u(PC_su), .R(RESET_out),
    .PC_plus__plus(PC_INC), .STRIDE(2'b00), .COUNT(PC_INC), .LOAD(JMPYX), .QW(pc16_1_qw));
  CREG16CR A (.E(A_eq_YX), .DW(driver_9_out), .CLK(CLOCK), .S_l(RA_sl), .S_u(RA_su), .R(RESET_out), .QW(A_qw));
  // od8x8bsrfV2 od8x8bsrfv2_3: pin names not known; wires that end beside it: od8x8bsrfv2_2_p8, od8x8bsrfv2_2_p10, STK_EN, od8x8bsrfv2_2_p9, od8x8bsrfv2_2_p7, RESET_out, od8x8bsrfv2_3_p7, od8x8bsrfv2_3_p8, od8x8bsrfv2_3_p9, od8x8bsrfv2_3_p10
  Multiplexer #(.Bits(16)) multiplexer_2 (.sel(FETCH), .in_0(A_qw), .in_1(pc16_1_qw), .out(multiplexer_2_out));
  // od8x8bsrfV2 od8x8bsrfv2_4: pin names not known; wires that end beside it: od8x8bsrfv2_3_p8, od8x8bsrfv2_3_p10, STK_EN, od8x8bsrfv2_3_p9, od8x8bsrfv2_3_p7, RESET_out, RSI, SRO
  not not_1 (not_1_out, multiplexer_2_out[15]);
  EEPROM #(.AddrBits(15), .Bits(8)) NSEC (
    .A(multiplexer_2_out[14:0]), .CS(multiplexer_2_out[15]), .WE(demultiplexer_3_out_1[1]),
    .OE(demultiplexer_3_out_1[0]), .D(NSEC_d));
  Demultiplexer #(.Bits(2)) demultiplexer_3 (
    .sel(multiplexer_2_out[15]), .in({MEM_WRT, MEM_RD}), .out_0(demultiplexer_3_out_0),
    .out_1(demultiplexer_3_out_1));
  RAMSinglePortSel #(.AddrBits(15), .Bits(8)) VSEC (
    .A(multiplexer_2_out[14:0]), .CS(not_1_out), .WE(demultiplexer_3_out_0[1]),
    .OE(demultiplexer_3_out_0[0]), .D(VSEC_d));
  PullDown #(.Bits(8)) pulldown_3 (.out(NSEC_d));
  PullDown #(.Bits(8)) pulldown_4 (.out(VSEC_d));
  assign driver_10_out = demultiplexer_3_out_1[0] ? NSEC_d : 8'bz;  // Driver driver_10
  assign NSEC_d = demultiplexer_3_out_1[1] ? demultiplexer_4_out_1 : 8'bz;  // Driver driver_11
  assign driver_12_out = demultiplexer_3_out_0[0] ? VSEC_d : 8'bz;  // Driver driver_12
  assign VSEC_d = demultiplexer_3_out_0[1] ? demultiplexer_4_out_0 : 8'bz;  // Driver driver_13
  PullDown #(.Bits(8)) pulldown_5 (.out(driver_10_out));
  PullDown #(.Bits(8)) pulldown_6 (.out(driver_12_out));
  and and_2 (and_2_out, CLOCK, SIG_ENABLE);
  Multiplexer #(.Bits(8)) multiplexer_3 (
    .sel(multiplexer_2_out[15]), .in_0(driver_12_out), .in_1(driver_10_out), .out(multiplexer_3_out));
  Demultiplexer #(.Bits(8)) demultiplexer_4 (
    .sel(multiplexer_2_out[15]), .in(driver_5_out), .out_0(demultiplexer_4_out_0),
    .out_1(demultiplexer_4_out_1));
  D_FF_AS FETCH_IR (.Set(SIG_BOOT), .D(EXECUTE), .C(and_2_out), .Clr(RESET_out), .Q(FETCH));  // open: nQ
  Demultiplexer #(.Bits(8)) demultiplexer_5 (
    .sel(FETCH), .in(multiplexer_3_out), .out_0(demultiplexer_5_out_0), .out_1(demultiplexer_5_out_1));
  Demultiplexer #(.Bits(8)) demultiplexer_6 (
    .sel(FETCH), .in(demultiplexer_5_out_1), .out_0(demultiplexer_6_out_0), .out_1(demultiplexer_6_out_1));
  D_FF_AS u_DECODE (.Set(1'b0), .D(FETCH), .C(and_2_out), .Clr(RESET_out), .Q(DECODE));  // open: nQ
  CREG16 IR (
    .E(FETCH), .DW({demultiplexer_6_out_1, demultiplexer_6_out_0}), .CLK(CLOCK), .S_l(FTCH_OR), .S_u(FETCH),
    .R(RESET_out), .QW({IR_qw_2, IR_qw}));
  Demultiplexer demultiplexer_7 (
    .sel(DECODER_d[31]), .in(DECODE), .out_0(demultiplexer_7_out_0), .out_1(demultiplexer_7_out_1));
  D_FF_AS FETCH_OR (.Set(1'b0), .D(demultiplexer_7_out_1), .C(and_2_out), .Clr(RESET_out), .Q(FTCH_OR));  // open: nQ
  or or_3 (PC_INC, DECODE, and_3_out);
  and and_3 (and_3_out, EXECUTE, DECODER_d[31]);
  or or_4 (or_4_out, demultiplexer_7_out_0, FTCH_OR);
  ROM #(.AddrBits(8), .Bits(32)) DECODER (.A(IR_qw_2), .sel(DECODE), .D(DECODER_d));
  PullDown #(.Bits(32)) pulldown_7 (.out(DECODER_d));
  D_FF_AS u_EXECUTE (.Set(1'b0), .D(or_4_out), .C(and_2_out), .Clr(RESET_out), .Q(EXECUTE));  // open: nQ
  CWR32 CONTROL_WORD (.DCW(DECODER_d), .CLK(CLOCK), .R(RESET_out), .E(DECODE), .QW(CONTROL_WORD_qw));
  assign {driver_14_out, ALU_WC, PC_su, PC_sl, MEM_RD, MEM_WRT, JMPYX, RA_su, RA_sl, A_eq_YX, ALU_ALT, ALU_OP1, ALU_OP0, ALU_BUS, STK_DIR, STK_EN, STK_IN, STK_OUT, YEN, XEN, YOUT, XOUT, LIT_RD} = EXECUTE ? CONTROL_WORD_qw : 32'bz;  // Driver driver_14
  PullDown #(.Bits(32)) pulldown_8 (.out({driver_14_out, ALU_WC, PC_su, PC_sl, MEM_RD, MEM_WRT, JMPYX, RA_su, RA_sl, A_eq_YX, ALU_ALT, ALU_OP1, ALU_OP0, ALU_BUS, STK_DIR, STK_EN, STK_IN, STK_OUT, YEN, XEN, YOUT, XOUT, LIT_RD}));
  and and_4 (and_4_out, CLOCK, ~ALU_BUS);  // And
  D_FF_AS CARRY (.Set(1'b0), .D(ALU_CO), .C(and_4_out), .Clr(RESET_out), .Q(CARRY_q));  // open: nQ
  D_FF_AS ZERO (.Set(1'b0), .D(ALU_ZERO), .C(and_4_out), .Clr(RESET_out));  // open: Q, nQ
  assign ALU_CIN = ALU_WC ? CARRY_q : 1'bz;  // Driver driver_15

  // Other names for the same wires on the sheet: MEMOP[1:0] = {MEM_WRT, MEM_RD}; FTCH_IR = FETCH
endmodule
