// Digital circuit STKR16P2EEP.dig as structural Verilog
module STKR16P2EEP (
  input  clk,
  input  [7:0] RSI,
  output [7:0] SRO
);

  wire A_eq_YX, ALU_ALT, ALU_BUS, ALU_CIN, ALU_CO, ALU_FLAG, ALU_OP0, ALU_OP1, ALU_WC, ALU_ZERO, and_1_out,
       and_2_out, and_3_out, and_4_out, and_5_out, and_6_out, and_7_out, and_8_out, AOUT, CARRY_q, CLOCK,
       CLOCK_ENABLE_out, DECODE, demultiplexer_7_out_0, demultiplexer_7_out_1, EDIT_MICROPROGRAM_out,
       EXECUTE, FETCH, FLG__NZ, FLG_ZERO, FTCH_IR, FTCH_OR, JMPYX, LIT_RD, MEM_RD, MEM_WRT,
       multiplexer_7_out, not_1_out, od8x8bsrfv2_1_p7, od8x8bsrfv2_1_p8, od8x8bsrfv2_1_p9, od8x8bsrfv2_1_p10,
       od8x8bsrfv2_2_p7, od8x8bsrfv2_2_p8, od8x8bsrfv2_2_p9, od8x8bsrfv2_2_p10, od8x8bsrfv2_3_p7,
       od8x8bsrfv2_3_p8, od8x8bsrfv2_3_p9, od8x8bsrfv2_3_p10, or_2_out, or_6_out, or_7_out, or_8_out,
       or_9_out, PC_INC, PC_sl, PC_su, PCOUT, RA_sl, RA_su, RESET_out, SIG_BOOT, SIG_ENABLE, STEP_out,
       STK_DIR, STK_EN, STK_IN, STK_OUT, STORE_CONTROL_WORD_out, WRBSEL, XEN, XOUT, YEN, YOUT;
  wire [0:0] MEMOP;
  wire [1:0] demultiplexer_3_out_0, demultiplexer_3_out_1;
  wire [3:0] dipswitch_7_out, dipswitch_11_out;
  wire [7:0] A_qw, A_qw_2, demultiplexer_1_out_0, demultiplexer_2_out_0, demultiplexer_2_out_1,
       demultiplexer_4_out_0, demultiplexer_4_out_1, demultiplexer_5_out_0, demultiplexer_5_out_1,
       demultiplexer_6_out_0, demultiplexer_6_out_1, driver_1_out, driver_2_out, driver_5_out, driver_12_out,
       driver_14_out, IR_qw, multiplexer_1_out, multiplexer_2_out, multiplexer_3_out, multiplexer_5_out,
       multiplexer_6_out, NSEC_d, od8x8bsrfv2_1_p5, pc16_1_qw, pc16_1_qw_2, pulldown_2_out, ssalu8b_1_y,
       VSEC_d, X_q, Y_q;
  wire [15:0] driver_9_out, driver_10_out, multiplexer_4_out;
  wire [15:8] IR_qw_2;
  wire [31:0] CONTROL_WORD_qw, demultiplexer_8_out_0, demultiplexer_8_out_1, INSTRUCTION_SET_d,
       W__OPERAND_out;
  wire [31:26] driver_16_out;

  DipSwitch START (.out(SIG_BOOT));
  DipSwitch RESET (.out(RESET_out));
  Button STEP (.out(STEP_out));
  DipSwitch CLOCK_ENABLE (.out(CLOCK_ENABLE_out));
  DipSwitch CPU_ENABLE (.out(SIG_ENABLE));
  assign driver_1_out = STK_OUT ? pulldown_2_out : 8'bz;  // Driver driver_1
  assign driver_2_out = STK_IN ? driver_1_out : 8'bz;  // Driver driver_2
  PullDown #(.Bits(8)) pulldown_1 (.out(driver_1_out));
  and and_1 (and_1_out, CLOCK_ENABLE_out, clk);
  PullDown #(.Bits(8)) pulldown_2 (.out(pulldown_2_out));
  Multiplexer #(.Bits(8)) multiplexer_1 (
    .sel(ALU_BUS), .in_0(ssalu8b_1_y), .in_1(driver_2_out), .out(multiplexer_1_out));
  or or_1 (CLOCK, STEP_out, and_1_out);
  assign driver_1_out = LIT_RD ? IR_qw : 8'bz;  // Driver driver_3
  // od8x8bsrfV2 od8x8bsrfv2_1: pin names not known; wires that end beside it: multiplexer_1_out, STK_DIR, STK_EN, CLOCK, od8x8bsrfv2_1_p5, RESET_out, od8x8bsrfv2_1_p7, od8x8bsrfv2_1_p8, od8x8bsrfv2_1_p9, od8x8bsrfv2_1_p10
  Demultiplexer #(.Bits(8)) demultiplexer_1 (
    .sel(ALU_BUS), .in(od8x8bsrfv2_1_p5), .out_0(demultiplexer_1_out_0), .out_1(pulldown_2_out));
  assign driver_1_out = MEM_RD ? demultiplexer_5_out_0 : 8'bz;  // Driver driver_4
  assign driver_5_out = MEM_WRT ? driver_1_out : 8'bz;  // Driver driver_5
  assign driver_1_out = XOUT ? X_q : 8'bz;  // Driver driver_6
  assign driver_1_out = YOUT ? Y_q : 8'bz;  // Driver driver_7
  Demultiplexer #(.Bits(8)) demultiplexer_2 (
    .sel(YEN), .in(demultiplexer_1_out_0), .out_0(demultiplexer_2_out_0), .out_1(demultiplexer_2_out_1));
  CREG8 X (.D(demultiplexer_2_out_0), .R(RESET_out), .CLK(CLOCK), .EN(XEN), .Q(X_q));
  CREG8 Y (.D(demultiplexer_2_out_1), .R(RESET_out), .CLK(CLOCK), .EN(YEN), .Q(Y_q));
  PullDown #(.Bits(8)) pulldown_3 (.out(driver_5_out));
  // od8x8bsrfV2 od8x8bsrfv2_2: pin names not known; wires that end beside it: od8x8bsrfv2_1_p8, od8x8bsrfv2_1_p10, STK_EN, od8x8bsrfv2_1_p9, od8x8bsrfv2_1_p7, RESET_out, od8x8bsrfv2_2_p7, od8x8bsrfv2_2_p8, od8x8bsrfv2_2_p9, od8x8bsrfv2_2_p10
  assign driver_1_out = PCOUT ? multiplexer_2_out : 8'bz;  // Driver driver_8
  or or_2 (or_2_out, JMPYX, PC_INC);
  Multiplexer #(.Bits(8)) multiplexer_2 (.sel(WRBSEL), .in_0(pc16_1_qw), .in_1(pc16_1_qw_2), .out(multiplexer_2_out));
  assign driver_9_out = or_2_out ? {Y_q, X_q} : 16'bz;  // Driver driver_9
  assign driver_10_out = A_eq_YX ? {Y_q, X_q} : 16'bz;  // Driver driver_10
  assign driver_1_out = AOUT ? multiplexer_3_out : 8'bz;  // Driver driver_11
  SSALU8B ssalu8b_1 (
    .A(X_q), .X(Y_q), .OP0(ALU_OP0), .OP1(ALU_OP1), .ALT(ALU_ALT), .CO(ALU_CO), .CIN(ALU_CIN),
    .Y(ssalu8b_1_y), .Z(ALU_ZERO));
  PC16 pc16_1 (
    .WE(or_2_out), .DW(driver_9_out), .CLK(CLOCK), .S_l(PC_sl), .S_u(PC_su), .R(RESET_out),
    .PC_plus__plus(PC_INC), .STRIDE(2'b00), .COUNT(PC_INC), .LOAD(JMPYX), .QW({pc16_1_qw_2, pc16_1_qw}));
  CREG16CR A (
    .E(A_eq_YX), .DW(driver_10_out), .CLK(CLOCK), .S_l(RA_sl), .S_u(RA_su), .R(RESET_out), .QW({A_qw_2, A_qw}));
  Multiplexer #(.Bits(8)) multiplexer_3 (.sel(WRBSEL), .in_0(A_qw), .in_1(A_qw_2), .out(multiplexer_3_out));
  // od8x8bsrfV2 od8x8bsrfv2_3: pin names not known; wires that end beside it: od8x8bsrfv2_2_p8, od8x8bsrfv2_2_p10, STK_EN, od8x8bsrfv2_2_p9, od8x8bsrfv2_2_p7, RESET_out, od8x8bsrfv2_3_p7, od8x8bsrfv2_3_p8, od8x8bsrfv2_3_p9, od8x8bsrfv2_3_p10
  Multiplexer #(.Bits(16)) multiplexer_4 (
    .sel(FETCH), .in_0({A_qw_2, A_qw}), .in_1({pc16_1_qw_2, pc16_1_qw}), .out(multiplexer_4_out));
  // od8x8bsrfV2 od8x8bsrfv2_4: pin names not known; wires that end beside it: od8x8bsrfv2_3_p8, od8x8bsrfv2_3_p10, STK_EN, od8x8bsrfv2_3_p9, od8x8bsrfv2_3_p7, RESET_out, RSI, SRO
  not not_1 (not_1_out, multiplexer_4_out[15]);
  EEPROM #(.AddrBits(15), .Bits(8)) NSEC (
    .A(multiplexer_4_out[14:0]), .CS(multiplexer_4_out[15]), .WE(demultiplexer_3_out_1[1]),
    .OE(demultiplexer_3_out_1[0]), .D(NSEC_d));
  Demultiplexer #(.Bits(2)) demultiplexer_3 (
    .sel(multiplexer_4_out[15]), .in({MEM_WRT, MEMOP[0]}), .out_0(demultiplexer_3_out_0),
    .out_1(demultiplexer_3_out_1));
  RAMSinglePortSel #(.AddrBits(15), .Bits(8)) VSEC (
    .A(multiplexer_4_out[14:0]), .CS(not_1_out), .WE(demultiplexer_3_out_0[1]),
    .OE(demultiplexer_3_out_0[0]), .D(VSEC_d));
  PullDown #(.Bits(8)) pulldown_4 (.out(NSEC_d));
  PullDown #(.Bits(8)) pulldown_5 (.out(VSEC_d));
  assign driver_12_out = demultiplexer_3_out_1[0] ? NSEC_d : 8'bz;  // Driver driver_12
  assign NSEC_d = demultiplexer_3_out_1[1] ? demultiplexer_4_out_1 : 8'bz;  // Driver driver_13
  assign driver_14_out = demultiplexer_3_out_0[0] ? VSEC_d : 8'bz;  // Driver driver_14
  assign VSEC_d = demultiplexer_3_out_0[1] ? demultiplexer_4_out_0 : 8'bz;  // Driver driver_15
  PullDown #(.Bits(8)) pulldown_6 (.out(driver_12_out));
  PullDown #(.Bits(8)) pulldown_7 (.out(driver_14_out));
  and and_2 (and_2_out, CLOCK, SIG_ENABLE);
  Multiplexer #(.Bits(8)) multiplexer_5 (
    .sel(multiplexer_4_out[15]), .in_0(driver_14_out), .in_1(driver_12_out), .out(multiplexer_5_out));
  Demultiplexer #(.Bits(8)) demultiplexer_4 (
    .sel(multiplexer_4_out[15]), .in(driver_5_out), .out_0(demultiplexer_4_out_0),
    .out_1(demultiplexer_4_out_1));
  D_FF_AS FETCH_IR (.Set(SIG_BOOT), .D(EXECUTE), .C(and_2_out), .Clr(RESET_out), .Q(FTCH_IR));  // open: nQ
  Demultiplexer #(.Bits(8)) demultiplexer_5 (
    .sel(FETCH), .in(multiplexer_5_out), .out_0(demultiplexer_5_out_0), .out_1(demultiplexer_5_out_1));
  LED led_1 (.in(demultiplexer_8_out_1[0]));
  LED led_2 (.in(demultiplexer_8_out_1[1]));
  LED led_3 (.in(demultiplexer_8_out_1[2]));
  LED led_4 (.in(demultiplexer_8_out_1[3]));
  LED led_5 (.in(demultiplexer_8_out_1[4]));
  LED led_6 (.in(demultiplexer_8_out_1[5]));
  LED led_7 (.in(demultiplexer_8_out_1[6]));
  LED led_8 (.in(demultiplexer_8_out_1[7]));
  LED led_9 (.in(demultiplexer_8_out_1[8]));
  LED led_10 (.in(demultiplexer_8_out_1[9]));
  LED led_11 (.in(demultiplexer_8_out_1[10]));
  LED led_12 (.in(demultiplexer_8_out_1[11]));
  LED led_13 (.in(demultiplexer_8_out_1[12]));
  LED led_14 (.in(demultiplexer_8_out_1[13]));
  LED led_15 (.in(demultiplexer_8_out_1[14]));
  LED led_16 (.in(demultiplexer_8_out_1[15]));
  LED led_17 (.in(demultiplexer_8_out_1[16]));
  LED led_18 (.in(demultiplexer_8_out_1[17]));
  LED led_19 (.in(demultiplexer_8_out_1[18]));
  LED led_20 (.in(demultiplexer_8_out_1[19]));
  LED led_21 (.in(demultiplexer_8_out_1[20]));
  LED led_22 (.in(demultiplexer_8_out_1[21]));
  LED led_23 (.in(demultiplexer_8_out_1[22]));
  LED led_24 (.in(demultiplexer_8_out_1[23]));
  LED led_25 (.in(demultiplexer_8_out_1[24]));
  LED led_26 (.in(demultiplexer_8_out_1[25]));
  LED led_27 (.in(demultiplexer_8_out_1[26]));
  LED led_28 (.in(demultiplexer_8_out_1[27]));
  LED led_29 (.in(demultiplexer_8_out_1[28]));
  LED led_30 (.in(demultiplexer_8_out_1[29]));
  LED led_31 (.in(demultiplexer_8_out_1[30]));
  LED led_32 (.in(demultiplexer_8_out_1[31]));
  Demultiplexer #(.Bits(8)) demultiplexer_6 (
    .sel(FTCH_IR), .in(demultiplexer_5_out_1), .out_0(demultiplexer_6_out_0), .out_1(demultiplexer_6_out_1));
  or or_3 (FETCH, FTCH_IR, FTCH_OR);
  D_FF_AS u_DECODE (.Set(1'b0), .D(FTCH_IR), .C(and_2_out), .Clr(RESET_out), .Q(DECODE));  // open: nQ
  or or_4 (MEMOP[0], MEM_RD, FTCH_IR, FTCH_OR);
  CREG16 IR (
    .E(FETCH), .DW({demultiplexer_6_out_1, demultiplexer_6_out_0}), .CLK(CLOCK), .S_l(FTCH_OR),
    .S_u(FTCH_IR), .R(RESET_out), .QW({IR_qw_2, IR_qw}));
  Demultiplexer demultiplexer_7 (
    .sel(or_8_out), .in(DECODE), .out_0(demultiplexer_7_out_0), .out_1(demultiplexer_7_out_1));
  DipSwitch u_LIT_RD (.out(W__OPERAND_out[0]));
  DipSwitch X_OUT (.out(W__OPERAND_out[1]));
  DipSwitch Y_OUT (.out(W__OPERAND_out[2]));
  DipSwitch X_EN (.out(W__OPERAND_out[3]));
  DipSwitch Y_EN (.out(W__OPERAND_out[4]));
  DipSwitch u_STK_OUT (.out(W__OPERAND_out[5]));
  DipSwitch u_STK_IN (.out(W__OPERAND_out[6]));
  DipSwitch u_STK_EN (.out(W__OPERAND_out[7]));
  DipSwitch u_STK_DIR (.out(W__OPERAND_out[8]));
  DipSwitch u_ALU_BUS (.out(W__OPERAND_out[9]));
  DipSwitch u_ALU_OP0 (.out(W__OPERAND_out[10]));
  DipSwitch u_ALU_OP1 (.out(W__OPERAND_out[11]));
  DipSwitch u_ALU_ALT (.out(W__OPERAND_out[12]));
  DipSwitch u_A_eq_YX (.out(W__OPERAND_out[13]));
  DipSwitch RA_S_LOW (.out(W__OPERAND_out[14]));
  DipSwitch RA_S_UP (.out(W__OPERAND_out[15]));
  DipSwitch u_JMPYX (.out(W__OPERAND_out[16]));
  DipSwitch u_MEM_WRT (.out(W__OPERAND_out[17]));
  DipSwitch u_MEM_RD (.out(W__OPERAND_out[18]));
  DipSwitch PC_S_LOW (.out(W__OPERAND_out[19]));
  DipSwitch PC_S_UP (.out(W__OPERAND_out[20]));
  DipSwitch W__CARRY (.out(W__OPERAND_out[21]));
  DipSwitch SETFLAGS (.out(W__OPERAND_out[22]));
  DipSwitch u_AOUT (.out(W__OPERAND_out[23]));
  DipSwitch u_PCOUT (.out(W__OPERAND_out[24]));
  DipSwitch SEL_BYTE (.out(W__OPERAND_out[25]));
  DipSwitch dipswitch_1 (.out(W__OPERAND_out[26]));
  DipSwitch dipswitch_2 (.out(W__OPERAND_out[27]));
  DipSwitch dipswitch_3 (.out(W__OPERAND_out[28]));
  DipSwitch ZERO_NZ (.out(W__OPERAND_out[29]));
  DipSwitch CONDITIONAL (.out(W__OPERAND_out[30]));
  DipSwitch W__OPERAND (.out(W__OPERAND_out[31]));
  DipSwitch EDIT_MICROPROGRAM (.out(EDIT_MICROPROGRAM_out));
  D_FF_AS FETCH_OR (.Set(1'b0), .D(demultiplexer_7_out_1), .C(and_2_out), .Clr(RESET_out), .Q(FTCH_OR));  // open: nQ
  or or_5 (PC_INC, DECODE, and_3_out);
  and and_3 (and_3_out, EXECUTE, or_8_out);
  Multiplexer #(.Bits(8)) multiplexer_6 (
    .sel(EDIT_MICROPROGRAM_out), .in_0(IR_qw_2), .in_1({dipswitch_11_out, dipswitch_7_out}),
    .out(multiplexer_6_out));
  or or_6 (or_6_out, EDIT_MICROPROGRAM_out, DECODE);
  or or_7 (or_7_out, demultiplexer_7_out_0, FTCH_OR);
  Seven_Seg_Hex seven_seg_hex_1 (.d(dipswitch_11_out), .dp(1'b0));
  and and_4 (and_4_out, EDIT_MICROPROGRAM_out, STORE_CONTROL_WORD_out);
  Seven_Seg_Hex seven_seg_hex_2 (.d(IR_qw_2[15:12]), .dp(1'b0));
  Seven_Seg_Hex seven_seg_hex_3 (.d(dipswitch_7_out), .dp(1'b0));
  DipSwitch dipswitch_4 (.out(dipswitch_7_out[0]));
  DipSwitch dipswitch_5 (.out(dipswitch_7_out[1]));
  DipSwitch dipswitch_6 (.out(dipswitch_7_out[2]));
  DipSwitch dipswitch_7 (.out(dipswitch_7_out[3]));
  DipSwitch dipswitch_8 (.out(dipswitch_11_out[0]));
  DipSwitch dipswitch_9 (.out(dipswitch_11_out[1]));
  DipSwitch dipswitch_10 (.out(dipswitch_11_out[2]));
  DipSwitch dipswitch_11 (.out(dipswitch_11_out[3]));
  DipSwitch STORE_CONTROL_WORD (.out(STORE_CONTROL_WORD_out));
  EEPROMDualPort #(.AddrBits(8), .Bits(32)) INSTRUCTION_SET (
    .A(multiplexer_6_out), .Din(W__OPERAND_out), .str(and_4_out), .C(CLOCK), .ld(or_6_out),
    .D(INSTRUCTION_SET_d));
  Seven_Seg_Hex seven_seg_hex_4 (.d(IR_qw_2[11:8]), .dp(1'b0));
  Demultiplexer #(.Bits(32)) demultiplexer_8 (
    .sel(EDIT_MICROPROGRAM_out), .in(INSTRUCTION_SET_d), .out_0(demultiplexer_8_out_0),
    .out_1(demultiplexer_8_out_1));
  PullDown #(.Bits(32)) pulldown_8 (.out(INSTRUCTION_SET_d));
  D_FF_AS u_EXECUTE (.Set(1'b0), .D(or_7_out), .C(and_2_out), .Clr(RESET_out), .Q(EXECUTE));  // open: nQ
  or or_8 (or_8_out, driver_16_out[31], demultiplexer_8_out_0[31]);
  CWR32 CONTROL_WORD (.DCW(demultiplexer_8_out_0), .CLK(CLOCK), .R(RESET_out), .E(DECODE), .QW(CONTROL_WORD_qw));
  assign {driver_16_out, WRBSEL, PCOUT, AOUT, ALU_FLAG, ALU_WC, PC_su, PC_sl, MEM_RD, MEM_WRT, JMPYX, RA_su, RA_sl, A_eq_YX, ALU_ALT, ALU_OP1, ALU_OP0, ALU_BUS, STK_DIR, STK_EN, STK_IN, STK_OUT, YEN, XEN, YOUT, XOUT, LIT_RD} = and_5_out ? CONTROL_WORD_qw : 32'bz;  // Driver driver_16
  and and_5 (and_5_out, or_9_out, EXECUTE);
  or or_9 (or_9_out, and_6_out, ~demultiplexer_8_out_0[30]);  // Or
  and and_6 (and_6_out, demultiplexer_8_out_0[30], multiplexer_7_out);
  and and_7 (and_7_out, ALU_FLAG, ALU_BUS);
  Multiplexer multiplexer_7 (.sel(demultiplexer_8_out_0[29]), .in_0(FLG_ZERO), .in_1(FLG__NZ), .out(multiplexer_7_out));
  and and_8 (and_8_out, CLOCK, ~and_7_out);  // And
  PullDown #(.Bits(32)) pulldown_9 (.out({driver_16_out, WRBSEL, PCOUT, AOUT, ALU_FLAG, ALU_WC, PC_su, PC_sl, MEM_RD, MEM_WRT, JMPYX, RA_su, RA_sl, A_eq_YX, ALU_ALT, ALU_OP1, ALU_OP0, ALU_BUS, STK_DIR, STK_EN, STK_IN, STK_OUT, YEN, XEN, YOUT, XOUT, LIT_RD}));
  D_FF_AS CARRY (.Set(1'b0), .D(ALU_CO), .C(and_8_out), .Clr(RESET_out), .Q(CARRY_q));  // open: nQ
  D_FF_AS ZERO (.Set(1'b0), .D(ALU_ZERO), .C(and_8_out), .Clr(RESET_out), .Q(FLG_ZERO), .nQ(FLG__NZ));
  assign ALU_CIN = ALU_WC ? CARRY_q : 1'bz;  // Driver driver_17

  // Other names for the same wires on the sheet: MEMOP[1] = MEM_WRT

  // Notes on the sheet:
  //   clk: Hz: 1000
  //   contents of INSTRUCTION_SET (hex, n*v repeats v):
  //   0,800002c1,402c0,203a0,188,190,e000,190000,80020001,40190000,60190000
  //   ,80,1080,480,1480,880,1880,c80,1c80,800280,2800280,1000280,3000280
endmodule
