// Digital circuit STKR3TB2.dig as structural Verilog
module STKR3TB2 (
  input  clk
);

  wire Address_ovf, and_1_out, and_2_out, and_3_out, d_ff_as_1_nq, d_ff_as_2_q, d_ff_as_3_q, d_ff_as_4_q,
       d_ff_as_5_q, d_ff_as_6_q, d_ff_as_7_q, dipswitch_17_out, dipswitch_18_out, ENABLE_CPU_out,
       ENABLE_DMA_out, LOAD_out, MANUAL_CLOCK_out, or_1_out, or_2_out, or_3_out, or_4_out, Page_Down_out,
       Page_Up_out, RESET_out, Reset_Page_out, RETRIEVE_out, RTC_ENABLE_out, stkr3p2_1_cpt, stkr3p2_1_dpt,
       stkr3p2_1_in_rd, stkr3p2_1_out_wrt, stkr3p2_1_str;
  wire [3:0] dipswitch_1_out, dipswitch_5_out, Page_out;
  wire [7:0] Address_out, blockramdualport_1_d, dipswitch_9_out, dipswitch_19_out, eepromdualport_1_d,
       stkr3p2_1_a, stkr3p2_1_din, stkr3p2_1_out, stkr3p2_1_sro;

  Button Page_Up (.out(Page_Up_out));
  Button Page_Down (.out(Page_Down_out));
  Button Reset_Page (.out(Reset_Page_out));
  Seven_Seg_Hex seven_seg_hex_1 (.d(dipswitch_5_out), .dp(1'b0));
  DipSwitch dipswitch_1 (.out(dipswitch_1_out[0]));
  DipSwitch dipswitch_2 (.out(dipswitch_1_out[1]));
  DipSwitch dipswitch_3 (.out(dipswitch_1_out[2]));
  DipSwitch dipswitch_4 (.out(dipswitch_1_out[3]));
  DipSwitch dipswitch_5 (.out(dipswitch_5_out[0]));
  DipSwitch dipswitch_6 (.out(dipswitch_5_out[1]));
  DipSwitch dipswitch_7 (.out(dipswitch_5_out[2]));
  DipSwitch dipswitch_8 (.out(dipswitch_5_out[3]));
  or or_1 (or_1_out, Page_Up_out, Page_Down_out);
  Seven_Seg_Hex seven_seg_hex_2 (.d(dipswitch_1_out), .dp(1'b0));
  Button MANUAL_CLOCK (.out(MANUAL_CLOCK_out));
  DipSwitch RTC_ENABLE (.out(RTC_ENABLE_out));
  Button RESET (.out(RESET_out));
  DipSwitch ENABLE_CPU (.out(ENABLE_CPU_out));
  DipSwitch ENABLE_DMA (.out(ENABLE_DMA_out));
  DipSwitch dipswitch_9 (.out(dipswitch_9_out[0]));
  DipSwitch dipswitch_10 (.out(dipswitch_9_out[1]));
  DipSwitch dipswitch_11 (.out(dipswitch_9_out[2]));
  DipSwitch dipswitch_12 (.out(dipswitch_9_out[3]));
  DipSwitch dipswitch_13 (.out(dipswitch_9_out[4]));
  DipSwitch dipswitch_14 (.out(dipswitch_9_out[5]));
  DipSwitch dipswitch_15 (.out(dipswitch_9_out[6]));
  DipSwitch dipswitch_16 (.out(dipswitch_9_out[7]));
  or or_2 (or_2_out, Reset_Page_out, or_1_out);
  DipSwitch dipswitch_17 (.out(dipswitch_17_out));
  DipSwitch dipswitch_18 (.out(dipswitch_18_out));
  and and_1 (and_1_out, RTC_ENABLE_out, clk);
  or or_3 (or_3_out, MANUAL_CLOCK_out, and_1_out);
  Seven_Seg_Hex seven_seg_hex_3 (.d(dipswitch_9_out[7:4]), .dp(1'b0));
  CounterPreset #(.Bits(4)) Page (
    .en(or_1_out), .C(or_2_out), .dir(Page_Down_out), .in(4'b0000), .ld(1'b0), .clr(Reset_Page_out),
    .out(Page_out));  // open: ovf
  CounterPreset #(.Bits(8)) Address (
    .en(or_4_out), .C(or_3_out), .dir(1'b0), .in({dipswitch_5_out, dipswitch_1_out}), .ld(dipswitch_17_out),
    .clr(dipswitch_18_out), .out(Address_out), .ovf(Address_ovf));
  Button LOAD (.out(LOAD_out));
  Button RETRIEVE (.out(RETRIEVE_out));
  Seven_Seg_Hex seven_seg_hex_4 (.d(dipswitch_9_out[3:0]), .dp(1'b0));
  or or_4 (or_4_out, and_2_out, and_3_out);
  Seven_Seg_Hex seven_seg_hex_5 (.d(Page_out), .dp(1'b0));
  D_FF_AS d_ff_as_1 (.Set(Address_ovf), .D(1'b0), .C(or_3_out), .Clr(RESET_out), .nQ(d_ff_as_1_nq));  // open: Q
  D_FF_AS d_ff_as_2 (.Set(LOAD_out), .D(d_ff_as_6_q), .C(or_3_out), .Clr(RESET_out), .Q(d_ff_as_2_q));  // open: nQ
  D_FF_AS d_ff_as_3 (.Set(RETRIEVE_out), .D(d_ff_as_7_q), .C(or_3_out), .Clr(RESET_out), .Q(d_ff_as_3_q));  // open: nQ
  LED led_1 (.in(stkr3p2_1_in_rd));
  Seven_Seg_Hex seven_seg_hex_6 (.d(Address_out[7:4]), .dp(1'b0));
  Seven_Seg_Hex seven_seg_hex_7 (.d(Address_out[3:0]), .dp(1'b0));
  and and_2 (and_2_out, d_ff_as_1_nq, d_ff_as_4_q);
  D_FF_AS d_ff_as_4 (.Set(1'b0), .D(d_ff_as_2_q), .C(or_3_out), .Clr(RESET_out), .Q(d_ff_as_4_q));  // open: nQ
  and and_3 (and_3_out, d_ff_as_1_nq, d_ff_as_5_q);
  D_FF_AS d_ff_as_5 (.Set(1'b0), .D(d_ff_as_3_q), .C(or_3_out), .Clr(RESET_out), .Q(d_ff_as_5_q));  // open: nQ
  D_FF_AS d_ff_as_6 (.Set(1'b0), .D(and_2_out), .C(or_3_out), .Clr(RESET_out), .Q(d_ff_as_6_q));  // open: nQ
  D_FF_AS d_ff_as_7 (.Set(1'b0), .D(and_3_out), .C(or_3_out), .Clr(RESET_out), .Q(d_ff_as_7_q));  // open: nQ
  STKR3P2 stkr3p2_1 (
    .IN(dipswitch_9_out), .IN_RD(stkr3p2_1_in_rd), .OUT(stkr3p2_1_out), .OUT_WRT(stkr3p2_1_out_wrt),
    .RSI(dipswitch_19_out), .SRO(stkr3p2_1_sro), .CPT(stkr3p2_1_cpt), .DPT(stkr3p2_1_dpt), .A(stkr3p2_1_a),
    .D(blockramdualport_1_d), .STR(stkr3p2_1_str), .DIN(stkr3p2_1_din), .DMA_ADDR(Address_out),
    .DMA_DATA(eepromdualport_1_d), .DMA_STR(d_ff_as_2_q), .SIG_DMA(ENABLE_DMA_out), .EN(ENABLE_CPU_out),
    .RST(RESET_out), .CLK(or_3_out));
  EEPROMDualPort #(.AddrBits(12), .Bits(8)) eepromdualport_1 (
    .A({Page_out, Address_out}), .Din(stkr3p2_1_out), .str(d_ff_as_3_q), .C(or_3_out), .ld(d_ff_as_2_q),
    .D(eepromdualport_1_d));
  BlockRAMDualPort #(.AddrBits(8), .Bits(8)) blockramdualport_1 (
    .A(stkr3p2_1_a), .Din(stkr3p2_1_din), .str(stkr3p2_1_str), .C(or_3_out), .D(blockramdualport_1_d));
  LED led_2 (.in(stkr3p2_1_cpt));
  LED led_3 (.in(stkr3p2_1_dpt));
  Seven_Seg_Hex seven_seg_hex_8 (.d(stkr3p2_1_out[7:4]), .dp(1'b0));
  Seven_Seg_Hex seven_seg_hex_9 (.d(stkr3p2_1_sro[7:4]), .dp(1'b0));
  Seven_Seg_Hex seven_seg_hex_10 (.d(stkr3p2_1_out[3:0]), .dp(1'b0));
  Seven_Seg_Hex seven_seg_hex_11 (.d(stkr3p2_1_sro[3:0]), .dp(1'b0));
  LED led_4 (.in(stkr3p2_1_out_wrt));
  Seven_Seg_Hex seven_seg_hex_12 (.d(dipswitch_19_out[7:4]), .dp(1'b0));
  Seven_Seg_Hex seven_seg_hex_13 (.d(dipswitch_19_out[3:0]), .dp(1'b0));
  DipSwitch dipswitch_19 (.out(dipswitch_19_out[0]));
  DipSwitch dipswitch_20 (.out(dipswitch_19_out[1]));
  DipSwitch dipswitch_21 (.out(dipswitch_19_out[2]));
  DipSwitch dipswitch_22 (.out(dipswitch_19_out[3]));
  DipSwitch dipswitch_23 (.out(dipswitch_19_out[4]));
  DipSwitch dipswitch_24 (.out(dipswitch_19_out[5]));
  DipSwitch dipswitch_25 (.out(dipswitch_19_out[6]));
  DipSwitch dipswitch_26 (.out(dipswitch_19_out[7]));

  // Notes on the sheet:
  //   clk: Hz: 100
  //   contents of eepromdualport_1 (hex, n*v repeats v):
  //   b,19,b,19,b,c,3b,19,20,19,9,3b,19,20,1c,238*0,40,1,10
endmodule
