// Digital circuit inc7chpdrafttstboard.dig as structural Verilog
module inc7chpdrafttstboard (
);

  wire counterpreset_1_ovf, d_ff_as_1_q, dipswitch_1_out, dipswitch_10_out, dipswitch_11_out,
       dipswitch_12_out, dipswitch_13_out, dipswitch_14_out, dipswitch_15_out, dipswitch_16_out,
       dipswitch_17_out, dipswitch_18_out, dipswitch_19_out, incrproto7chipdraft_1_p4,
       incrproto7chipdraft_1_p6, incrproto7chipdraft_1_p8;
  wire [3:0] dipswitch_2_out, dipswitch_6_out;
  wire [7:0] counterpreset_1_out, demultiplexer_1_out_0, demultiplexer_1_out_1, driver_1_out, driver_2_out,
       driver_3_out, incrproto7chipdraft_1_p9, NVPAGE_d;

  D_FF_AS d_ff_as_1 (
    .Set(1'b0), .D(dipswitch_1_out), .C(incrproto7chipdraft_1_p4), .Clr(counterpreset_1_ovf), .Q(d_ff_as_1_q));  // open: nQ
  DipSwitch dipswitch_1 (.out(dipswitch_1_out));
  Seven_Seg_Hex seven_seg_hex_1 (.d(dipswitch_6_out), .dp(1'b0));
  DipSwitch dipswitch_2 (.out(dipswitch_2_out[0]));
  DipSwitch dipswitch_3 (.out(dipswitch_2_out[1]));
  DipSwitch dipswitch_4 (.out(dipswitch_2_out[2]));
  DipSwitch dipswitch_5 (.out(dipswitch_2_out[3]));
  DipSwitch dipswitch_6 (.out(dipswitch_6_out[0]));
  DipSwitch dipswitch_7 (.out(dipswitch_6_out[1]));
  DipSwitch dipswitch_8 (.out(dipswitch_6_out[2]));
  DipSwitch dipswitch_9 (.out(dipswitch_6_out[3]));
  Seven_Seg_Hex seven_seg_hex_2 (.d(dipswitch_2_out), .dp(1'b0));
  DipSwitch dipswitch_10 (.out(dipswitch_10_out));
  DipSwitch dipswitch_11 (.out(dipswitch_11_out));
  assign driver_1_out = dipswitch_12_out ? {dipswitch_6_out, dipswitch_2_out} : 8'bz;  // Driver driver_1
  DipSwitch dipswitch_12 (.out(dipswitch_12_out));
  CounterPreset #(.Bits(8)) counterpreset_1 (
    .en(d_ff_as_1_q), .C(incrproto7chipdraft_1_p4), .dir(dipswitch_10_out), .in(driver_1_out),
    .ld(dipswitch_11_out), .clr(dipswitch_16_out), .out(counterpreset_1_out), .ovf(counterpreset_1_ovf));
  assign driver_2_out = dipswitch_13_out ? {dipswitch_6_out, dipswitch_2_out} : 8'bz;  // Driver driver_2
  assign driver_3_out = dipswitch_14_out ? {dipswitch_6_out, dipswitch_2_out} : 8'bz;  // Driver driver_3
  DipSwitch dipswitch_13 (.out(dipswitch_13_out));
  DipSwitch dipswitch_14 (.out(dipswitch_14_out));
  DipSwitch dipswitch_15 (.out(dipswitch_15_out));
  DipSwitch dipswitch_16 (.out(dipswitch_16_out));
  DipSwitch dipswitch_17 (.out(dipswitch_17_out));
  DipSwitch dipswitch_18 (.out(dipswitch_18_out));
  // incrproto7chipdraft incrproto7chipdraft_1: pin names not known; wires that end beside it: driver_3_out, dipswitch_15_out, dipswitch_16_out, incrproto7chipdraft_1_p4, counterpreset_1_out, incrproto7chipdraft_1_p6, dipswitch_17_out, incrproto7chipdraft_1_p8, incrproto7chipdraft_1_p9
  DipSwitch dipswitch_19 (.out(dipswitch_19_out));
  Multiplexer multiplexer_1 (
    .sel(dipswitch_19_out), .in_0(NVPAGE_d[0]), .in_1(driver_2_out[0]), .out(incrproto7chipdraft_1_p6));
  or or_1 (incrproto7chipdraft_1_p8, dipswitch_17_out, dipswitch_18_out);
  Demultiplexer #(.Bits(8)) demultiplexer_1 (
    .sel(incrproto7chipdraft_1_p8), .in(incrproto7chipdraft_1_p9), .out_0(demultiplexer_1_out_0),
    .out_1(demultiplexer_1_out_1));
  Seven_Seg_Hex seven_seg_hex_3 (.d(demultiplexer_1_out_0[7:4]), .dp(1'b0));
  EEPROMDualPort #(.AddrBits(8), .Bits(8)) NVPAGE (
    .A(counterpreset_1_out), .Din(demultiplexer_1_out_1), .str(dipswitch_18_out),
    .C(incrproto7chipdraft_1_p4), .ld(dipswitch_17_out), .D(NVPAGE_d));
  Seven_Seg_Hex seven_seg_hex_4 (.d(demultiplexer_1_out_0[3:0]), .dp(1'b0));
  // Pins of 1 and 8 bits meet at NVPAGE_d
  // Pins of 1 and 8 bits meet at driver_2_out
endmodule
