// Digital circuit incr8upgr8.dig as structural Verilog
module incr8upgr8 (
  input  [7:0] IN,
  input  [7:0] CA_DATA,
  input  [15:0] CA_ADDR,
  input  CA_STR,
  input  SIG_CA,
  input  CLK,
  input  RST,
  input  EN,
  input  [7:0] IRV,
  input  IRQ,
  input  [7:0] FPPT,
  output [7:0] OUT,
  output IORQ,
  output [7:0] SPT,
  output CPT,
  output DPT
);

  wire and_1_out, and_2_out, and_3_out, and_5_out, and_6_out, and_7_out, EXECUTE_q, FETCH_q, INTERRUPT_1_q,
       INTERRUPT_2_q, INTERRUPT_3_q, INTERRUPT_4_q, INTERRUPT_5_q, INTERRUPT_6_q, multiplexer_1_out,
       multiplexer_15_out, not_1_out, not_2_out, or_1_out, or_2_out, or_3_out, or_4_out, or_5_out, or_6_out,
       or_7_out, PC_LSB_ovf, PUSH_REGS_q;
  wire [0:0] demultiplexer_4_out_3;
  wire [1:0] demultiplexer_2_out_0, demultiplexer_2_out_1, demultiplexer_4_out_1, demultiplexer_5_out_0,
       demultiplexer_5_out_1;
  wire [1:1] demultiplexer_4_out_1_2;
  wire [2:0] demultiplexer_4_out_0, demultiplexer_4_out_2;
  wire [5:0] driver_6_out, driver_7_out;
  wire [7:0] blockramdualport_1_d, d_ff_as_1_q, d_ff_as_2_q, d_ff_as_3_q, d_ff_as_4_q, d_ff_as_5_q,
       d_ff_as_6_q, d_ff_as_7_q, demultiplexer_1_out_0, demultiplexer_1_out_1, demultiplexer_3_out_0,
       demultiplexer_3_out_1, demultiplexer_6_out_0, demultiplexer_6_out_1, demultiplexer_7_out_0,
       demultiplexer_7_out_1, demultiplexer_7_out_2, demultiplexer_7_out_3, driver_1_out, driver_8_out, IR_q,
       MACLSB, MACMSB, MDC, multiplexer_2_out, multiplexer_3_out, multiplexer_4_out, multiplexer_5_out,
       multiplexer_6_out, multiplexer_7_out, multiplexer_8_out, multiplexer_9_out, multiplexer_11_out,
       multiplexer_12_out, multiplexer_14_out, multiplexer_16_out, multiplexer_17_out, multiplexer_18_out,
       multiplexer_19_out, PCLSB, PCMSB;
  wire [7:6] driver_7_out_2;
  wire [15:0] multiplexer_10_out, multiplexer_13_out;

  RS_FF_AS PUSH_REGS (.S(INTERRUPT_1_q), .R(INTERRUPT_6_q), .Q(PUSH_REGS_q));  // open: nQ
  D_FF_AS INTERRUPT_1 (.Set(1'b0), .D(and_1_out), .C(and_3_out), .Clr(RST), .Q(INTERRUPT_1_q));  // open: nQ
  D_FF_AS INTERRUPT_2 (.Set(1'b0), .D(INTERRUPT_1_q), .C(and_3_out), .Clr(RST), .Q(INTERRUPT_2_q));  // open: nQ
  D_FF_AS INTERRUPT_3 (.Set(1'b0), .D(INTERRUPT_2_q), .C(and_3_out), .Clr(RST), .Q(INTERRUPT_3_q));  // open: nQ
  D_FF_AS INTERRUPT_4 (.Set(1'b0), .D(INTERRUPT_3_q), .C(and_3_out), .Clr(RST), .Q(INTERRUPT_4_q));  // open: nQ
  D_FF_AS INTERRUPT_5 (.Set(1'b0), .D(INTERRUPT_4_q), .C(and_3_out), .Clr(RST), .Q(INTERRUPT_5_q));  // open: nQ
  D_FF_AS INTERRUPT_6 (.Set(1'b0), .D(INTERRUPT_5_q), .C(and_3_out), .Clr(RST), .Q(INTERRUPT_6_q));  // open: nQ
  and and_1 (and_1_out, EXECUTE_q, IRQ);
  and and_2 (and_2_out, EXECUTE_q, ~IRQ);  // And
  D_FF_AS FETCH (.Set(RST), .D(and_2_out), .C(and_3_out), .Clr(1'b0), .Q(FETCH_q));  // open: nQ
  or or_1 (or_1_out, FETCH_q, INTERRUPT_6_q);
  or or_2 (or_2_out, INTERRUPT_1_q, INTERRUPT_2_q, INTERRUPT_3_q, INTERRUPT_4_q, INTERRUPT_5_q);
  assign driver_1_out = INTERRUPT_1_q ? MDC : 8'bz;  // Driver driver_1
  D_FF_AS EXECUTE (.Set(1'b0), .D(or_1_out), .C(and_3_out), .Clr(RST), .Q(EXECUTE_q));  // open: nQ
  assign driver_1_out = INTERRUPT_2_q ? MACLSB : 8'bz;  // Driver driver_2
  or or_3 (or_3_out, ~EN, SIG_CA);  // Or
  and and_3 (and_3_out, ~or_3_out, CLK);  // And
  assign driver_1_out = INTERRUPT_3_q ? MACMSB : 8'bz;  // Driver driver_3
  assign driver_1_out = INTERRUPT_4_q ? PCLSB : 8'bz;  // Driver driver_4
  not not_1 (not_1_out, and_6_out);
  assign driver_1_out = INTERRUPT_5_q ? PCMSB : 8'bz;  // Driver driver_5
  Multiplexer multiplexer_1 (.sel(driver_7_out_2[6]), .in_0(and_6_out), .in_1(not_1_out), .out(multiplexer_1_out));
  assign driver_6_out = or_4_out ? driver_7_out : 6'bz;  // Driver driver_6
  PullDown #(.Bits(6)) pulldown_1 (.out(driver_6_out));
  or or_4 (or_4_out, multiplexer_1_out, ~driver_7_out_2[7]);  // Or
  assign {driver_7_out_2, driver_7_out} = EXECUTE_q ? IR_q : 8'bz;  // Driver driver_7
  PullDown #(.Bits(8)) pulldown_2 (.out({driver_7_out_2, driver_7_out}));
  Demultiplexer #(.Bits(8)) demultiplexer_1 (
    .sel(demultiplexer_4_out_2[1]), .in(demultiplexer_7_out_2), .out_0(demultiplexer_1_out_0),
    .out_1(demultiplexer_1_out_1));
  Demultiplexer #(.Bits(2)) demultiplexer_2 (
    .sel(demultiplexer_4_out_2[1]), .in({demultiplexer_4_out_2[2], demultiplexer_4_out_2[0]}),
    .out_0(demultiplexer_2_out_0), .out_1(demultiplexer_2_out_1));
  Demultiplexer #(.Bits(8)) demultiplexer_3 (
    .sel(demultiplexer_4_out_1_2[1]), .in(demultiplexer_7_out_1), .out_0(demultiplexer_3_out_0),
    .out_1(demultiplexer_3_out_1));
  Multiplexer #(.Bits(8)) multiplexer_2 (
    .sel(PUSH_REGS_q), .in_0(demultiplexer_7_out_3), .in_1(driver_1_out), .out(multiplexer_2_out));
  Demultiplexer #(.Selector_Bits(2), .Bits(3)) demultiplexer_4 (
    .sel(driver_6_out[4:3]), .in(driver_6_out[2:0]), .out_0(demultiplexer_4_out_0),
    .out_1({demultiplexer_4_out_1[1], demultiplexer_4_out_1_2[1], demultiplexer_4_out_1[0]}),
    .out_2(demultiplexer_4_out_2), .out_3({IORQ, DPT, demultiplexer_4_out_3[0]}));
  or or_5 (or_5_out, or_2_out, demultiplexer_4_out_3[0]);
  Multiplexer #(.Bits(8)) multiplexer_3 (
    .sel(INTERRUPT_6_q), .in_0(demultiplexer_1_out_1), .in_1(IRV), .out(multiplexer_3_out));
  Demultiplexer #(.Bits(2)) demultiplexer_5 (
    .sel(demultiplexer_4_out_1_2[1]), .in(demultiplexer_4_out_1), .out_0(demultiplexer_5_out_0),
    .out_1(demultiplexer_5_out_1));
  Multiplexer #(.Bits(8)) multiplexer_4 (.sel(IORQ), .in_0(multiplexer_2_out), .in_1(IN), .out(multiplexer_4_out));
  and and_4 (CPT, or_5_out, ~CLK);  // And
  or or_6 (or_6_out, INTERRUPT_6_q, demultiplexer_2_out_1[1]);
  Multiplexer #(.Bits(8)) multiplexer_5 (
    .sel(DPT), .in_0(multiplexer_4_out), .in_1(d_ff_as_2_q), .out(multiplexer_5_out));
  or or_7 (or_7_out, EXECUTE_q, demultiplexer_2_out_0[0]);
  D_FF_AS #(.Bits(8)) d_ff_as_1 (.Set(1'b0), .D(multiplexer_5_out), .C(CPT), .Clr(RST), .Q(d_ff_as_1_q));  // open: nQ
  CounterPreset #(.Bits(8)) PC_MSB (
    .en(PC_LSB_ovf), .C(CLK), .dir(1'b0), .in(multiplexer_3_out), .ld(or_6_out), .clr(RST), .out(PCMSB));  // open: ovf
  CounterPreset #(.Bits(8)) PC_LSB (
    .en(or_7_out), .C(CLK), .dir(1'b0), .in(demultiplexer_1_out_0), .ld(demultiplexer_2_out_0[1]), .clr(RST),
    .out(PCLSB), .ovf(PC_LSB_ovf));
  CounterPreset #(.Bits(8)) MAC_LSB (
    .en(demultiplexer_5_out_0[0]), .C(CLK), .dir(1'b0), .in(demultiplexer_3_out_0),
    .ld(demultiplexer_5_out_0[1]), .clr(RST), .out(MACLSB));  // open: ovf
  CounterPreset #(.Bits(8)) u_MDC (
    .en(demultiplexer_4_out_0[0]), .C(CLK), .dir(demultiplexer_4_out_0[1]), .in(demultiplexer_7_out_0),
    .ld(demultiplexer_4_out_0[2]), .clr(RST), .out(MDC));  // open: ovf
  Multiplexer #(.Bits(8)) multiplexer_6 (.sel(DPT), .in_0(d_ff_as_1_q), .in_1(d_ff_as_3_q), .out(multiplexer_6_out));
  Multiplexer #(.Bits(8)) multiplexer_7 (
    .sel(demultiplexer_4_out_1_2[1]), .in_0(MACLSB), .in_1(MACMSB), .out(multiplexer_7_out));
  Multiplexer #(.Bits(8)) multiplexer_8 (
    .sel(demultiplexer_4_out_2[1]), .in_0(PCLSB), .in_1(PCMSB), .out(multiplexer_8_out));
  D_FF_AS #(.Bits(8)) d_ff_as_2 (.Set(1'b0), .D(multiplexer_6_out), .C(CPT), .Clr(RST), .Q(d_ff_as_2_q));  // open: nQ
  Multiplexer #(.Bits(8)) multiplexer_9 (.sel(DPT), .in_0(d_ff_as_2_q), .in_1(d_ff_as_4_q), .out(multiplexer_9_out));
  CounterPreset #(.Bits(8)) MAC_MSB (
    .en(demultiplexer_5_out_1[0]), .C(CLK), .dir(1'b0), .in(demultiplexer_3_out_1),
    .ld(demultiplexer_5_out_1[1]), .clr(RST), .out(MACMSB));  // open: ovf
  Multiplexer #(.Bits(16)) multiplexer_10 (
    .sel(FETCH_q), .in_0({MACMSB, MACLSB}), .in_1({PCMSB, PCLSB}), .out(multiplexer_10_out));
  Multiplexer #(.Selector_Bits(2), .Bits(8)) multiplexer_11 (
    .sel(driver_6_out[4:3]), .in_0(MDC), .in_1(multiplexer_7_out), .in_2(multiplexer_8_out),
    .in_3(d_ff_as_1_q), .out(multiplexer_11_out));
  D_FF_AS #(.Bits(8)) d_ff_as_3 (.Set(1'b0), .D(multiplexer_9_out), .C(CPT), .Clr(RST), .Q(d_ff_as_3_q));  // open: nQ
  Multiplexer #(.Bits(8)) multiplexer_12 (.sel(DPT), .in_0(d_ff_as_3_q), .in_1(d_ff_as_5_q), .out(multiplexer_12_out));
  Multiplexer #(.Bits(16)) multiplexer_13 (
    .sel(SIG_CA), .in_0(multiplexer_10_out), .in_1(CA_ADDR), .out(multiplexer_13_out));
  Multiplexer #(.Bits(8)) multiplexer_14 (
    .sel(SIG_CA), .in_0(multiplexer_11_out), .in_1(CA_DATA), .out(multiplexer_14_out));
  not not_2 (not_2_out, CLK);
  D_FF_AS #(.Bits(8)) d_ff_as_4 (.Set(1'b0), .D(multiplexer_12_out), .C(CPT), .Clr(RST), .Q(d_ff_as_4_q));  // open: nQ
  Multiplexer multiplexer_15 (.sel(SIG_CA), .in_0(driver_6_out[5]), .in_1(CA_STR), .out(multiplexer_15_out));
  BlockRAMDualPort #(.AddrBits(16), .Bits(8)) blockramdualport_1 (
    .A(multiplexer_13_out), .Din(multiplexer_14_out), .str(multiplexer_15_out), .C(not_2_out),
    .D(blockramdualport_1_d));
  Multiplexer #(.Bits(8)) multiplexer_16 (.sel(DPT), .in_0(d_ff_as_4_q), .in_1(d_ff_as_6_q), .out(multiplexer_16_out));
  Demultiplexer #(.Bits(8)) demultiplexer_6 (
    .sel(FETCH_q), .in(blockramdualport_1_d), .out_0(demultiplexer_6_out_0), .out_1(demultiplexer_6_out_1));
  D_FF_AS #(.Bits(8)) d_ff_as_5 (.Set(1'b0), .D(multiplexer_16_out), .C(CPT), .Clr(RST), .Q(d_ff_as_5_q));  // open: nQ
  Register #(.Bits(8)) IR (.D(demultiplexer_6_out_1), .C(CLK), .en(FETCH_q), .Q(IR_q));
  and and_5 (and_5_out, ~demultiplexer_6_out_0[4], ~demultiplexer_6_out_0[5], ~demultiplexer_6_out_0[6], ~demultiplexer_6_out_0[7]);  // And
  and and_6 (and_6_out, and_7_out, and_5_out);
  Multiplexer #(.Bits(8)) multiplexer_17 (.sel(DPT), .in_0(d_ff_as_5_q), .in_1(d_ff_as_7_q), .out(multiplexer_17_out));
  Demultiplexer #(.Selector_Bits(2), .Bits(8)) demultiplexer_7 (
    .sel(driver_6_out[4:3]), .in(demultiplexer_6_out_0), .out_0(demultiplexer_7_out_0),
    .out_1(demultiplexer_7_out_1), .out_2(demultiplexer_7_out_2), .out_3(demultiplexer_7_out_3));
  and and_7 (and_7_out, ~demultiplexer_6_out_0[0], ~demultiplexer_6_out_0[1], ~demultiplexer_6_out_0[2], ~demultiplexer_6_out_0[3]);  // And
  D_FF_AS #(.Bits(8)) d_ff_as_6 (.Set(1'b0), .D(multiplexer_17_out), .C(CPT), .Clr(RST), .Q(d_ff_as_6_q));  // open: nQ
  Multiplexer #(.Bits(8)) multiplexer_18 (.sel(DPT), .in_0(d_ff_as_6_q), .in_1(SPT), .out(multiplexer_18_out));
  D_FF_AS #(.Bits(8)) d_ff_as_7 (.Set(1'b0), .D(multiplexer_18_out), .C(CPT), .Clr(RST), .Q(d_ff_as_7_q));  // open: nQ
  Multiplexer #(.Bits(8)) multiplexer_19 (.sel(DPT), .in_0(d_ff_as_7_q), .in_1(FPPT), .out(multiplexer_19_out));
  D_FF_AS #(.Bits(8)) d_ff_as_8 (.Set(1'b0), .D(multiplexer_19_out), .C(CPT), .Clr(RST), .Q(SPT));  // open: nQ
  assign driver_8_out = IORQ ? d_ff_as_1_q : 8'bz;  // Driver driver_8
  PullDown #(.Bits(8)) pulldown_3 (.out(driver_8_out));
  Multiplexer #(.Bits(8)) multiplexer_20 (.sel(SIG_CA), .in_0(driver_8_out), .in_1(blockramdualport_1_d), .out(OUT));

  // Notes on the sheet:
  //   EN: ENABLE
  //   IRV: Interrupt request vector
  //   IRQ: ENABLE
  //   IORQ: CPU is requesting data
  //   SPT: Stack Pass-through
  //   CPT: Clock Pass-through
  //   DPT: Direction Pass-through (push/pop)
  //   FPPT: Forward Pop Pass-Through
endmodule
