// Digital circuit incrchiptestboard.dig as structural Verilog
module incrchiptestboard (
  input  MAIN_CLOCK
);

  wire and_1_out, and_2_out, d_ff_as_1_q, dipswitch_9_out, dipswitch_10_out, dipswitch_11_out,
       dipswitch_12_out, dipswitch_13_out, ENABLE_CPU_out, ENABLE_DMA_out, ENABLE_LOAD_out,
       MAIN_CLOCK_ENABLE_out, MANUAL_STEP_out, or_1_out, or_2_out, PAGE_ADDRESS_ovf, pulldown_1_out,
       pulldown_2_out, pulldown_3_out, RESET_out, STORE_2_NVM_out;
  wire [3:0] dipswitch_2_out, dipswitch_3_out, dipswitch_15_out, dipswitch_16_out, incrproto7chipdraft_1_out,
       incrproto7chipdraft_1_out_2;
  wire [7:0] driver_2_out, NVM_BANK_d, PAGE_ADDRESS_out, PAGE_SELECT_q;

  Seven_Seg_Hex seven_seg_hex_1 (.d(dipswitch_2_out), .dp(pulldown_1_out));
  DipSwitch dipswitch_1 (.out(dipswitch_2_out[2]));
  DipSwitch dipswitch_2 (.out(dipswitch_2_out[3]));
  Button MANUAL_STEP (.out(MANUAL_STEP_out));
  DipSwitch MAIN_CLOCK_ENABLE (.out(MAIN_CLOCK_ENABLE_out));
  Button RESET (.out(RESET_out));
  DipSwitch ENABLE_CPU (.out(ENABLE_CPU_out));
  DipSwitch ENABLE_DMA (.out(ENABLE_DMA_out));
  DipSwitch ENABLE_LOAD (.out(ENABLE_LOAD_out));
  Seven_Seg_Hex seven_seg_hex_2 (.d(dipswitch_3_out), .dp(pulldown_1_out));
  DipSwitch dipswitch_3 (.out(dipswitch_3_out[3]));
  DipSwitch dipswitch_4 (.out(dipswitch_2_out[0]));
  DipSwitch dipswitch_5 (.out(dipswitch_2_out[1]));
  and and_1 (and_1_out, MAIN_CLOCK_ENABLE_out, MAIN_CLOCK);
  DipSwitch dipswitch_6 (.out(dipswitch_3_out[0]));
  DipSwitch dipswitch_7 (.out(dipswitch_3_out[1]));
  DipSwitch dipswitch_8 (.out(dipswitch_3_out[2]));
  or or_1 (or_1_out, MANUAL_STEP_out, and_1_out);
  PullDown pulldown_1 (.out(pulldown_1_out));
  DipSwitch dipswitch_9 (.out(dipswitch_9_out));
  DipSwitch dipswitch_10 (.out(dipswitch_10_out));
  or or_2 (or_2_out, dipswitch_10_out, ENABLE_LOAD_out);
  DipSwitch dipswitch_11 (.out(dipswitch_11_out));
  DipSwitch dipswitch_12 (.out(dipswitch_12_out));
  Register #(.Bits(8)) PAGE_SELECT (
    .D({dipswitch_2_out, dipswitch_3_out}), .C(or_1_out), .en(dipswitch_9_out), .Q(PAGE_SELECT_q));
  DipSwitch STORE_2_NVM (.out(STORE_2_NVM_out));
  CounterPreset #(.Bits(8)) PAGE_ADDRESS (
    .en(or_2_out), .C(or_1_out), .dir(dipswitch_11_out), .in({dipswitch_2_out, dipswitch_3_out}),
    .ld(dipswitch_12_out), .clr(RESET_out), .out(PAGE_ADDRESS_out), .ovf(PAGE_ADDRESS_ovf));
  DipSwitch dipswitch_13 (.out(dipswitch_13_out));
  Seven_Seg_Hex seven_seg_hex_3 (.d(dipswitch_15_out), .dp(pulldown_2_out));
  DipSwitch dipswitch_14 (.out(dipswitch_15_out[2]));
  DipSwitch dipswitch_15 (.out(dipswitch_15_out[3]));
  D_FF_AS d_ff_as_1 (
    .Set(dipswitch_13_out), .D(STORE_2_NVM_out), .C(or_1_out), .Clr(PAGE_ADDRESS_ovf), .Q(d_ff_as_1_q));  // open: nQ
  Seven_Seg_Hex seven_seg_hex_4 (.d(dipswitch_16_out), .dp(pulldown_2_out));
  DipSwitch dipswitch_16 (.out(dipswitch_16_out[3]));
  DipSwitch dipswitch_17 (.out(dipswitch_15_out[0]));
  DipSwitch dipswitch_18 (.out(dipswitch_15_out[1]));
  DipSwitch dipswitch_19 (.out(dipswitch_16_out[0]));
  DipSwitch dipswitch_20 (.out(dipswitch_16_out[1]));
  DipSwitch dipswitch_21 (.out(dipswitch_16_out[2]));
  and and_2 (and_2_out, ~or_1_out, d_ff_as_1_q);  // And
  PullDown pulldown_2 (.out(pulldown_2_out));
  incrproto7chipdraft incrproto7chipdraft_1 (
    .IN({dipswitch_15_out, dipswitch_16_out}), .EN(ENABLE_CPU_out), .RST(RESET_out), .CLK(or_1_out),
    .OUT({incrproto7chipdraft_1_out_2, incrproto7chipdraft_1_out}), .DMA_ADDR(PAGE_ADDRESS_out),
    .DMA_DATA(driver_2_out), .DMA_STR(ENABLE_LOAD_out), .SIG_DMA(ENABLE_DMA_out));
  EEPROM #(.AddrBits(16), .Bits(8)) NVM_BANK (
    .A({PAGE_SELECT_q, PAGE_ADDRESS_out}), .CS(ENABLE_DMA_out), .WE(and_2_out), .OE(ENABLE_LOAD_out),
    .D(NVM_BANK_d));
  Seven_Seg_Hex seven_seg_hex_5 (.d(incrproto7chipdraft_1_out_2), .dp(pulldown_3_out));
  assign NVM_BANK_d = d_ff_as_1_q ? {incrproto7chipdraft_1_out_2, incrproto7chipdraft_1_out} : 8'bz;  // Driver driver_1
  assign driver_2_out = ENABLE_LOAD_out ? NVM_BANK_d : 8'bz;  // Driver driver_2
  Seven_Seg_Hex seven_seg_hex_6 (.d(incrproto7chipdraft_1_out), .dp(pulldown_3_out));
  PullDown pulldown_3 (.out(pulldown_3_out));

  // Notes on the sheet:
  //   MAIN_CLOCK: Hz: 100
  //   contents of NVM_BANK (hex, n*v repeats v):
  //   4*1,b,20,19,b,3,20,19,b,3b,b,3b,b,30,14,238*0,5*1,b,20,19,b,3
  //   ,20,19,b,3b,b,3b,b,30,14,232*0,11,4,3,3,e7
endmodule
