// Digital circuit incrproto0.dig as structural Verilog
module incrproto0 (
  input  [7:0] in_1,
  input  clk
);

  wire dipswitch_1_out, dipswitch_2_out, dipswitch_3_out, dipswitch_4_out, dipswitch_5_out, dipswitch_6_out,
       dipswitch_7_out, dipswitch_8_out, dipswitch_9_out;
  wire [7:0] blockramdualport_1_d, MAC_out, MDC_out;

  DipSwitch dipswitch_1 (.out(dipswitch_1_out));
  DipSwitch dipswitch_2 (.out(dipswitch_2_out));
  DipSwitch dipswitch_3 (.out(dipswitch_3_out));
  DipSwitch dipswitch_4 (.out(dipswitch_4_out));
  DipSwitch dipswitch_5 (.out(dipswitch_5_out));
  DipSwitch dipswitch_6 (.out(dipswitch_6_out));
  DipSwitch dipswitch_7 (.out(dipswitch_7_out));
  DipSwitch dipswitch_8 (.out(dipswitch_8_out));
  CounterPreset #(.Bits(8)) MAC (
    .en(dipswitch_1_out), .C(clk), .dir(dipswitch_2_out), .in(in_1), .ld(dipswitch_3_out),
    .clr(dipswitch_4_out), .out(MAC_out));  // open: ovf
  CounterPreset #(.Bits(8)) MDC (
    .en(dipswitch_5_out), .C(clk), .dir(dipswitch_6_out), .in(blockramdualport_1_d), .ld(dipswitch_7_out),
    .clr(dipswitch_8_out), .out(MDC_out));  // open: ovf
  DipSwitch dipswitch_9 (.out(dipswitch_9_out));
  BlockRAMDualPort #(.AddrBits(8), .Bits(8)) blockramdualport_1 (
    .A(MAC_out), .Din(MDC_out), .str(dipswitch_9_out), .C(clk), .D(blockramdualport_1_d));
endmodule
