// Digital circuit incrproto1.dig as structural Verilog
module incrproto1 (
  input  clk
);

  wire dipswitch_5_out, dipswitch_6_out;
  wire [3:0] demultiplexer_1_out_0, demultiplexer_1_out_1, dipswitch_1_out;
  wire [7:0] blockramdualport_1_d, MAC_out, MDC_out;

  DipSwitch dipswitch_1 (.out(dipswitch_1_out[0]));
  DipSwitch dipswitch_2 (.out(dipswitch_1_out[1]));
  DipSwitch dipswitch_3 (.out(dipswitch_1_out[2]));
  DipSwitch dipswitch_4 (.out(dipswitch_1_out[3]));
  DipSwitch dipswitch_5 (.out(dipswitch_5_out));
  DipSwitch dipswitch_6 (.out(dipswitch_6_out));
  DipSwitch dipswitch_7 ();  // open: out
  DipSwitch dipswitch_8 ();  // open: out
  Demultiplexer #(.Bits(4)) demultiplexer_1 (
    .sel(dipswitch_5_out), .in(dipswitch_1_out), .out_0(demultiplexer_1_out_0), .out_1(demultiplexer_1_out_1));
  CounterPreset #(.Bits(8)) MAC (
    .en(demultiplexer_1_out_1[0]), .C(clk), .dir(demultiplexer_1_out_1[1]), .in(blockramdualport_1_d),
    .ld(demultiplexer_1_out_1[2]), .clr(demultiplexer_1_out_1[3]), .out(MAC_out));  // open: ovf
  CounterPreset #(.Bits(8)) MDC (
    .en(demultiplexer_1_out_0[0]), .C(clk), .dir(demultiplexer_1_out_0[1]), .in(blockramdualport_1_d),
    .ld(demultiplexer_1_out_0[2]), .clr(demultiplexer_1_out_0[3]), .out(MDC_out));  // open: ovf
  BlockRAMDualPort #(.AddrBits(8), .Bits(8)) blockramdualport_1 (
    .A(MAC_out), .Din(MDC_out), .str(dipswitch_6_out), .C(clk), .D(blockramdualport_1_d));
endmodule
