// Digital circuit incrproto3.dig as structural Verilog
module incrproto3 (
  input  clk
);

  wire and_1_out, and_2_out, and_3_out, d_ff_as_1_q, d_ff_as_2_q, d_ff_as_3_q, multiplexer_1_out, not_1_out,
       not_2_out, or_2_out, or_3_out, RESET_out;
  wire [2:0] demultiplexer_1_out_0, demultiplexer_1_out_1, demultiplexer_1_out_2, demultiplexer_1_out_3;
  wire [5:0] driver_1_out, or_1_out;
  wire [7:0] blockramdualport_1_d, demultiplexer_2_out_0, demultiplexer_2_out_1, demultiplexer_3_out_0,
       demultiplexer_3_out_1, demultiplexer_3_out_2, demultiplexer_3_out_3, driver_2_out, IOC_out, IR_q,
       MAC_out, MDC_out, multiplexer_2_out, multiplexer_3_out, PC_out, STEP_out;
  wire [7:6] or_1_out_2;

  D_FF_AS d_ff_as_1 (.Set(RESET_out), .D(d_ff_as_3_q), .C(clk), .Clr(1'b0), .Q(d_ff_as_1_q));  // open: nQ
  D_FF_AS d_ff_as_2 (.Set(1'b0), .D(d_ff_as_1_q), .C(clk), .Clr(RESET_out), .Q(d_ff_as_2_q));  // open: nQ
  D_FF_AS d_ff_as_3 (.Set(1'b0), .D(d_ff_as_2_q), .C(clk), .Clr(RESET_out), .Q(d_ff_as_3_q));  // open: nQ
  DipSwitch STEP (.out(STEP_out[0]));
  DipSwitch DIR (.out(STEP_out[1]));
  DipSwitch LOAD (.out(STEP_out[2]));
  DipSwitch R0 (.out(STEP_out[3]));
  DipSwitch R1 (.out(STEP_out[4]));
  DipSwitch STORE (.out(STEP_out[5]));
  DipSwitch ZERO_NZ (.out(STEP_out[6]));
  DipSwitch CONDITIONAL (.out(STEP_out[7]));
  assign {or_1_out_2, or_1_out} = driver_2_out | STEP_out;  // Or or_1, 8 bits wide
  not not_1 (not_1_out, and_2_out);
  Multiplexer multiplexer_1 (.sel(or_1_out_2[6]), .in_0(and_2_out), .in_1(not_1_out), .out(multiplexer_1_out));
  assign driver_1_out = or_2_out ? or_1_out : 6'bz;  // Driver driver_1
  PullDown #(.Bits(6)) pulldown_1 (.out(driver_1_out));
  or or_2 (or_2_out, multiplexer_1_out, ~or_1_out_2[7]);  // Or
  assign driver_2_out = d_ff_as_3_q ? IR_q : 8'bz;  // Driver driver_2
  PullDown #(.Bits(8)) pulldown_2 (.out(driver_2_out));
  LED STP (.in(driver_2_out[0]));
  LED DIR_2 (.in(driver_2_out[1]));
  LED LDC (.in(driver_2_out[2]));
  LED R0_2 (.in(driver_2_out[3]));
  LED R1_2 (.in(driver_2_out[4]));
  LED STR (.in(driver_2_out[5]));
  LED ZNZ (.in(driver_2_out[6]));
  LED CON (.in(driver_2_out[7]));
  DipSwitch RESET (.out(RESET_out));
  Demultiplexer #(.Selector_Bits(2), .Bits(3)) demultiplexer_1 (
    .sel(driver_1_out[4:3]), .in(driver_1_out[2:0]), .out_0(demultiplexer_1_out_0),
    .out_1(demultiplexer_1_out_1), .out_2(demultiplexer_1_out_2), .out_3(demultiplexer_1_out_3));
  or or_3 (or_3_out, d_ff_as_2_q, demultiplexer_1_out_2[0]);
  CounterPreset #(.Bits(8)) IOC (
    .en(demultiplexer_1_out_3[0]), .C(clk), .dir(demultiplexer_1_out_3[1]), .in(demultiplexer_3_out_3),
    .ld(demultiplexer_1_out_3[2]), .clr(RESET_out), .out(IOC_out));  // open: ovf
  CounterPreset #(.Bits(8)) PC (
    .en(or_3_out), .C(clk), .dir(demultiplexer_1_out_2[1]), .in(demultiplexer_3_out_2),
    .ld(demultiplexer_1_out_2[2]), .clr(RESET_out), .out(PC_out));  // open: ovf
  CounterPreset #(.Bits(8)) MAC (
    .en(demultiplexer_1_out_1[0]), .C(clk), .dir(demultiplexer_1_out_1[1]), .in(demultiplexer_3_out_1),
    .ld(demultiplexer_1_out_1[2]), .clr(RESET_out), .out(MAC_out));  // open: ovf
  CounterPreset #(.Bits(8)) MDC (
    .en(demultiplexer_1_out_0[0]), .C(clk), .dir(demultiplexer_1_out_0[1]), .in(demultiplexer_3_out_0),
    .ld(demultiplexer_1_out_0[2]), .clr(RESET_out), .out(MDC_out));  // open: ovf
  Multiplexer #(.Bits(8)) multiplexer_2 (.sel(d_ff_as_1_q), .in_0(MAC_out), .in_1(PC_out), .out(multiplexer_2_out));
  Multiplexer #(.Selector_Bits(2), .Bits(8)) multiplexer_3 (
    .sel(driver_1_out[4:3]), .in_0(MDC_out), .in_1(MAC_out), .in_2(PC_out), .in_3(IOC_out),
    .out(multiplexer_3_out));
  BlockRAMDualPort #(.AddrBits(8), .Bits(8)) blockramdualport_1 (
    .A(multiplexer_2_out), .Din(multiplexer_3_out), .str(driver_1_out[5]), .C(not_2_out),
    .D(blockramdualport_1_d));
  not not_2 (not_2_out, clk);
  Demultiplexer #(.Bits(8)) demultiplexer_2 (
    .sel(d_ff_as_1_q), .in(blockramdualport_1_d), .out_0(demultiplexer_2_out_0), .out_1(demultiplexer_2_out_1));
  Register #(.Bits(8)) IR (.D(demultiplexer_2_out_1), .C(clk), .en(d_ff_as_1_q), .Q(IR_q));
  and and_1 (and_1_out, ~demultiplexer_2_out_0[4], ~demultiplexer_2_out_0[5], ~demultiplexer_2_out_0[6], ~demultiplexer_2_out_0[7]);  // And
  and and_2 (and_2_out, and_3_out, and_1_out);
  LED ZERO (.in(and_2_out));
  Demultiplexer #(.Bits(8), .Selector_Bits(2)) demultiplexer_3 (
    .sel(driver_1_out[4:3]), .in(demultiplexer_2_out_0), .out_0(demultiplexer_3_out_0),
    .out_1(demultiplexer_3_out_1), .out_2(demultiplexer_3_out_2), .out_3(demultiplexer_3_out_3));
  and and_3 (and_3_out, ~demultiplexer_2_out_0[0], ~demultiplexer_2_out_0[1], ~demultiplexer_2_out_0[2], ~demultiplexer_2_out_0[3]);  // And

  // Notes on the sheet:
  //   clk: Hz: 10
endmodule
