// Digital circuit incrproto6dma.dig as structural Verilog
module incrproto6dma (
  input  clk,
  input  [7:0] IN,
  input  [7:0] DMA_DATA,
  input  [7:0] DMA_ADDR,
  input  DMA_STR,
  input  SIG_DMA,
  output [7:0] OUT
);

  wire and_1_out, and_2_out, and_3_out, and_4_out, and_5_out, d_ff_as_1_q, d_ff_as_2_q, d_ff_as_3_q,
       multiplexer_1_out, multiplexer_11_out, not_1_out, not_2_out, or_2_out, or_3_out, RESET_out;
  wire [2:0] demultiplexer_1_out_0, demultiplexer_1_out_1, demultiplexer_1_out_2, demultiplexer_1_out_3;
  wire [5:0] driver_1_out, or_1_out;
  wire [7:0] blockramdualport_1_d, d_ff_as_4_q, d_ff_as_5_q, d_ff_as_6_q, d_ff_as_7_q, d_ff_as_8_q,
       d_ff_as_9_q, d_ff_as_10_q, d_ff_as_11_q, demultiplexer_2_out_0, demultiplexer_2_out_1,
       demultiplexer_3_out_0, demultiplexer_3_out_1, demultiplexer_3_out_2, demultiplexer_3_out_3,
       driver_2_out, driver_3_out, IR_q, MAC_out, MDC_out, multiplexer_2_out, multiplexer_3_out,
       multiplexer_4_out, multiplexer_5_out, multiplexer_6_out, multiplexer_7_out, multiplexer_8_out,
       multiplexer_9_out, multiplexer_10_out, multiplexer_12_out, multiplexer_13_out, multiplexer_14_out,
       multiplexer_15_out, PC_out, STEP_out;
  wire [7:6] or_1_out_2;

  D_FF_AS d_ff_as_1 (.Set(RESET_out), .D(d_ff_as_3_q), .C(and_1_out), .Clr(1'b0), .Q(d_ff_as_1_q));  // open: nQ
  D_FF_AS d_ff_as_2 (.Set(1'b0), .D(d_ff_as_1_q), .C(and_1_out), .Clr(RESET_out), .Q(d_ff_as_2_q));  // open: nQ
  D_FF_AS d_ff_as_3 (.Set(1'b0), .D(d_ff_as_2_q), .C(and_1_out), .Clr(RESET_out), .Q(d_ff_as_3_q));  // open: nQ
  and and_1 (and_1_out, ~SIG_DMA, clk);  // And
  DipSwitch STEP (.out(STEP_out[0]));
  DipSwitch DIR (.out(STEP_out[1]));
  DipSwitch LOAD (.out(STEP_out[2]));
  DipSwitch R0 (.out(STEP_out[3]));
  DipSwitch R1 (.out(STEP_out[4]));
  DipSwitch STORE (.out(STEP_out[5]));
  DipSwitch ZERO_NZ (.out(STEP_out[6]));
  DipSwitch CONDITIONAL (.out(STEP_out[7]));
  assign {or_1_out_2, or_1_out} = driver_2_out | STEP_out;  // Or or_1, 8 bits wide
  not not_1 (not_1_out, and_4_out);
  Multiplexer multiplexer_1 (.sel(or_1_out_2[6]), .in_0(and_4_out), .in_1(not_1_out), .out(multiplexer_1_out));
  assign driver_1_out = or_2_out ? or_1_out : 6'bz;  // Driver driver_1
  PullDown #(.Bits(6)) pulldown_1 (.out(driver_1_out));
  or or_2 (or_2_out, multiplexer_1_out, ~or_1_out_2[7]);  // Or
  assign driver_2_out = d_ff_as_3_q ? IR_q : 8'bz;  // Driver driver_2
  PullDown #(.Bits(8)) pulldown_2 (.out(driver_2_out));
  LED STP (.in(driver_2_out[0]));
  LED DIR_2 (.in(driver_2_out[1]));
  LED LDC (.in(driver_2_out[2]));
  LED R0_2 (.in(driver_2_out[3]));
  LED R1_2 (.in(driver_2_out[4]));
  LED STR (.in(driver_2_out[5]));
  LED ZNZ (.in(driver_2_out[6]));
  LED CON (.in(driver_2_out[7]));
  DipSwitch RESET (.out(RESET_out));
  Demultiplexer #(.Selector_Bits(2), .Bits(3)) demultiplexer_1 (
    .sel(driver_1_out[4:3]), .in(driver_1_out[2:0]), .out_0(demultiplexer_1_out_0),
    .out_1(demultiplexer_1_out_1), .out_2(demultiplexer_1_out_2), .out_3(demultiplexer_1_out_3));
  Multiplexer #(.Bits(8)) multiplexer_2 (
    .sel(demultiplexer_1_out_3[2]), .in_0(demultiplexer_3_out_3), .in_1(IN), .out(multiplexer_2_out));
  and and_2 (and_2_out, demultiplexer_1_out_3[0], ~clk);  // And
  Multiplexer #(.Bits(8)) multiplexer_3 (
    .sel(demultiplexer_1_out_3[1]), .in_0(multiplexer_2_out), .in_1(d_ff_as_5_q), .out(multiplexer_3_out));
  or or_3 (or_3_out, d_ff_as_2_q, demultiplexer_1_out_2[0]);
  D_FF_AS #(.Bits(8)) d_ff_as_4 (
    .Set(1'b0), .D(multiplexer_3_out), .C(and_2_out), .Clr(RESET_out), .Q(d_ff_as_4_q));  // open: nQ
  CounterPreset #(.Bits(8)) PC (
    .en(or_3_out), .C(clk), .dir(demultiplexer_1_out_2[1]), .in(demultiplexer_3_out_2),
    .ld(demultiplexer_1_out_2[2]), .clr(RESET_out), .out(PC_out));  // open: ovf
  CounterPreset #(.Bits(8)) MAC (
    .en(demultiplexer_1_out_1[0]), .C(clk), .dir(demultiplexer_1_out_1[1]), .in(demultiplexer_3_out_1),
    .ld(demultiplexer_1_out_1[2]), .clr(RESET_out), .out(MAC_out));  // open: ovf
  CounterPreset #(.Bits(8)) MDC (
    .en(demultiplexer_1_out_0[0]), .C(clk), .dir(demultiplexer_1_out_0[1]), .in(demultiplexer_3_out_0),
    .ld(demultiplexer_1_out_0[2]), .clr(RESET_out), .out(MDC_out));  // open: ovf
  Multiplexer #(.Bits(8)) multiplexer_4 (
    .sel(demultiplexer_1_out_3[1]), .in_0(d_ff_as_4_q), .in_1(d_ff_as_6_q), .out(multiplexer_4_out));
  D_FF_AS #(.Bits(8)) d_ff_as_5 (
    .Set(1'b0), .D(multiplexer_4_out), .C(and_2_out), .Clr(RESET_out), .Q(d_ff_as_5_q));  // open: nQ
  Multiplexer #(.Bits(8)) multiplexer_5 (
    .sel(demultiplexer_1_out_3[1]), .in_0(d_ff_as_5_q), .in_1(d_ff_as_7_q), .out(multiplexer_5_out));
  Multiplexer #(.Bits(8)) multiplexer_6 (.sel(d_ff_as_1_q), .in_0(MAC_out), .in_1(PC_out), .out(multiplexer_6_out));
  Multiplexer #(.Selector_Bits(2), .Bits(8)) multiplexer_7 (
    .sel(driver_1_out[4:3]), .in_0(MDC_out), .in_1(MAC_out), .in_2(PC_out), .in_3(d_ff_as_4_q),
    .out(multiplexer_7_out));
  D_FF_AS #(.Bits(8)) d_ff_as_6 (
    .Set(1'b0), .D(multiplexer_5_out), .C(and_2_out), .Clr(RESET_out), .Q(d_ff_as_6_q));  // open: nQ
  Multiplexer #(.Bits(8)) multiplexer_8 (
    .sel(demultiplexer_1_out_3[1]), .in_0(d_ff_as_6_q), .in_1(d_ff_as_10_q), .out(multiplexer_8_out));
  Multiplexer #(.Bits(8)) multiplexer_9 (
    .sel(SIG_DMA), .in_0(multiplexer_6_out), .in_1(DMA_ADDR), .out(multiplexer_9_out));
  Multiplexer #(.Bits(8)) multiplexer_10 (
    .sel(SIG_DMA), .in_0(multiplexer_7_out), .in_1(DMA_DATA), .out(multiplexer_10_out));
  not not_2 (not_2_out, clk);
  D_FF_AS #(.Bits(8)) d_ff_as_7 (
    .Set(1'b0), .D(multiplexer_8_out), .C(and_2_out), .Clr(RESET_out), .Q(d_ff_as_7_q));  // open: nQ
  Multiplexer multiplexer_11 (.sel(SIG_DMA), .in_0(driver_1_out[5]), .in_1(DMA_STR), .out(multiplexer_11_out));
  BlockRAMDualPort #(.AddrBits(8), .Bits(8)) blockramdualport_1 (
    .A(multiplexer_9_out), .Din(multiplexer_10_out), .str(multiplexer_11_out), .C(not_2_out),
    .D(blockramdualport_1_d));
  Multiplexer #(.Bits(8)) multiplexer_12 (
    .sel(demultiplexer_1_out_3[1]), .in_0(d_ff_as_7_q), .in_1(d_ff_as_9_q), .out(multiplexer_12_out));
  Demultiplexer #(.Bits(8)) demultiplexer_2 (
    .sel(d_ff_as_1_q), .in(blockramdualport_1_d), .out_0(demultiplexer_2_out_0), .out_1(demultiplexer_2_out_1));
  D_FF_AS #(.Bits(8)) d_ff_as_8 (
    .Set(1'b0), .D(multiplexer_12_out), .C(and_2_out), .Clr(RESET_out), .Q(d_ff_as_8_q));  // open: nQ
  Multiplexer #(.Bits(8)) multiplexer_13 (
    .sel(demultiplexer_1_out_3[1]), .in_0(d_ff_as_8_q), .in_1(d_ff_as_10_q), .out(multiplexer_13_out));
  Register #(.Bits(8)) IR (.D(demultiplexer_2_out_1), .C(clk), .en(d_ff_as_1_q), .Q(IR_q));
  and and_3 (and_3_out, ~demultiplexer_2_out_0[4], ~demultiplexer_2_out_0[5], ~demultiplexer_2_out_0[6], ~demultiplexer_2_out_0[7]);  // And
  and and_4 (and_4_out, and_5_out, and_3_out);
  LED ZERO (.in(and_4_out));
  Demultiplexer #(.Bits(8), .Selector_Bits(2)) demultiplexer_3 (
    .sel(driver_1_out[4:3]), .in(demultiplexer_2_out_0), .out_0(demultiplexer_3_out_0),
    .out_1(demultiplexer_3_out_1), .out_2(demultiplexer_3_out_2), .out_3(demultiplexer_3_out_3));
  and and_5 (and_5_out, ~demultiplexer_2_out_0[0], ~demultiplexer_2_out_0[1], ~demultiplexer_2_out_0[2], ~demultiplexer_2_out_0[3]);  // And
  D_FF_AS #(.Bits(8)) d_ff_as_9 (
    .Set(1'b0), .D(multiplexer_13_out), .C(and_2_out), .Clr(RESET_out), .Q(d_ff_as_9_q));  // open: nQ
  Multiplexer #(.Bits(8)) multiplexer_14 (
    .sel(demultiplexer_1_out_3[1]), .in_0(d_ff_as_9_q), .in_1(d_ff_as_11_q), .out(multiplexer_14_out));
  D_FF_AS #(.Bits(8)) d_ff_as_10 (
    .Set(1'b0), .D(multiplexer_14_out), .C(and_2_out), .Clr(RESET_out), .Q(d_ff_as_10_q));  // open: nQ
  Multiplexer #(.Bits(8)) multiplexer_15 (
    .sel(demultiplexer_1_out_3[1]), .in_0(d_ff_as_10_q), .in_1({8{1'b0}}), .out(multiplexer_15_out));
  D_FF_AS #(.Bits(8)) d_ff_as_11 (
    .Set(1'b0), .D(multiplexer_15_out), .C(and_2_out), .Clr(RESET_out), .Q(d_ff_as_11_q));  // open: nQ
  assign driver_3_out = demultiplexer_1_out_3[2] ? d_ff_as_11_q : 8'bz;  // Driver driver_3
  PullDown #(.Bits(8)) pulldown_3 (.out(driver_3_out));
  Multiplexer #(.Bits(8)) multiplexer_16 (.sel(SIG_DMA), .in_0(driver_3_out), .in_1(blockramdualport_1_d), .out(OUT));

  // Notes on the sheet:
  //   clk: Hz: 10
endmodule
