// Digital circuit ledmattest.dig as structural Verilog
module ledmattest (
  input  [15:0] D,
  input  [15:0] A,
  input  clk,
  output [15:0] OUT
);

  wire and_1_out, CLOCK_ENABLE_out, dipswitch_1_out, dipswitch_2_out, LOAD_out, or_1_out, RESET_COUNTER_out,
       SCR_ENABLE_out, SCRCD_out, STEP_out;
  wire [5:0] counterpreset_1_out;
  wire [15:0] ramdualaccess_1_d2;

  Button STEP (.out(STEP_out));
  DipSwitch CLOCK_ENABLE (.out(CLOCK_ENABLE_out));
  and and_1 (and_1_out, CLOCK_ENABLE_out, clk);
  DipSwitch SCR_ENABLE (.out(SCR_ENABLE_out));
  DipSwitch SCRCD (.out(SCRCD_out));
  DipSwitch LOAD (.out(LOAD_out));
  DipSwitch RESET_COUNTER (.out(RESET_COUNTER_out));
  or or_1 (or_1_out, STEP_out, and_1_out);
  CounterPreset #(.Bits(6)) counterpreset_1 (
    .en(SCR_ENABLE_out), .C(or_1_out), .dir(SCRCD_out), .in({6{1'b0}}), .ld(LOAD_out),
    .clr(RESET_COUNTER_out), .out(counterpreset_1_out));  // open: ovf
  RAMDualAccess #(.AddrBits(16), .Bits(16)) ramdualaccess_1 (
    .str(dipswitch_1_out), .C(or_1_out), .ld(dipswitch_2_out), .A1(A), .Din1(D),
    .A2({10'h4, counterpreset_1_out}), .D1(OUT), .D2(ramdualaccess_1_d2));
  DipSwitch dipswitch_1 (.out(dipswitch_1_out));
  DipSwitch dipswitch_2 (.out(dipswitch_2_out));
  LedMatrix #(.colAddrBits(6), .ledPersistence("true"), .rowDataBits(16)) ledmatrix_1 (
    .rows(ramdualaccess_1_d2), .column(counterpreset_1_out));

  // Notes on the sheet:
  //   clk: Hz: 5000
endmodule
