// Digital circuit od8x8bsrf.dig as structural Verilog
// 8 cell serial organized register file, think a shift register but 8 of them in parallel
module od8x8bsrf (
  input  EN,
  input  CLK,
  input  DIR,
  input  RST,
  input  [7:0] SRI,
  input  LOOP,
  output [7:0] SRO,
  output [7:0] TOP
);

  wire and_1_out;
  wire [7:0] driver_1_out, multiplexer_1_out, multiplexer_2_out, multiplexer_3_out, multiplexer_4_out,
       multiplexer_5_out, multiplexer_6_out, multiplexer_7_out, multiplexer_8_out, SR1_q, SR2_q, SR3_q,
       SR4_q, SR5_q, SR6_q;

  and and_1 (and_1_out, EN, CLK);
  Multiplexer #(.Bits(8)) multiplexer_1 (.sel(DIR), .in_0(SRI), .in_1(SR1_q), .out(multiplexer_1_out));
  D_FF_AS #(.Bits(8)) SR0 (.Set(1'b0), .D(multiplexer_1_out), .C(and_1_out), .Clr(RST), .Q(TOP));  // open: nQ
  assign driver_1_out = LOOP ? TOP : 8'bz;  // Driver driver_1
  Multiplexer #(.Bits(8)) multiplexer_2 (.sel(DIR), .in_0(TOP), .in_1(SR2_q), .out(multiplexer_2_out));
  D_FF_AS #(.Bits(8)) SR1 (.Set(1'b0), .D(multiplexer_2_out), .C(and_1_out), .Clr(RST), .Q(SR1_q));  // open: nQ
  Multiplexer #(.Bits(8)) multiplexer_3 (.sel(DIR), .in_0(SR1_q), .in_1(SR3_q), .out(multiplexer_3_out));
  D_FF_AS #(.Bits(8)) SR2 (.Set(1'b0), .D(multiplexer_3_out), .C(and_1_out), .Clr(RST), .Q(SR2_q));  // open: nQ
  Multiplexer #(.Bits(8)) multiplexer_4 (.sel(DIR), .in_0(SR2_q), .in_1(SR4_q), .out(multiplexer_4_out));
  D_FF_AS #(.Bits(8)) SR3 (.Set(1'b0), .D(multiplexer_4_out), .C(and_1_out), .Clr(RST), .Q(SR3_q));  // open: nQ
  PullDown #(.Bits(8)) pulldown_1 (.out(driver_1_out));
  Multiplexer #(.Bits(8)) multiplexer_5 (.sel(DIR), .in_0(SR3_q), .in_1(SR5_q), .out(multiplexer_5_out));
  D_FF_AS #(.Bits(8)) SR4 (.Set(1'b0), .D(multiplexer_5_out), .C(and_1_out), .Clr(RST), .Q(SR4_q));  // open: nQ
  Multiplexer #(.Bits(8)) multiplexer_6 (.sel(DIR), .in_0(SR4_q), .in_1(SR6_q), .out(multiplexer_6_out));
  D_FF_AS #(.Bits(8)) SR5 (.Set(1'b0), .D(multiplexer_6_out), .C(and_1_out), .Clr(RST), .Q(SR5_q));  // open: nQ
  Multiplexer #(.Bits(8)) multiplexer_7 (.sel(DIR), .in_0(SR5_q), .in_1(SRO), .out(multiplexer_7_out));
  D_FF_AS #(.Bits(8)) SR6 (.Set(1'b0), .D(multiplexer_7_out), .C(and_1_out), .Clr(RST), .Q(SR6_q));  // open: nQ
  Multiplexer #(.Bits(8)) multiplexer_8 (.sel(DIR), .in_0(SR6_q), .in_1(driver_1_out), .out(multiplexer_8_out));
  D_FF_AS #(.Bits(8)) SR7 (.Set(1'b0), .D(multiplexer_8_out), .C(and_1_out), .Clr(RST), .Q(SRO));  // open: nQ

  // Notes on the sheet:
  //   SRI: Serial Input
  //   LOOP: Serial Input
  //   SRO: Serial Output
  //   TOP: SR0 OUTPUT
endmodule
