// Digital circuit stackerproto0.dig as structural Verilog
module stackerproto0 (
  input  clk
);

  wire ALU_ALT_out, CARRY_q, dipswitch_3_out, dipswitch_4_out, dipswitch_5_out, dipswitch_6_out,
       dipswitch_7_out, dipswitch_8_out, REGX_ENABLE_out, SIG_RESET_out, ssalu8_1_co, ssalu8_1_n, ssalu8_1_z,
       STK_INPUT_out, \STK_LOOÅ_out , STK_PSHPOP_out, STK_STORE_out;
  wire [1:0] ALU_OP0_out;
  wire [7:0] creg8_1_q, multiplexer_1_out, od8x8bsrf_1_sro, od8x8bsrf_1_top, ssalu8_1_y, STK_IN0_out;

  DipSwitch STK_PSHPOP (.out(STK_PSHPOP_out));
  DipSwitch STK_STORE (.out(STK_STORE_out));
  DipSwitch SIG_RESET (.out(SIG_RESET_out));
  DipSwitch \STK_LOOÅ  (.out(\STK_LOOÅ_out ));
  DipSwitch STK_INPUT (.out(STK_INPUT_out));
  DipSwitch dipswitch_1 ();  // open: out
  DipSwitch dipswitch_2 ();  // open: out
  DipSwitch STK_IN0 (.out(STK_IN0_out[0]));
  DipSwitch STK_IN1 (.out(STK_IN0_out[1]));
  DipSwitch STK_IN2 (.out(STK_IN0_out[2]));
  DipSwitch STK_IN3 (.out(STK_IN0_out[3]));
  DipSwitch STK_IN4 (.out(STK_IN0_out[4]));
  DipSwitch STK_IN5 (.out(STK_IN0_out[5]));
  DipSwitch STK_IN6 (.out(STK_IN0_out[6]));
  DipSwitch STK_IN7 (.out(STK_IN0_out[7]));
  DipSwitch ALU_OP0 (.out(ALU_OP0_out[0]));
  DipSwitch ALU_OP1 (.out(ALU_OP0_out[1]));
  DipSwitch ALU_ALT (.out(ALU_ALT_out));
  DipSwitch REGX_ENABLE (.out(REGX_ENABLE_out));
  Seven_Seg_Hex seven_seg_hex_1 (.d(multiplexer_1_out[7:4]), .dp(1'b0));
  CREG8 creg8_1 (.D(od8x8bsrf_1_top), .R(SIG_RESET_out), .CLK(clk), .EN(REGX_ENABLE_out), .Q(creg8_1_q));
  Seven_Seg_Hex seven_seg_hex_2 (.d(multiplexer_1_out[3:0]), .dp(1'b0));
  Multiplexer #(.Bits(8)) multiplexer_1 (
    .sel(STK_INPUT_out), .in_0(ssalu8_1_y), .in_1(STK_IN0_out), .out(multiplexer_1_out));
  od8x8bsrf od8x8bsrf_1 (
    .SRI(multiplexer_1_out), .DIR(STK_PSHPOP_out), .EN(STK_STORE_out), .CLK(clk), .RST(SIG_RESET_out),
    .LOOP(\STK_LOOÅ_out ), .SRO(od8x8bsrf_1_sro), .TOP(od8x8bsrf_1_top));
  SSALU8 ssalu8_1 (
    .A(od8x8bsrf_1_top), .X(creg8_1_q), .OP(ALU_OP0_out), .ALT(ALU_ALT_out), .CO(ssalu8_1_co), .CIN(CARRY_q),
    .Y(ssalu8_1_y), .Z(ssalu8_1_z), .N(ssalu8_1_n));
  Seven_Seg_Hex seven_seg_hex_3 (.d(od8x8bsrf_1_top[7:4]), .dp(1'b0));
  Seven_Seg_Hex seven_seg_hex_4 (.d(od8x8bsrf_1_top[3:0]), .dp(1'b0));
  D_FF_AS CARRY (.Set(dipswitch_3_out), .D(ssalu8_1_co), .C(clk), .Clr(dipswitch_4_out), .Q(CARRY_q));  // open: nQ
  DipSwitch dipswitch_3 (.out(dipswitch_3_out));
  DipSwitch dipswitch_4 (.out(dipswitch_4_out));
  D_FF_AS ZERO (.Set(dipswitch_5_out), .D(ssalu8_1_z), .C(clk), .Clr(dipswitch_6_out));  // open: Q, nQ
  DipSwitch dipswitch_5 (.out(dipswitch_5_out));
  DipSwitch dipswitch_6 (.out(dipswitch_6_out));
  D_FF_AS NEGATIVE (.Set(dipswitch_7_out), .D(ssalu8_1_n), .C(clk), .Clr(dipswitch_8_out));  // open: Q, nQ
  DipSwitch dipswitch_7 (.out(dipswitch_7_out));
  DipSwitch dipswitch_8 (.out(dipswitch_8_out));
  Seven_Seg_Hex seven_seg_hex_5 (.d(od8x8bsrf_1_sro[7:4]), .dp(1'b0));
  Seven_Seg_Hex seven_seg_hex_6 (.d(od8x8bsrf_1_sro[3:0]), .dp(1'b0));

  // Notes on the sheet:
  //   clk: Hz: 2
endmodule
