// Digital circuit stackerproto1.dig as structural Verilog
module stackerproto1 (
  input  clk,
  output [7:0] A,
  output [7:0] OUTPUT
);

  wire ADDR_A, ALUALT, ALUO0, ALUO1, AOUT, CARRY_q, DECODE, DIPIN, dipswitch_1_out, dipswitch_2_out,
       dipswitch_3_out, dipswitch_4_out, dipswitch_5_out, dipswitch_6_out, FETCH, JUMP, LEDOUT, MEMRD,
       MEMWRT, PCINC, RAE, RXE, SIG_RESET, ssalu8_1_co, ssalu8_1_n, ssalu8_1_z, STKDIR, STKEN, STKIN, TOP,
       XOUT;
  wire [7:0] A_q, blockramdualport_1_d, driver_2_out, driver_5_out, driver_7_out, driver_10_out,
       driver_12_out, IR_q, IROUT, multiplexer_1_out, od8x8bsrf_1_sro, od8x8bsrf_1_top, PC_out,
       pulldown_1_out, ssalu8_1_y, STK_IN0_out, X_q;

  DipSwitch u_SIG_RESET (.out(SIG_RESET));
  PullDown #(.Bits(8)) pulldown_1 (.out(pulldown_1_out));
  Seven_Seg_Hex seven_seg_hex_1 (.d(multiplexer_1_out[7:4]), .dp(1'b0));
  CREG8 X (.D(pulldown_1_out), .R(SIG_RESET), .CLK(clk), .EN(RXE), .Q(X_q));
  Seven_Seg_Hex seven_seg_hex_2 (.d(multiplexer_1_out[3:0]), .dp(1'b0));
  assign pulldown_1_out = RXE ? driver_2_out : 8'bz;  // Driver driver_1
  Multiplexer #(.Bits(8)) multiplexer_1 (.sel(STKIN), .in_0(ssalu8_1_y), .in_1(driver_2_out), .out(multiplexer_1_out));
  od8x8bsrf od8x8bsrf_1 (
    .SRI(multiplexer_1_out), .DIR(STKDIR), .EN(STKEN), .CLK(clk), .RST(SIG_RESET), .LOOP(1'b0),
    .SRO(od8x8bsrf_1_sro), .TOP(od8x8bsrf_1_top));
  SSALU8 ssalu8_1 (
    .A(od8x8bsrf_1_top), .X(X_q), .OP({ALUO1, ALUO0}), .ALT(ALUALT), .CO(ssalu8_1_co), .CIN(CARRY_q),
    .Y(ssalu8_1_y), .Z(ssalu8_1_z), .N(ssalu8_1_n));
  assign driver_2_out = XOUT ? X_q : 8'bz;  // Driver driver_2
  Seven_Seg_Hex seven_seg_hex_3 (.d(od8x8bsrf_1_top[7:4]), .dp(1'b0));
  Seven_Seg_Hex seven_seg_hex_4 (.d(od8x8bsrf_1_top[3:0]), .dp(1'b0));
  D_FF_AS CARRY (.Set(dipswitch_1_out), .D(ssalu8_1_co), .C(clk), .Clr(dipswitch_2_out), .Q(CARRY_q));  // open: nQ
  DipSwitch dipswitch_1 (.out(dipswitch_1_out));
  DipSwitch dipswitch_2 (.out(dipswitch_2_out));
  D_FF_AS ZERO (.Set(dipswitch_3_out), .D(ssalu8_1_z), .C(clk), .Clr(dipswitch_4_out));  // open: Q, nQ
  DipSwitch dipswitch_3 (.out(dipswitch_3_out));
  DipSwitch dipswitch_4 (.out(dipswitch_4_out));
  D_FF_AS NEGATIVE (.Set(dipswitch_5_out), .D(ssalu8_1_n), .C(clk), .Clr(dipswitch_6_out));  // open: Q, nQ
  DipSwitch dipswitch_5 (.out(dipswitch_5_out));
  DipSwitch dipswitch_6 (.out(dipswitch_6_out));
  assign driver_2_out = TOP ? od8x8bsrf_1_top : 8'bz;  // Driver driver_3
  PullDown #(.Bits(8)) pulldown_2 (.out(driver_2_out));
  Seven_Seg_Hex seven_seg_hex_5 (.d(od8x8bsrf_1_sro[7:4]), .dp(1'b0));
  Seven_Seg_Hex seven_seg_hex_6 (.d(od8x8bsrf_1_sro[3:0]), .dp(1'b0));
  assign driver_2_out = AOUT ? A_q : 8'bz;  // Driver driver_4
  assign driver_5_out = RAE ? driver_2_out : 8'bz;  // Driver driver_5
  assign driver_2_out = MEMRD ? blockramdualport_1_d : 8'bz;  // Driver driver_6
  assign driver_7_out = MEMWRT ? driver_2_out : 8'bz;  // Driver driver_7
  DipSwitch STK_IN0 (.out(STK_IN0_out[0]));
  DipSwitch STK_IN1 (.out(STK_IN0_out[1]));
  DipSwitch STK_IN2 (.out(STK_IN0_out[2]));
  DipSwitch STK_IN3 (.out(STK_IN0_out[3]));
  DipSwitch STK_IN4 (.out(STK_IN0_out[4]));
  DipSwitch STK_IN5 (.out(STK_IN0_out[5]));
  DipSwitch STK_IN6 (.out(STK_IN0_out[6]));
  DipSwitch STK_IN7 (.out(STK_IN0_out[7]));
  DipSwitch STK_PSHPOP (.out(STKDIR));
  DipSwitch STK_EN (.out(STKEN));
  DipSwitch STK_INPUT (.out(STKIN));
  DipSwitch MEM_RD (.out(MEMRD));
  DipSwitch MEM_WRT (.out(MEMWRT));
  DipSwitch ALU_OP0 (.out(ALUO0));
  DipSwitch ALU_OP1 (.out(ALUO1));
  DipSwitch ALU_ALT (.out(ALUALT));
  DipSwitch TOP_OUT (.out(TOP));
  DipSwitch u_XOUT (.out(XOUT));
  DipSwitch REGX_ENABLE (.out(RXE));
  DipSwitch u_AOUT (.out(AOUT));
  DipSwitch REGA_ENABLE (.out(RAE));
  DipSwitch DIP_IN (.out(DIPIN));
  DipSwitch LED_OUT (.out(LEDOUT));
  DipSwitch u_ADDR_A (.out(ADDR_A));
  DipSwitch dipswitch_7 (.out(PCINC));
  DipSwitch dipswitch_8 (.out(FETCH));
  DipSwitch dipswitch_9 (.out(JUMP));
  DipSwitch dipswitch_10 (.out(DECODE));
  CREG8 u_A (.D(driver_5_out), .R(SIG_RESET), .CLK(clk), .EN(RAE), .Q(A_q));
  assign driver_2_out = DIPIN ? STK_IN0_out : 8'bz;  // Driver driver_8
  assign OUTPUT = LEDOUT ? driver_2_out : 8'bz;  // Driver driver_9
  LED led_1 (.in(IROUT[0]));
  LED led_2 (.in(IROUT[1]));
  LED led_3 (.in(IROUT[2]));
  LED led_4 (.in(IROUT[3]));
  LED led_5 (.in(IROUT[4]));
  LED led_6 (.in(IROUT[5]));
  LED led_7 (.in(IROUT[6]));
  LED led_8 (.in(IROUT[7]));
  assign driver_10_out = JUMP ? driver_2_out : 8'bz;  // Driver driver_10
  assign A = ADDR_A ? A_q : 8'bz;  // Driver driver_11
  assign driver_12_out = FETCH ? driver_2_out : 8'bz;  // Driver driver_12
  CounterPreset #(.Bits(8), .maxValue(8)) PC (
    .en(PCINC), .C(clk), .dir(1'b0), .in(driver_10_out), .ld(JUMP), .clr(SIG_RESET), .out(PC_out));  // open: ovf
  CREG8 IR (.D(driver_12_out), .R(SIG_RESET), .CLK(clk), .EN(FETCH), .Q(IR_q));
  assign A = FETCH ? PC_out : 8'bz;  // Driver driver_13
  assign IROUT = DECODE ? IR_q : 8'bz;  // Driver driver_14
  BlockRAMDualPort #(.AddrBits(8), .Bits(8)) blockramdualport_1 (
    .A(A), .Din(driver_7_out), .str(MEMWRT), .C(clk), .D(blockramdualport_1_d));

  // Other names for the same wires on the sheet: SIG_CLOCK = clk

  // Notes on the sheet:
  //   clk: Hz: 2
endmodule
