// Digital circuit stackerproto2.dig as structural Verilog
module stackerproto2 (
  input  clk,
  output [7:0] A,
  output [7:0] OUTPUT
);

  wire ADDR_A, ALUALT, ALUO0, ALUO1, and_1_out, and_2_out, and_3_out, and_4_out, and_7_out, AOUT,
       button_1_out, CARRY_q, d_ff_as_3_q, DECODE, decoder_1_out_3, decoder_2_out_3, DIPIN, dipswitch_1_out,
       dipswitch_2_out, dipswitch_3_out, dipswitch_4_out, ENABLE_CLK_out, FETCH, JUMP, LEDOUT, MEMRD, MEMWRT,
       or_2_out, PCINC, RAE, RXE, SIG_CLOCK, SIG_EXEC, SIG_RESET, ssalu8_1_co, ssalu8_1_n, ssalu8_1_z,
       SSALUBUS, STKDIR, STKEN, TOP, XOUT, ZERO_q;
  wire [3:0] demultiplexer_2_out_0;
  wire [6:0] driver_13_out;
  wire [7:0] A_q, blockramdualport_1_d, driver_2_out, driver_5_out, driver_7_out, driver_10_out,
       driver_12_out, IR_q, IROUT, multiplexer_1_out, od8x8bsrf_1_sro, od8x8bsrf_1_top, PC_out,
       pulldown_1_out, ssalu8_1_y, STK_IN0_out, X_q;

  Button button_1 (.out(button_1_out));
  DipSwitch ENABLE_CLK (.out(ENABLE_CLK_out));
  DipSwitch RESET (.out(SIG_RESET));
  DipSwitch ENABLE_CPU (.out(SIG_EXEC));
  and and_1 (and_1_out, ENABLE_CLK_out, clk);
  or or_1 (SIG_CLOCK, button_1_out, and_1_out);
  PullDown #(.Bits(8)) pulldown_1 (.out(pulldown_1_out));
  Seven_Seg_Hex seven_seg_hex_1 (.d(multiplexer_1_out[7:4]), .dp(1'b0));
  CREG8 X (.D(pulldown_1_out), .R(SIG_RESET), .CLK(SIG_CLOCK), .EN(RXE), .Q(X_q));
  Seven_Seg_Hex seven_seg_hex_2 (.d(multiplexer_1_out[3:0]), .dp(1'b0));
  assign pulldown_1_out = RXE ? driver_2_out : 8'bz;  // Driver driver_1
  Multiplexer #(.Bits(8)) multiplexer_1 (
    .sel(SSALUBUS), .in_0(driver_2_out), .in_1(ssalu8_1_y), .out(multiplexer_1_out));
  od8x8bsrf od8x8bsrf_1 (
    .SRI(multiplexer_1_out), .DIR(STKDIR), .EN(STKEN), .CLK(SIG_CLOCK), .RST(SIG_RESET), .LOOP(1'b0),
    .SRO(od8x8bsrf_1_sro), .TOP(od8x8bsrf_1_top));
  SSALU8 ssalu8_1 (
    .A(od8x8bsrf_1_top), .X(X_q), .OP({ALUO1, ALUO0}), .ALT(ALUALT), .CO(ssalu8_1_co), .CIN(CARRY_q),
    .Y(ssalu8_1_y), .Z(ssalu8_1_z), .N(ssalu8_1_n));
  assign driver_2_out = XOUT ? X_q : 8'bz;  // Driver driver_2
  Seven_Seg_Hex seven_seg_hex_3 (.d(od8x8bsrf_1_top[7:4]), .dp(1'b0));
  Seven_Seg_Hex seven_seg_hex_4 (.d(od8x8bsrf_1_top[3:0]), .dp(1'b0));
  D_FF_AS CARRY (
    .Set(dipswitch_1_out), .D(ssalu8_1_co), .C(SIG_CLOCK), .Clr(dipswitch_2_out), .Q(CARRY_q));  // open: nQ
  DipSwitch dipswitch_1 (.out(dipswitch_1_out));
  DipSwitch dipswitch_2 (.out(dipswitch_2_out));
  D_FF_AS ZERO (.Set(dipswitch_3_out), .D(ssalu8_1_z), .C(SIG_CLOCK), .Clr(dipswitch_4_out), .Q(ZERO_q));  // open: nQ
  DipSwitch dipswitch_3 (.out(dipswitch_3_out));
  DipSwitch dipswitch_4 (.out(dipswitch_4_out));
  assign driver_2_out = TOP ? od8x8bsrf_1_top : 8'bz;  // Driver driver_3
  PullDown #(.Bits(8)) pulldown_2 (.out(driver_2_out));
  Seven_Seg_Hex seven_seg_hex_5 (.d(od8x8bsrf_1_sro[7:4]), .dp(1'b0));
  Seven_Seg_Hex seven_seg_hex_6 (.d(od8x8bsrf_1_sro[3:0]), .dp(1'b0));
  assign driver_2_out = AOUT ? A_q : 8'bz;  // Driver driver_4
  assign driver_5_out = RAE ? driver_2_out : 8'bz;  // Driver driver_5
  assign driver_2_out = MEMRD ? blockramdualport_1_d : 8'bz;  // Driver driver_6
  assign driver_7_out = MEMWRT ? driver_2_out : 8'bz;  // Driver driver_7
  DipSwitch STK_IN0 (.out(STK_IN0_out[0]));
  DipSwitch STK_IN1 (.out(STK_IN0_out[1]));
  DipSwitch STK_IN2 (.out(STK_IN0_out[2]));
  DipSwitch STK_IN3 (.out(STK_IN0_out[3]));
  DipSwitch STK_IN4 (.out(STK_IN0_out[4]));
  DipSwitch STK_IN5 (.out(STK_IN0_out[5]));
  DipSwitch STK_IN6 (.out(STK_IN0_out[6]));
  DipSwitch STK_IN7 (.out(STK_IN0_out[7]));
  DipSwitch STK_PSHPOP ();  // open: out
  DipSwitch STK_EN ();  // open: out
  DipSwitch STK_INPUT ();  // open: out
  DipSwitch MEM_RD ();  // open: out
  DipSwitch MEM_WRT ();  // open: out
  DipSwitch ALU_OP0 ();  // open: out
  DipSwitch ALU_OP1 ();  // open: out
  DipSwitch ALU_ALT ();  // open: out
  DipSwitch TOP_OUT ();  // open: out
  DipSwitch u_XOUT ();  // open: out
  DipSwitch REGX_ENABLE ();  // open: out
  DipSwitch u_AOUT ();  // open: out
  DipSwitch REGA_ENABLE ();  // open: out
  DipSwitch DIP_IN ();  // open: out
  DipSwitch LED_OUT ();  // open: out
  DipSwitch u_ADDR_A ();  // open: out
  CREG8 u_A (.D(driver_5_out), .R(SIG_RESET), .CLK(SIG_CLOCK), .EN(RAE), .Q(A_q));
  assign driver_2_out = DIPIN ? STK_IN0_out : 8'bz;  // Driver driver_8
  assign OUTPUT = LEDOUT ? driver_2_out : 8'bz;  // Driver driver_9
  LED led_1 (.in(IROUT[0]));
  LED led_2 (.in(IROUT[1]));
  LED led_3 (.in(IROUT[2]));
  LED led_4 (.in(IROUT[3]));
  LED led_5 (.in(IROUT[4]));
  LED led_6 (.in(IROUT[5]));
  LED led_7 (.in(IROUT[6]));
  LED led_8 (.in(IROUT[7]));
  and and_2 (and_2_out, IROUT[7], d_ff_as_3_q, ZERO_q);
  assign driver_10_out = JUMP ? driver_2_out : 8'bz;  // Driver driver_10
  assign A = ADDR_A ? A_q : 8'bz;  // Driver driver_11
  assign driver_12_out = FETCH ? driver_2_out : 8'bz;  // Driver driver_12
  assign driver_13_out = and_3_out ? IROUT[6:0] : 7'bz;  // Driver driver_13
  and and_3 (and_3_out, or_2_out, d_ff_as_3_q);
  or or_2 (or_2_out, ~IROUT[7], and_2_out);  // Or
  CounterPreset #(.Bits(8), .maxValue(8)) PC (
    .en(PCINC), .C(SIG_CLOCK), .dir(1'b0), .in(driver_10_out), .ld(JUMP), .clr(SIG_RESET), .out(PC_out));  // open: ovf
  CREG8 IR (.D(driver_12_out), .R(SIG_RESET), .CLK(SIG_CLOCK), .EN(FETCH), .Q(IR_q));
  PullDown #(.Bits(7)) pulldown_3 (.out(driver_13_out));
  assign A = FETCH ? PC_out : 8'bz;  // Driver driver_14
  assign IROUT = DECODE ? IR_q : 8'bz;  // Driver driver_15
  PullDown #(.Bits(8)) pulldown_4 (.out(A));
  Demultiplexer #(.Bits(2)) demultiplexer_1 (
    .sel(driver_13_out[6]), .in(driver_13_out[5:4]), .out_0({LEDOUT, DIPIN}), .out_1({STKEN, STKDIR}));
  BlockRAMDualPort #(.AddrBits(8), .Bits(8)) blockramdualport_1 (
    .A(A), .Din(driver_7_out), .str(MEMWRT), .C(SIG_CLOCK), .D(blockramdualport_1_d));
  PullDown #(.Bits(8)) pulldown_5 (.out(IROUT));
  LED led_9 (.in(OUTPUT[0]));
  LED led_10 (.in(OUTPUT[1]));
  LED led_11 (.in(OUTPUT[2]));
  LED led_12 (.in(OUTPUT[3]));
  LED led_13 (.in(OUTPUT[4]));
  LED led_14 (.in(OUTPUT[5]));
  LED led_15 (.in(OUTPUT[6]));
  LED led_16 (.in(OUTPUT[7]));
  and and_4 (and_4_out, SIG_CLOCK, SIG_EXEC);
  Demultiplexer #(.Bits(4)) demultiplexer_2 (
    .sel(driver_13_out[6]), .in(driver_13_out[3:0]), .out_0(demultiplexer_2_out_0),
    .out_1({ALUALT, ALUO1, ALUO0, SSALUBUS}));
  D_FF_AS d_ff_as_1 (.Set(SIG_RESET), .D(d_ff_as_3_q), .C(and_4_out), .Clr(1'b0), .Q(FETCH));  // open: nQ
  Decoder #(.Selector_Bits(2)) decoder_1 (
    .sel(demultiplexer_2_out_0[1:0]), .out_0(RXE), .out_1(RAE), .out_2(JUMP), .out_3(decoder_1_out_3));
  D_FF_AS d_ff_as_2 (.Set(1'b0), .D(FETCH), .C(and_4_out), .Clr(SIG_RESET), .Q(PCINC));  // open: nQ
  and and_5 (MEMWRT, d_ff_as_3_q, decoder_1_out_3);
  Decoder #(.Selector_Bits(2)) decoder_2 (
    .sel(demultiplexer_2_out_0[3:2]), .out_0(XOUT), .out_1(AOUT), .out_2(TOP), .out_3(decoder_2_out_3));
  D_FF_AS d_ff_as_3 (.Set(1'b0), .D(PCINC), .C(and_4_out), .Clr(SIG_RESET), .Q(d_ff_as_3_q));  // open: nQ
  // And and_6 is placed but not wired
  and and_7 (and_7_out, d_ff_as_3_q, decoder_2_out_3);
  or or_3 (DECODE, PCINC, d_ff_as_3_q);
  or or_4 (ADDR_A, decoder_1_out_3, decoder_2_out_3);
  or or_5 (MEMRD, FETCH, and_7_out);

  // Notes on the sheet:
  //   clk: Hz: 20
endmodule
