// Digital circuit stackerproto3ntb.dig as structural Verilog
module stackerproto3ntb (
);

  wire ALT, and_1_out, and_2_out, and_3_out, and_4_out, and_5_out, and_6_out, BUS_ALU, BUSIN, BUSOUT,
       CLOCK_out, d_ff_as_1_q, d_ff_as_3_q, DECODE, decoder_1_out_0, decoder_1_out_1, decoder_1_out_2,
       decoder_1_out_3, decoder_1_out_4, decoder_1_out_5, decoder_1_out_6, decoder_1_out_7, dipswitch_9_out,
       driver_26_out, driver_27_out, driver_28_out, driver_29_out, driver_30_out, driver_31_out,
       driver_32_out, driver_33_out, EXECUTE, FETCH, MEM_RD, MEM_WRT, MXOP, not_1_out, OP_0, OP_1, PCa_ovf,
       RESET_out, RS_0, RS_1, RS_2, ssalu8b_1_co, ssalu8b_1_z, STK_DIR, STK_EN, undriven, undriven_2,
       undriven_3, undriven_4, undriven_5, undriven_6, undriven_7, XEN;
  wire [7:0] creg8_1_q, D_q, demultiplexer_1_out_0, demultiplexer_1_out_1, dipswitch_8_out, driver_1_out,
       driver_2_out, driver_3_out, driver_4_out, driver_5_out, driver_6_out, driver_10_out, driver_18_out,
       driver_19_out, driver_22_out, driver_23_out, eeprom_1_d, IN_q, IR_q, multiplexer_1_out,
       od8x8bsrfv2_1_sro, od8x8bsrfv2_1_top, OUT_q, PCa_out, RAM_d, SR_q, ssalu8b_1_y;
  wire [14:0] d_ff_as_2_q, stackercl_1_busin;
  wire [15:0] Aa_q, multiplexer_2_out;
  wire [15:8] PCp_out;

  Driver #(.Bits(8)) driver_1 (.in(driver_6_out), .out(driver_1_out));  // open: en
  Driver #(.Bits(8)) driver_2 (.in(driver_6_out), .out(driver_2_out));  // open: en
  Driver #(.Bits(8)) driver_3 (.in(driver_6_out), .out(driver_3_out));  // open: en
  assign driver_4_out = undriven_7 ? driver_6_out : 8'bz;  // Driver driver_4
  assign driver_5_out = FETCH ? driver_6_out : 8'bz;  // Driver driver_5
  CREG8 Aa (.D(driver_1_out), .R(undriven_6), .CLK(CLOCK_out), .Q(Aa_q[7:0]));  // open: EN
  CREG8 Ap (.D(driver_2_out), .R(undriven_6), .CLK(CLOCK_out), .Q(Aa_q[15:8]));  // open: EN
  CREG8 IR (.D(driver_5_out), .R(RESET_out), .CLK(CLOCK_out), .EN(FETCH), .Q(IR_q));
  and and_1 (and_1_out, CLOCK_out, BUS_ALU);
  Driver #(.Bits(8)) driver_6 (.in(Aa_q[7:0]), .out(driver_6_out));  // open: en
  Driver #(.Bits(8)) driver_7 (.in(Aa_q[15:8]), .out(driver_6_out));  // open: en
  CounterPreset #(.Bits(8)) PCa (
    .en(DECODE), .C(CLOCK_out), .dir(1'b0), .in(driver_3_out), .clr(undriven_6), .out(PCa_out), .ovf(PCa_ovf));  // open: ld
  CounterPreset #(.Bits(8)) PCp (
    .en(PCa_ovf), .C(CLOCK_out), .dir(1'b0), .in(driver_4_out), .ld(undriven_7), .clr(undriven_6),
    .out(PCp_out));  // open: ovf
  DipSwitch ALU_BUS ();  // open: out
  DipSwitch u_XEN ();  // open: out
  DipSwitch STKDIR ();  // open: out
  DipSwitch ENABLE ();  // open: out
  D_FF_AS d_ff_as_1 (.Set(1'b0), .D(ssalu8b_1_z), .C(and_1_out), .Clr(RESET_out), .Q(d_ff_as_1_q));  // open: nQ
  Driver #(.Bits(8)) driver_8 (.in(PCa_out), .out(driver_6_out));  // open: en
  Driver #(.Bits(8)) driver_9 (.in(PCp_out), .out(driver_6_out));  // open: en
  STACKERCL stackercl_1 (
    .IN(IR_q), .ZERO(d_ff_as_1_q), .BUSIN(stackercl_1_busin[0]), .BUSOUT(stackercl_1_busin[1]),
    .MEM_RD(stackercl_1_busin[2]), .MEM_WRT(stackercl_1_busin[3]), .BUS_ALU(stackercl_1_busin[4]),
    .STK_DIR(stackercl_1_busin[5]), .STK_EN(stackercl_1_busin[6]), .MXOP(stackercl_1_busin[7]),
    .XEN(stackercl_1_busin[8]), .RS_0(stackercl_1_busin[9]), .RS_1(stackercl_1_busin[10]),
    .RS_2(stackercl_1_busin[11]), .OP_0(stackercl_1_busin[12]), .OP_1(stackercl_1_busin[13]),
    .ALT(stackercl_1_busin[14]));
  Button RESET (.out(RESET_out));
  Button CLOCK (.out(CLOCK_out));
  Multiplexer #(.Bits(8)) multiplexer_1 (
    .sel(BUS_ALU), .in_0(driver_10_out), .in_1(ssalu8b_1_y), .out(multiplexer_1_out));
  and and_2 (and_2_out, CLOCK_out, DECODE);
  Multiplexer multiplexer_2 (.sel(FETCH), .in_0(Aa_q[0]), .in_1(PCa_out[0]), .out(multiplexer_2_out[0]));
  DipSwitch dipswitch_1 (.out(dipswitch_8_out[0]));
  DipSwitch dipswitch_2 (.out(dipswitch_8_out[1]));
  DipSwitch dipswitch_3 (.out(dipswitch_8_out[2]));
  DipSwitch dipswitch_4 (.out(dipswitch_8_out[3]));
  DipSwitch dipswitch_5 (.out(dipswitch_8_out[4]));
  DipSwitch dipswitch_6 (.out(dipswitch_8_out[5]));
  DipSwitch dipswitch_7 (.out(dipswitch_8_out[6]));
  DipSwitch dipswitch_8 (.out(dipswitch_8_out[7]));
  DipSwitch dipswitch_9 (.out(dipswitch_9_out));
  assign driver_10_out = BUSIN ? driver_6_out : 8'bz;  // Driver driver_10
  D_FF_AS #(.Bits(15)) d_ff_as_2 (
    .Set(1'b0), .D(stackercl_1_busin), .C(and_2_out), .Clr(ssalu8b_1_z), .Q(d_ff_as_2_q));  // open: nQ
  assign driver_6_out = dipswitch_9_out ? dipswitch_8_out : 8'bz;  // Driver driver_11
  Seven_Seg_Hex seven_seg_hex_1 (.d(driver_6_out[7:4]), .dp(1'b0));
  // Probe on od8x8bsrfv2_1_top
  od8x8bsrfV2 od8x8bsrfv2_1 (
    .SRI(multiplexer_1_out), .DIR(STK_DIR), .EN(STK_EN), .CLK(CLOCK_out), .RST(RESET_out), .RSI({8{1'b0}}),
    .SRO(od8x8bsrfv2_1_sro), .TOP(od8x8bsrfv2_1_top));  // open: CPT, DPT
  assign {ALT, OP_1, OP_0, RS_2, RS_1, RS_0, XEN, MXOP, STK_EN, STK_DIR, BUS_ALU, MEM_WRT, MEM_RD, BUSOUT, BUSIN} = EXECUTE ? d_ff_as_2_q : 15'bz;  // Driver driver_12
  not not_1 (not_1_out, multiplexer_2_out[15]);
  Seven_Seg_Hex seven_seg_hex_2 (.d(driver_6_out[3:0]), .dp(1'b0));
  Demultiplexer #(.Bits(8)) demultiplexer_1 (
    .sel(BUS_ALU), .in(od8x8bsrfv2_1_top), .out_0(demultiplexer_1_out_0), .out_1(demultiplexer_1_out_1));
  assign driver_6_out = BUSOUT ? demultiplexer_1_out_0 : 8'bz;  // Driver driver_13
  EEPROM #(.AddrBits(15), .Bits(8)) eeprom_1 (
    .A(multiplexer_2_out[14:0]), .CS(multiplexer_2_out[15]), .WE(MEM_WRT), .OE(MEM_RD), .D(eeprom_1_d));
  RAMSinglePortSel #(.AddrBits(15), .Bits(8)) RAM (
    .A(multiplexer_2_out[14:0]), .CS(not_1_out), .WE(MEM_WRT), .OE(MEM_RD), .D(RAM_d));
  CREG8 creg8_1 (.D(demultiplexer_1_out_1), .R(RESET_out), .CLK(CLOCK_out), .EN(XEN), .Q(creg8_1_q));
  // Probe on od8x8bsrfv2_1_sro
  // Probe on creg8_1_q
  and and_3 (and_3_out, MEM_WRT, multiplexer_2_out[15]);
  and and_4 (and_4_out, MEM_RD, multiplexer_2_out[15]);
  and and_5 (and_5_out, MEM_WRT, not_1_out);
  and and_6 (and_6_out, MEM_RD, not_1_out);
  SEQGEN_FDE seqgen_fde_1 (.R(RESET_out), .C(CLOCK_out), .F(FETCH), .D(DECODE), .E(EXECUTE));
  assign eeprom_1_d = and_3_out ? driver_6_out : 8'bz;  // Driver driver_14
  assign driver_6_out = and_4_out ? eeprom_1_d : 8'bz;  // Driver driver_15
  assign RAM_d = and_5_out ? driver_6_out : 8'bz;  // Driver driver_16
  assign driver_6_out = and_6_out ? RAM_d : 8'bz;  // Driver driver_17
  SSALU8B ssalu8b_1 (
    .A(demultiplexer_1_out_1), .X(creg8_1_q), .OP0(ALT), .OP1(OP_1), .ALT(OP_0), .CO(ssalu8b_1_co),
    .CIN(d_ff_as_3_q), .Y(ssalu8b_1_y), .Z(ssalu8b_1_z));
  assign driver_18_out = undriven_2 ? driver_6_out : 8'bz;  // Driver driver_18
  assign driver_19_out = undriven ? driver_6_out : 8'bz;  // Driver driver_19
  D_FF_AS d_ff_as_3 (.Set(1'b0), .D(ssalu8b_1_co), .C(CLOCK_out), .Clr(RESET_out), .Q(d_ff_as_3_q));  // open: nQ
  Driver #(.Bits(8)) driver_20 (.in(D_q), .out(driver_6_out));  // open: en
  CREG8 D (.D(driver_18_out), .R(undriven_3), .CLK(CLOCK_out), .EN(undriven_2), .Q(D_q));
  Driver #(.Bits(8)) driver_21 (.in(OUT_q), .out(driver_6_out));  // open: en
  CREG8 OUT (.D(driver_19_out), .R(undriven_3), .CLK(CLOCK_out), .EN(undriven), .Q(OUT_q));
  // Probe on ssalu8b_1_y
  LED led_1 (.in(ssalu8b_1_z));
  assign driver_22_out = undriven_5 ? driver_6_out : 8'bz;  // Driver driver_22
  assign driver_23_out = undriven_4 ? driver_6_out : 8'bz;  // Driver driver_23
  Driver #(.Bits(8)) driver_24 (.in(SR_q), .out(driver_6_out));  // open: en
  CREG8 SR (.D(driver_22_out), .R(undriven_3), .CLK(CLOCK_out), .EN(undriven_5), .Q(SR_q));
  Driver #(.Bits(8)) driver_25 (.in(IN_q), .out(driver_6_out));  // open: en
  CREG8 IN (.D(driver_23_out), .R(undriven_3), .CLK(CLOCK_out), .EN(undriven_4), .Q(IN_q));
  Decoder #(.Selector_Bits(3)) decoder_1 (
    .sel({RS_0, RS_1, RS_2}), .out_0(decoder_1_out_0), .out_1(decoder_1_out_1), .out_2(decoder_1_out_2),
    .out_3(decoder_1_out_3), .out_4(decoder_1_out_4), .out_5(decoder_1_out_5), .out_6(decoder_1_out_6),
    .out_7(decoder_1_out_7));
  assign driver_26_out = EXECUTE ? decoder_1_out_0 : 1'bz;  // Driver driver_26
  assign driver_27_out = EXECUTE ? decoder_1_out_1 : 1'bz;  // Driver driver_27
  assign driver_28_out = EXECUTE ? decoder_1_out_2 : 1'bz;  // Driver driver_28
  assign driver_29_out = EXECUTE ? decoder_1_out_3 : 1'bz;  // Driver driver_29
  assign driver_30_out = EXECUTE ? decoder_1_out_4 : 1'bz;  // Driver driver_30
  assign driver_31_out = EXECUTE ? decoder_1_out_5 : 1'bz;  // Driver driver_31
  assign driver_32_out = EXECUTE ? decoder_1_out_6 : 1'bz;  // Driver driver_32
  assign driver_33_out = EXECUTE ? decoder_1_out_7 : 1'bz;  // Driver driver_33
  // Pins of 1 and 8 bits meet at {8{1'b0}}
  // Pins of 1 and 16 bits meet at {PCp_out, PCa_out}
  // Pins of 1 and 16 bits meet at multiplexer_2_out
  // Pins of 1 and 16 bits meet at Aa_q
  // Pins of 1 and 8 bits meet at {8{1'b0}}
endmodule
